// Logisim project CPU_Final.circ as structural Verilog
module OneBitAdder (
  input  A,
  input  B,
  input  CarryIn,
  output Sum,
  output CarryOut
);

  wire and_1_out, and_2_out, xor_1_out;

  xor xor_1 (xor_1_out, A, B);
  and and_1 (and_1_out, A, B);
  and and_2 (and_2_out, xor_1_out, CarryIn);
  xor xor_2 (Sum, CarryIn, xor_1_out);
  or or_1 (CarryOut, and_2_out, and_1_out);
  LED led_1 (.in(Sum));
  LED led_2 (.in(CarryOut));

  // Notes on the sheet:
  //   Intermediate Sum
  //   Intermediate Carry
endmodule

module FourBitAdder (
  input  CarryIn,
  input  [3:0] A,
  input  [3:0] B,
  output [3:0] Sum,
  output CarryOut
);

  wire onebitadder_1_carryout, onebitadder_2_carryout, onebitadder_3_carryout;

  // Probe on A
  // Probe on B
  OneBitAdder onebitadder_1 (.A(A[0]), .B(B[0]), .CarryIn(CarryIn), .Sum(Sum[0]), .CarryOut(onebitadder_1_carryout));
  OneBitAdder onebitadder_2 (
    .A(A[1]), .B(B[1]), .CarryIn(onebitadder_1_carryout), .Sum(Sum[1]), .CarryOut(onebitadder_2_carryout));
  OneBitAdder onebitadder_3 (
    .A(A[2]), .B(B[2]), .CarryIn(onebitadder_2_carryout), .Sum(Sum[2]), .CarryOut(onebitadder_3_carryout));
  OneBitAdder onebitadder_4 (.A(A[3]), .B(B[3]), .CarryIn(onebitadder_3_carryout), .Sum(Sum[3]), .CarryOut(CarryOut));
  // Probe on Sum

  // Notes on the sheet:
  //   First
  //   Second
  //   Third
  //   Fourth
endmodule

module EightBitAdder (
  input  CarryIn,
  input  [7:0] A,
  input  [7:0] B,
  output [7:0] Sum,
  output CarryOut
);

  wire fourbitadder_1_carryout;

  // Probe on A
  // Probe on B
  FourBitAdder fourbitadder_1 (
    .CarryIn(CarryIn), .A(A[3:0]), .B(B[3:0]), .Sum(Sum[3:0]), .CarryOut(fourbitadder_1_carryout));
  FourBitAdder fourbitadder_2 (
    .CarryIn(fourbitadder_1_carryout), .A(A[7:4]), .B(B[7:4]), .Sum(Sum[7:4]), .CarryOut(CarryOut));
  // Probe on Sum

  // Notes on the sheet:
  //   First
  //   Second 
endmodule

module SixteenBitAdder (
  input  CarryIn,
  input  [15:0] A,
  input  [15:0] B,
  output [15:0] Sum,
  output CarryOut
);

  wire eightbitadder_1_carryout;

  // Probe on A
  // Probe on B
  EightBitAdder eightbitadder_1 (
    .CarryIn(CarryIn), .A(A[7:0]), .B(B[7:0]), .Sum(Sum[7:0]), .CarryOut(eightbitadder_1_carryout));
  EightBitAdder eightbitadder_2 (
    .CarryIn(eightbitadder_1_carryout), .A(A[15:8]), .B(B[15:8]), .Sum(Sum[15:8]), .CarryOut(CarryOut));
  // Probe on Sum

  // Notes on the sheet:
  //   First
  //   Second 
endmodule

module SixteenBitAddSub (
  input  CarryIn,
  input  [15:0] A,
  input  [15:0] B,
  input  [15:0] Sub,
  output [15:0] Result,
  output CarryOut
);

  wire [15:0] xor_1_out;

  // Probe on Sub
  // Probe on A
  // Probe on B
  // Probe on A
  // Probe on B
  assign xor_1_out = B ^ Sub;  // XOR_Gate xor_1, 16 bits wide
  SixteenBitAdder sixteenbitadder_1 (.CarryIn(CarryIn), .A(A), .B(xor_1_out), .Sum(Result), .CarryOut(CarryOut));
  // Probe on Result
endmodule

module Memory_Cell (
  input  Clock,
  input  WE,
  input  Din,
  input  OE,
  input  Reset,
  output Dout,
  output Stored_Data
);

  wire and_1_out, and_2_out, not_1_out, or_1_out;

  not not_1 (not_1_out, WE);
  and and_1 (and_1_out, Stored_Data, not_1_out);
  and and_2 (and_2_out, WE, Din);
  or or_1 (or_1_out, and_1_out, and_2_out);
  D_Flip_Flop d_ff_1 (.D(or_1_out), .clk(Clock), .Q(Stored_Data), .reset(Reset));  // open: Qn, preset
  assign Dout = OE ? Stored_Data : 1'bz;  // Controlled_Buffer controlled_buffer_1

  // Notes on the sheet:
  //   Memory Cell
endmodule

module EightBitRegister (
  input  Clock,
  input  WE,
  input  [7:0] Din,
  input  OE,
  output [7:0] Dout,
  output [7:0] StoredData
);

  Memory_Cell memory_cell_1 (
    .Clock(Clock), .WE(WE), .Din(Din[0]), .OE(OE), .Dout(Dout[0]), .Stored_Data(StoredData[0]));  // open: Reset
  Memory_Cell memory_cell_2 (
    .Clock(Clock), .WE(WE), .Din(Din[1]), .OE(OE), .Dout(Dout[1]), .Stored_Data(StoredData[1]));  // open: Reset
  Memory_Cell memory_cell_3 (
    .Clock(Clock), .WE(WE), .Din(Din[2]), .OE(OE), .Dout(Dout[2]), .Stored_Data(StoredData[2]));  // open: Reset
  Memory_Cell memory_cell_4 (
    .Clock(Clock), .WE(WE), .Din(Din[3]), .OE(OE), .Dout(Dout[3]), .Stored_Data(StoredData[3]));  // open: Reset
  Memory_Cell memory_cell_5 (
    .Clock(Clock), .WE(WE), .Din(Din[4]), .OE(OE), .Dout(Dout[4]), .Stored_Data(StoredData[4]));  // open: Reset
  Memory_Cell memory_cell_6 (
    .Clock(Clock), .WE(WE), .Din(Din[5]), .OE(OE), .Dout(Dout[5]), .Stored_Data(StoredData[5]));  // open: Reset
  Memory_Cell memory_cell_7 (
    .Clock(Clock), .WE(WE), .Din(Din[6]), .OE(OE), .Dout(Dout[6]), .Stored_Data(StoredData[6]));  // open: Reset
  Memory_Cell memory_cell_8 (
    .Clock(Clock), .WE(WE), .Din(Din[7]), .OE(OE), .Dout(Dout[7]), .Stored_Data(StoredData[7]));  // open: Reset

  // Notes on the sheet:
  //   8 Bits Register 
endmodule

module MAR (
  input  Clock,
  input  WE,
  input  [3:0] Din,
  input  OE,
  output [3:0] Dout,
  output [3:0] StoredData
);

  Memory_Cell memory_cell_1 (
    .Clock(Clock), .WE(WE), .Din(Din[0]), .OE(OE), .Dout(Dout[0]), .Stored_Data(StoredData[0]));  // open: Reset
  Memory_Cell memory_cell_2 (
    .Clock(Clock), .WE(WE), .Din(Din[1]), .OE(OE), .Dout(Dout[1]), .Stored_Data(StoredData[1]));  // open: Reset
  Memory_Cell memory_cell_3 (
    .Clock(Clock), .WE(WE), .Din(Din[2]), .OE(OE), .Dout(Dout[2]), .Stored_Data(StoredData[2]));  // open: Reset
  Memory_Cell memory_cell_4 (
    .Clock(Clock), .WE(WE), .Din(Din[3]), .OE(OE), .Dout(Dout[3]), .Stored_Data(StoredData[3]));  // open: Reset

  // Notes on the sheet:
  //   MAR
endmodule

module Multiplier_4x4 (
  input  [3:0] B,
  input  [3:0] A,
  output [7:0] Product
);

  wire [2:0] and_15_out;
  wire [3:0] and_4_out, and_8_out, and_12_out, fourbitadder_2_carryout;
  wire [3:1] fourbitadder_3_sum;
  wire [3:3] fourbitadder_3_carryout;

  // Probe on B
  and and_1 (and_4_out[3], B[3], A[3]);
  and and_2 (and_4_out[2], B[3], A[2]);
  and and_3 (and_4_out[1], B[3], A[1]);
  and and_4 (and_4_out[0], B[3], A[0]);
  and and_5 (and_8_out[3], B[2], A[3]);
  and and_6 (and_8_out[2], B[2], A[2]);
  and and_7 (and_8_out[1], B[2], A[1]);
  and and_8 (and_8_out[0], B[2], A[0]);
  and and_9 (and_12_out[3], B[1], A[3]);
  and and_10 (and_12_out[2], B[1], A[2]);
  and and_11 (and_12_out[1], B[1], A[1]);
  and and_12 (and_12_out[0], B[1], A[0]);
  FourBitAdder fourbitadder_1 (
    .CarryIn(1'b0), .A(fourbitadder_2_carryout), .B(and_4_out), .Sum(Product[6:3]), .CarryOut(Product[7]));
  FourBitAdder fourbitadder_2 (
    .CarryIn(1'b0), .A({fourbitadder_3_carryout[3], fourbitadder_3_sum}), .B(and_8_out),
    .Sum({fourbitadder_2_carryout[2:0], Product[2]}), .CarryOut(fourbitadder_2_carryout[3]));
  and and_13 (and_15_out[2], B[0], A[3]);
  and and_14 (and_15_out[1], B[0], A[2]);
  and and_15 (and_15_out[0], B[0], A[1]);
  FourBitAdder fourbitadder_3 (
    .CarryIn(1'b0), .A({1'b0, and_15_out}), .B(and_12_out), .Sum({fourbitadder_3_sum, Product[1]}),
    .CarryOut(fourbitadder_3_carryout[3]));
  // Probe on A
  and and_16 (Product[0], B[0], A[0]);
  // Probe on Product

  // Notes on the sheet:
  //   8 Bit Multiplier 
endmodule

module ALU_8_bit (
  input  [7:0] Reg_A,
  input  [7:0] Reg_B,
  input  OE,
  output [7:0] ALU_Result,
  output [7:0] Dout,
  output CarryOut
);

  EightBitAdder eightbitadder_1 (.A(Reg_A), .B(Reg_B), .Sum(ALU_Result), .CarryOut(CarryOut));  // open: CarryIn
  assign Dout = OE ? ALU_Result : 8'bz;  // Controlled_Buffer controlled_buffer_1
endmodule

module PCU8Bit (
  input  [7:0] in_1,
  input  OE,
  input  in_3,
  input  [3:0] OE_Testing_Data,
  output [3:0] out_5,
  output [3:0] Counter_Content,
  output [7:0] IR_Content,
  output [7:0] out_8,
  output [7:0] Reg_A_Content,
  output [7:0] out_10,
  output [7:0] out_11,
  output [7:0] Reg_B_Content,
  output [2:0] Counter_Content_2
);

  wire clock_1_out, cu_4_8_bit_1_alu_oe, cu_4_8_bit_1_c_e, cu_4_8_bit_1_c_oe, cu_4_8_bit_1_ir_oe,
       cu_4_8_bit_1_ir_we, cu_4_8_bit_1_mar_oe, cu_4_8_bit_1_mar_we, cu_4_8_bit_1_mbr_ioe,
       cu_4_8_bit_1_mbr_oe, cu_4_8_bit_1_mbr_we, cu_4_8_bit_1_or_oe, cu_4_8_bit_1_or_we, cu_4_8_bit_1_ram_oe,
       cu_4_8_bit_1_ram_we, cu_4_8_bit_1_reg_a_we, cu_4_8_bit_1_reg_b_we;
  wire [3:0] bitselector_2_out, controlled_buffer_1_out, mar_1_dout;
  wire [7:0] alu_8_bit_1_dout, eightbitregister_1_dout;

  Clock clock_1 (.out(clock_1_out));
  Counter #(.max('h3), .width(4)) counter_1 (
    .D(controlled_buffer_1_out), .count(cu_4_8_bit_1_c_e), .Q(Counter_Content), .clk(clock_1_out));  // open: load, carry, up, clr
  EightBitRegister eightbitregister_1 (
    .Clock(clock_1_out), .WE(cu_4_8_bit_1_ir_we), .Din(alu_8_bit_1_dout), .OE(cu_4_8_bit_1_ir_oe),
    .Dout(eightbitregister_1_dout), .StoredData(IR_Content));
  EightBitRegister eightbitregister_2 (
    .Clock(clock_1_out), .WE(cu_4_8_bit_1_reg_a_we), .Din(alu_8_bit_1_dout), .StoredData(Reg_A_Content));  // open: OE, Dout
  ALU_8_bit alu_8_bit_1 (
    .Reg_A(Reg_A_Content), .Reg_B(Reg_B_Content), .OE(cu_4_8_bit_1_alu_oe), .ALU_Result(out_10),
    .Dout(alu_8_bit_1_dout));  // open: CarryOut
  EightBitRegister eightbitregister_3 (
    .Clock(clock_1_out), .WE(cu_4_8_bit_1_reg_b_we), .Din(alu_8_bit_1_dout), .StoredData(Reg_B_Content));  // open: OE, Dout
  assign controlled_buffer_1_out = cu_4_8_bit_1_c_oe ? Counter_Content : 4'bz;  // Controlled_Buffer controlled_buffer_1
  // Probe on Reg_A_Content
  // Probe on Reg_B_Content
  BitSelector #(.group(4)) bitselector_1 (.in(eightbitregister_1_dout), .out(controlled_buffer_1_out), .sel(1'b0));
  LED led_1 (.in(alu_8_bit_1_dout[7]));
  LED led_2 (.in(alu_8_bit_1_dout[6]));
  LED led_3 (.in(alu_8_bit_1_dout[5]));
  LED led_4 (.in(alu_8_bit_1_dout[4]));
  assign alu_8_bit_1_dout = in_3 ? in_1 : 8'bz;  // Controlled_Buffer controlled_buffer_2
  LED led_5 (.in(alu_8_bit_1_dout[3]));
  LED led_6 (.in(alu_8_bit_1_dout[2]));
  LED led_7 (.in(alu_8_bit_1_dout[1]));
  LED led_8 (.in(alu_8_bit_1_dout[0]));
  assign alu_8_bit_1_dout = cu_4_8_bit_1_mbr_ioe ? out_8 : 8'bz;  // Controlled_Buffer controlled_buffer_3
  EightBitRegister eightbitregister_4 (
    .Clock(clock_1_out), .WE(cu_4_8_bit_1_mbr_we), .Din(alu_8_bit_1_dout), .OE(cu_4_8_bit_1_mbr_oe),
    .Dout(alu_8_bit_1_dout), .StoredData(out_8));
  MAR mar_1 (
    .Clock(clock_1_out), .WE(cu_4_8_bit_1_mar_we), .Din(controlled_buffer_1_out), .OE(cu_4_8_bit_1_mar_oe),
    .Dout(mar_1_dout), .StoredData(out_5));
  EightBitRegister eightbitregister_5 (
    .Clock(clock_1_out), .WE(cu_4_8_bit_1_or_we), .Din(alu_8_bit_1_dout), .OE(cu_4_8_bit_1_or_oe),
    .Dout(alu_8_bit_1_dout), .StoredData(out_11));
  LED led_9 (.in(alu_8_bit_1_dout[7]));
  LED led_10 (.in(alu_8_bit_1_dout[6]));
  LED led_11 (.in(alu_8_bit_1_dout[5]));
  LED led_12 (.in(alu_8_bit_1_dout[4]));
  LED led_13 (.in(alu_8_bit_1_dout[3]));
  LED led_14 (.in(alu_8_bit_1_dout[2]));
  LED led_15 (.in(alu_8_bit_1_dout[1]));
  LED led_16 (.in(alu_8_bit_1_dout[0]));
  assign mar_1_dout = OE ? OE_Testing_Data : 4'bz;  // Controlled_Buffer controlled_buffer_4
  RAM #(.addrWidth(4), .trigger("falling")) ram_1 (
    .addr(mar_1_dout), .we(cu_4_8_bit_1_ram_we), .oe(cu_4_8_bit_1_ram_oe), .clk(clock_1_out),
    .din(alu_8_bit_1_dout), .dout(alu_8_bit_1_dout));
  BitSelector #(.group(4)) bitselector_2 (.in(IR_Content), .out(bitselector_2_out), .sel(1'b1));
  Counter #(.max('h7), .width(3)) counter_2 (
    .Q(Counter_Content_2), .clk(clock_1_out));  // open: load, D, count, carry, up, clr
  CU_4_8_bit cu_4_8_bit_1 (
    .OPC3(bitselector_2_out[3]), .OPC2(bitselector_2_out[2]), .OPC1(bitselector_2_out[1]),
    .OPC0(bitselector_2_out[0]), .SC2(Counter_Content_2[2]), .SC1(Counter_Content_2[1]),
    .SC0(Counter_Content_2[0]), .C_OE(cu_4_8_bit_1_c_oe), .MAR_WE(cu_4_8_bit_1_mar_we),
    .MAR_OE(cu_4_8_bit_1_mar_oe), .RAM_OE(cu_4_8_bit_1_ram_oe), .MBR_WE(cu_4_8_bit_1_mbr_we),
    .C_E(cu_4_8_bit_1_c_e), .MBR_IOE(cu_4_8_bit_1_mbr_ioe), .IR_WE(cu_4_8_bit_1_ir_we),
    .IR_OE(cu_4_8_bit_1_ir_oe), .REG_A_WE(cu_4_8_bit_1_reg_a_we), .REG_B_WE(cu_4_8_bit_1_reg_b_we),
    .OR_WE(cu_4_8_bit_1_or_we), .OR_OE(cu_4_8_bit_1_or_oe), .MBR_OE(cu_4_8_bit_1_mbr_oe),
    .RAM_WE(cu_4_8_bit_1_ram_we), .ALU_OE(cu_4_8_bit_1_alu_oe));

  // Notes on the sheet:
  //   Clock
  //   Program Counter 
  //   Instruction Reg
  //   REG_A
  //   ALU
  //   REG_B
  //   Internal Address Bus
  //   ALU Result
  //   OE Testing Data
  //   D7
  //   Testing Data 
  //   D6
  //   D5
  //   D4
  //   D3
  //   D2
  //   D1
  //   Internal Data Bus 
  //   D0
  //   MAR
  //   MBR
  //   Output Reg
  //   MAR content 
  //   MBR content
  //   D7
  //   D6
  //   D3
  //   D5
  //   D4
  //   D2
  //   External Data Bus 
  //   External Address Bus 
  //   D1
  //   D0
  //   Step Counter 
endmodule

module CU_I_8_bit (
  input  OPC3,
  input  OPC2,
  input  OPC1,
  input  OPC0,
  input  SC2,
  input  SC1,
  input  SC0,
  output C0,
  output C1,
  output C2,
  output C3,
  output C4,
  output C5,
  output C6,
  output C7,
  output C8,
  output C9,
  output C10,
  output C11
);

  wire not_1_out, not_2_out, not_3_out, not_4_out, not_5_out, or_1_out, or_2_out, or_3_out, or_4_out,
       or_5_out, or_6_out, or_7_out, or_8_out, or_9_out, or_10_out, or_11_out, or_12_out, or_13_out,
       or_14_out, or_15_out, or_16_out, or_17_out, or_18_out, or_19_out;

  not not_1 (not_1_out, OPC1);
  not not_2 (not_2_out, OPC0);
  not not_3 (not_3_out, SC2);
  not not_4 (not_4_out, SC1);
  not not_5 (not_5_out, SC0);
  and and_1 (C0, not_5_out, not_4_out, not_3_out);
  and and_2 (C1, SC0, not_4_out, not_3_out);
  and and_3 (C2, OPC1, OPC0, SC2, not_5_out, not_4_out);
  or or_1 (or_1_out, SC2, SC0);
  or or_2 (or_2_out, not_3_out, not_5_out);
  or or_3 (or_3_out, not_1_out, SC0);
  or or_4 (or_4_out, SC2, SC0);
  or or_5 (or_5_out, not_3_out, not_5_out);
  or or_6 (or_6_out, OPC1, not_4_out);
  or or_7 (or_7_out, OPC0, not_4_out);
  or or_8 (or_8_out, not_1_out, SC0);
  or or_9 (or_9_out, SC2, not_5_out);
  or or_10 (or_10_out, SC1, SC0);
  or or_11 (or_11_out, not_3_out, not_4_out);
  or or_12 (or_12_out, not_1_out, not_3_out);
  and and_4 (C6, OPC1, OPC0, SC2, not_5_out, not_4_out);
  and and_5 (C7, SC1, not_5_out, not_3_out);
  or or_13 (or_13_out, not_1_out, OPC0);
  or or_14 (or_14_out, SC1, not_5_out);
  or or_15 (or_15_out, not_4_out, SC0);
  or or_16 (or_16_out, not_1_out, OPC0, not_4_out);
  or or_17 (or_17_out, SC2, SC0);
  or or_18 (or_18_out, not_3_out, not_5_out);
  or or_19 (or_19_out, not_1_out, OPC0, SC0);
  and and_6 (C11, OPC1, SC1, SC0, not_3_out, not_2_out);
  and and_7 (C3, or_1_out, not_4_out, or_2_out, or_3_out);
  and and_8 (C4, or_4_out, or_5_out, or_6_out, or_7_out, or_8_out);
  and and_9 (C5, or_9_out, or_10_out, or_11_out, or_12_out);
  and and_10 (C8, SC1, SC0, not_3_out, or_13_out);
  and and_11 (C9, or_14_out, or_15_out, not_3_out, or_16_out);
  and and_12 (C10, or_17_out, not_4_out, or_18_out, or_19_out);
endmodule

module CU_II_8_bit (
  input  OPC3,
  input  OPC2,
  input  OPC1,
  input  OPC0,
  input  SC2,
  input  SC1,
  input  SC0,
  output C12,
  output C13,
  output C14,
  output C15
);

  wire not_1_out, not_2_out, not_3_out, not_4_out;

  not not_1 (not_1_out, OPC1);
  not not_2 (not_2_out, OPC0);
  not not_3 (not_3_out, SC2);
  not not_4 (not_4_out, SC1);
  and and_1 (C12, SC2, SC0, not_4_out, not_2_out, not_1_out);
  and and_2 (C13, OPC0, SC2, SC0, not_4_out, not_1_out);
  and and_3 (C14, OPC1, OPC0, SC1, SC0, not_3_out);
  and and_4 (C15, OPC1, SC1, SC0, not_3_out, not_2_out);
endmodule

module CU_8_bit (
  input  OPC3,
  input  OPC2,
  input  OPC1,
  input  OPC0,
  input  SC2,
  input  SC1,
  input  SC0,
  output C_OE,
  output MAR_WE,
  output MAR_OE,
  output RAM_OE,
  output MBR_WE,
  output C_E,
  output MBR_IOE,
  output IR_WE,
  output IR_OE,
  output REG_A_WE,
  output REG_B_WE,
  output OR_WE,
  output OR_OE,
  output MBR_OE,
  output RAM_WE,
  output ALU_OE
);

  wire not_1_out, not_2_out, not_3_out, not_4_out, not_5_out, or_1_out, or_2_out, or_3_out, or_4_out,
       or_5_out, or_6_out, or_7_out, or_8_out, or_9_out, or_10_out, or_11_out, or_12_out, or_13_out,
       or_14_out, or_15_out, or_16_out, or_17_out, or_18_out, or_19_out, or_20_out;

  not not_1 (not_1_out, OPC1);
  not not_2 (not_2_out, OPC0);
  not not_3 (not_3_out, SC2);
  not not_4 (not_4_out, SC1);
  not not_5 (not_5_out, SC0);
  and and_1 (C_OE, not_5_out, not_4_out, not_3_out);
  or or_1 (or_1_out, not_1_out, OPC0, not_3_out);
  or or_2 (or_2_out, SC1, SC0);
  or or_3 (or_3_out, not_4_out, not_5_out);
  or or_4 (or_4_out, not_1_out, OPC0, not_3_out);
  or or_5 (or_5_out, not_1_out, not_3_out, SC0);
  or or_6 (or_6_out, not_4_out, not_5_out);
  or or_7 (or_7_out, OPC0, SC1, SC0);
  or or_8 (or_8_out, SC2, SC1, SC0);
  or or_9 (or_9_out, not_2_out, not_3_out, not_5_out);
  or or_10 (or_10_out, not_1_out, not_3_out);
  or or_11 (or_11_out, OPC1, SC1);
  or or_12 (or_12_out, SC2, SC1);
  or or_13 (or_13_out, not_1_out, not_3_out, not_4_out);
  or or_14 (or_14_out, OPC0, SC1);
  and and_2 (C_E, SC1, not_5_out, not_3_out);
  or or_15 (or_15_out, not_1_out, not_3_out);
  and and_3 (IR_WE, SC1, SC0, not_3_out);
  or or_16 (or_16_out, not_1_out, OPC0);
  and and_4 (REG_A_WE, SC2, SC1, SC0, not_2_out, not_1_out);
  and and_5 (REG_B_WE, OPC0, SC2, SC1, SC0, not_1_out);
  and and_6 (OR_WE, OPC1, SC2, not_5_out, not_4_out, not_2_out);
  and and_7 (OR_OE, OPC1, OPC0, SC2, not_5_out, not_4_out);
  and and_8 (MBR_OE, OPC1, OPC0, SC2, SC0, not_4_out);
  and and_9 (RAM_WE, OPC1, OPC0, SC2, SC0, not_4_out);
  or or_17 (or_17_out, OPC0, not_4_out);
  or or_18 (or_18_out, SC2, SC0);
  or or_19 (or_19_out, SC1, not_5_out);
  or or_20 (or_20_out, not_2_out, not_3_out);
  and and_10 (MAR_WE, not_5_out, not_4_out, or_1_out);
  and and_11 (MAR_OE, or_2_out, or_3_out, or_4_out, or_5_out);
  and and_12 (RAM_OE, or_6_out, or_7_out, or_8_out, or_9_out, or_10_out);
  and and_13 (MBR_WE, not_5_out, or_11_out, or_12_out, or_13_out, or_14_out);
  and and_14 (MBR_IOE, SC1, SC0, or_15_out);
  and and_15 (IR_OE, SC2, not_5_out, not_4_out, or_16_out);
  and and_16 (ALU_OE, OPC1, or_17_out, or_18_out, or_19_out, or_20_out);
endmodule

module CU2_8_bit (
  input  OPC3,
  input  OPC2,
  input  OPC1,
  input  OPC0,
  input  SC2,
  input  SC1,
  input  SC0,
  output C_OE,
  output MAR_WE,
  output MAR_OE,
  output RAM_OE,
  output MBR_WE,
  output C_E,
  output MBR_IOE,
  output IR_WE,
  output IR_OE,
  output REG_A_WE,
  output REG_B_WE,
  output OR_WE,
  output OR_OE,
  output MBR_OE,
  output RAM_WE,
  output ALU_OE
);

  wire not_1_out, not_2_out, not_3_out, not_4_out, not_5_out, or_1_out, or_2_out, or_3_out, or_4_out,
       or_5_out, or_6_out, or_7_out, or_8_out, or_9_out, or_10_out, or_11_out, or_12_out, or_13_out,
       or_14_out, or_15_out, or_16_out, or_17_out, or_18_out, or_19_out, or_20_out;

  not not_1 (not_1_out, OPC1);
  not not_2 (not_2_out, OPC0);
  not not_3 (not_3_out, SC2);
  not not_4 (not_4_out, SC1);
  not not_5 (not_5_out, SC0);
  and and_1 (C_OE, not_5_out, not_4_out, not_3_out);
  or or_1 (or_1_out, not_1_out, OPC0, not_3_out);
  or or_2 (or_2_out, SC1, SC0);
  or or_3 (or_3_out, not_4_out, not_5_out);
  or or_4 (or_4_out, not_1_out, OPC0, not_3_out);
  or or_5 (or_5_out, not_1_out, not_3_out, SC0);
  or or_6 (or_6_out, not_4_out, not_5_out);
  or or_7 (or_7_out, OPC0, SC1, SC0);
  or or_8 (or_8_out, SC2, SC1, SC0);
  or or_9 (or_9_out, not_2_out, not_3_out, not_5_out);
  or or_10 (or_10_out, not_1_out, not_3_out);
  or or_11 (or_11_out, OPC1, SC1);
  or or_12 (or_12_out, SC2, SC1);
  or or_13 (or_13_out, not_1_out, not_3_out, not_4_out);
  or or_14 (or_14_out, OPC0, SC1);
  and and_2 (C_E, SC1, not_5_out, not_3_out);
  or or_15 (or_15_out, not_1_out, not_3_out);
  and and_3 (IR_WE, SC1, SC0, not_3_out);
  or or_16 (or_16_out, not_1_out, OPC0);
  and and_4 (REG_A_WE, SC2, SC1, SC0, not_2_out, not_1_out);
  and and_5 (REG_B_WE, OPC0, SC2, SC1, SC0, not_1_out);
  and and_6 (OR_WE, OPC1, SC2, not_5_out, not_4_out, not_2_out);
  and and_7 (OR_OE, OPC1, OPC0, SC2, not_5_out, not_4_out);
  and and_8 (MBR_OE, OPC1, OPC0, SC2, SC0, not_4_out);
  and and_9 (RAM_WE, OPC1, OPC0, SC2, SC0, not_4_out);
  or or_17 (or_17_out, OPC0, not_4_out);
  or or_18 (or_18_out, SC2, SC0);
  or or_19 (or_19_out, SC1, not_5_out);
  or or_20 (or_20_out, not_2_out, not_3_out);
  and and_10 (MAR_WE, not_5_out, not_4_out, or_1_out);
  and and_11 (MAR_OE, or_2_out, or_3_out, or_4_out, or_5_out);
  and and_12 (RAM_OE, or_6_out, or_7_out, or_8_out, or_9_out, or_10_out);
  and and_13 (MBR_WE, not_5_out, or_11_out, or_12_out, or_13_out, or_14_out);
  and and_14 (MBR_IOE, SC1, SC0, or_15_out);
  and and_15 (IR_OE, SC2, not_5_out, not_4_out, or_16_out);
  and and_16 (ALU_OE, OPC1, or_17_out, or_18_out, or_19_out, or_20_out);
endmodule

module CU_3_8_bit (
  input  OPC3,
  input  OPC2,
  input  OPC1,
  input  OPC0,
  input  SC2,
  input  SC1,
  input  SC0,
  output C_OE,
  output MAR_WE,
  output MAR_OE,
  output RAM_OE,
  output MBR_WE,
  output C_E,
  output MBR_IOE,
  output IR_WE,
  output IR_OE,
  output REG_A_WE,
  output REG_B_WE,
  output OR_WE,
  output OR_OE,
  output MBR_OE,
  output RAM_WE,
  output ALU_OE
);

  wire not_1_out, not_2_out, not_3_out, not_4_out, not_5_out, or_1_out, or_2_out, or_3_out, or_4_out,
       or_5_out, or_6_out, or_7_out, or_8_out, or_9_out, or_10_out, or_11_out, or_12_out, or_13_out,
       or_14_out, or_15_out, or_16_out, or_17_out, or_18_out, or_19_out, or_20_out;

  not not_1 (not_1_out, OPC1);
  not not_2 (not_2_out, OPC0);
  not not_3 (not_3_out, SC2);
  not not_4 (not_4_out, SC1);
  not not_5 (not_5_out, SC0);
  and and_1 (C_OE, not_5_out, not_4_out, not_3_out);
  or or_1 (or_1_out, not_1_out, OPC0, not_3_out);
  or or_2 (or_2_out, SC1, SC0);
  or or_3 (or_3_out, not_4_out, not_5_out);
  or or_4 (or_4_out, not_1_out, OPC0, not_3_out);
  or or_5 (or_5_out, not_1_out, not_3_out, SC0);
  or or_6 (or_6_out, not_4_out, not_5_out);
  or or_7 (or_7_out, OPC0, SC1, SC0);
  or or_8 (or_8_out, SC2, SC1, SC0);
  or or_9 (or_9_out, not_2_out, not_3_out, not_5_out);
  or or_10 (or_10_out, not_1_out, not_3_out);
  or or_11 (or_11_out, OPC1, SC1);
  or or_12 (or_12_out, SC2, SC1);
  or or_13 (or_13_out, not_1_out, not_3_out, not_4_out);
  or or_14 (or_14_out, OPC0, SC1);
  and and_2 (C_E, SC1, not_5_out, not_3_out);
  or or_15 (or_15_out, not_1_out, not_3_out);
  and and_3 (IR_WE, SC1, SC0, not_3_out);
  or or_16 (or_16_out, not_1_out, OPC0);
  and and_4 (REG_A_WE, SC2, SC1, SC0, not_2_out, not_1_out);
  and and_5 (REG_B_WE, OPC0, SC2, SC1, SC0, not_1_out);
  and and_6 (OR_WE, OPC1, SC2, not_5_out, not_4_out, not_2_out);
  and and_7 (OR_OE, OPC1, OPC0, SC2, not_5_out, not_4_out);
  and and_8 (MBR_OE, OPC1, OPC0, SC2, SC0, not_4_out);
  and and_9 (RAM_WE, OPC1, OPC0, SC2, SC0, not_4_out);
  or or_17 (or_17_out, OPC0, not_4_out);
  or or_18 (or_18_out, SC2, SC0);
  or or_19 (or_19_out, SC1, not_5_out);
  or or_20 (or_20_out, not_2_out, not_3_out);
  and and_10 (MAR_WE, not_5_out, not_4_out, or_1_out);
  and and_11 (MAR_OE, or_2_out, or_3_out, or_4_out, or_5_out);
  and and_12 (RAM_OE, or_6_out, or_7_out, or_8_out, or_9_out, or_10_out);
  and and_13 (MBR_WE, not_5_out, or_11_out, or_12_out, or_13_out, or_14_out);
  and and_14 (MBR_IOE, SC1, SC0, or_15_out);
  and and_15 (IR_OE, SC2, not_5_out, not_4_out, or_16_out);
  and and_16 (ALU_OE, OPC1, or_17_out, or_18_out, or_19_out, or_20_out);
endmodule

module CU_4_8_bit (
  input  OPC3,
  input  OPC2,
  input  OPC1,
  input  OPC0,
  input  SC2,
  input  SC1,
  input  SC0,
  output C_OE,
  output MAR_WE,
  output MAR_OE,
  output RAM_OE,
  output MBR_WE,
  output C_E,
  output MBR_IOE,
  output IR_WE,
  output IR_OE,
  output REG_A_WE,
  output REG_B_WE,
  output OR_WE,
  output OR_OE,
  output MBR_OE,
  output RAM_WE,
  output ALU_OE
);

  wire and_2_out, and_3_out, and_4_out, and_5_out, and_6_out, and_7_out, and_8_out, and_9_out, and_10_out,
       and_11_out, and_12_out, and_13_out, and_14_out, and_15_out, and_16_out, and_17_out, and_19_out,
       and_20_out, and_22_out, and_23_out, not_1_out, not_2_out, not_3_out, not_4_out, not_5_out, not_6_out,
       not_7_out, or_1_out, or_2_out, or_3_out, or_4_out;

  not not_1 (not_1_out, OPC3);
  not not_2 (not_2_out, OPC2);
  not not_3 (not_3_out, OPC1);
  not not_4 (not_4_out, OPC0);
  not not_5 (not_5_out, SC2);
  not not_6 (not_6_out, SC1);
  not not_7 (not_7_out, SC0);
  and and_1 (C_OE, not_1_out, not_2_out, not_5_out, not_6_out, not_7_out);
  and and_2 (and_2_out, not_1_out, not_2_out, not_5_out, not_6_out, not_7_out);
  and and_3 (and_3_out, not_1_out, not_2_out, not_3_out, not_6_out, not_7_out);
  and and_4 (and_4_out, not_1_out, not_2_out, OPC0, not_6_out, not_7_out);
  and and_5 (and_5_out, not_1_out, not_2_out, not_3_out, not_6_out, SC0);
  and and_6 (and_6_out, not_1_out, not_2_out, not_3_out, SC1, not_7_out);
  and and_7 (and_7_out, not_1_out, not_2_out, not_5_out, not_6_out, SC0);
  and and_8 (and_8_out, not_1_out, not_2_out, not_5_out, SC1, not_7_out);
  and and_9 (and_9_out, not_1_out, not_2_out, OPC0, not_6_out, SC0);
  and and_10 (and_10_out, not_1_out, not_2_out, not_5_out, not_6_out, SC0);
  and and_11 (and_11_out, not_1_out, not_2_out, not_5_out, SC1, not_7_out);
  and and_12 (and_12_out, not_1_out, not_2_out, not_3_out, not_4_out, not_6_out, SC0);
  and and_13 (and_13_out, not_1_out, not_2_out, not_3_out, SC1, not_7_out);
  and and_14 (and_14_out, not_1_out, not_2_out, not_3_out, OPC0, SC2, not_7_out);
  and and_15 (and_15_out, not_1_out, not_2_out, not_5_out, SC1, not_7_out);
  and and_16 (and_16_out, not_1_out, not_2_out, not_3_out, SC1, not_7_out);
  and and_17 (and_17_out, not_1_out, not_2_out, OPC1, OPC0, SC2, not_6_out, not_7_out);
  and and_18 (C_E, not_1_out, not_2_out, not_5_out, SC1, not_7_out);
  and and_19 (and_19_out, not_1_out, not_2_out, not_5_out, SC1, SC0);
  and and_20 (and_20_out, not_1_out, not_2_out, not_3_out, SC1, SC0);
  and and_21 (IR_WE, not_1_out, not_2_out, not_5_out, SC1, SC0);
  and and_22 (and_22_out, not_1_out, not_2_out, not_3_out, SC2, not_6_out, not_7_out);
  and and_23 (and_23_out, not_1_out, not_2_out, OPC0, SC2, not_6_out, not_7_out);
  and and_24 (REG_A_WE, not_1_out, not_2_out, not_3_out, not_4_out, SC2, SC1, SC0);
  and and_25 (REG_B_WE, not_1_out, not_2_out, not_3_out, OPC0, SC2, SC1, SC0);
  and and_26 (OR_WE, not_1_out, not_2_out, OPC1, not_4_out, SC2, not_6_out, not_7_out);
  and and_27 (OR_OE, OPC1, OPC0, SC2, not_7_out, not_6_out);
  and and_28 (MBR_OE, OPC1, OPC0, SC2, SC0, not_6_out);
  and and_29 (RAM_WE, OPC1, OPC0, SC2, SC0, not_6_out);
  or or_1 (or_1_out, OPC0, not_6_out);
  or or_2 (or_2_out, SC2, SC0);
  or or_3 (or_3_out, SC1, not_7_out);
  or or_4 (or_4_out, not_4_out, not_5_out);
  or or_5 (MAR_WE, and_2_out, and_3_out, and_4_out);
  or or_6 (MAR_OE, and_5_out, and_6_out, and_7_out, and_8_out, and_9_out);
  or or_7 (RAM_OE, and_10_out, and_11_out, and_12_out, and_13_out, and_14_out);
  or or_8 (MBR_WE, and_15_out, and_16_out, and_17_out);
  or or_9 (MBR_IOE, and_19_out, and_20_out);
  or or_10 (IR_OE, and_22_out, and_23_out);
  and and_30 (ALU_OE, OPC1, or_1_out, or_2_out, or_3_out, or_4_out);
endmodule

module Instruction_splitter (
  input  [15:0] Instruction_Input,
  input  WE,
  input  Clock,
  output [4:0] Address_B,
  output [4:0] Address_A,
  output [4:0] OPCODE,
  output FLAG_BIT
);

  Register #(.width(16)) register_1 (
    .D(Instruction_Input), .en(WE), .clk(Clock), .Q({FLAG_BIT, OPCODE, Address_A, Address_B}));  // open: clr
endmodule

module buses (
  input  CE,
  input  Inst_splitter_OE,
  input  MAR_Z_WE,
  input  OPCODE_WE,
  input  MAR_A_WE,
  input  MAR_B_WE,
  input  MBR_Z_WE,
  input  MBR_A_WE,
  input  MBR_B_WE,
  input  INSTRUCT_RAM_OE,
  input  INSTRUCT_RAM_WE,
  input  SYSTEM_RAM_WE,
  input  SYSTEM_RAM_OE,
  input  RAM_A_OE,
  input  RAM_A_WE,
  input  RAM_B_OE,
  input  RAM_B_WE,
  input  MBR_Z_CB,
  input  MBR_A_CB,
  input  MBR_B_CB,
  input  OPCODE_CB,
  input  RESULT_CB,
  input  REG_5_WE,
  input  REG_6_WE,
  input  REG_7_WE,
  input  REG_8_WE,
  input  REG_1_WE,
  input  REG_2_WE,
  input  REG_3_WE,
  input  REG_4_WE,
  input  COUNTER_RESET
);

  wire clock_1_out, undriven;
  wire [4:0] controlled_buffer_1_out, counter_1_q, instruction_splitter_1_address_a,
       instruction_splitter_1_address_b, MAR_A_q, MAR_B_q, MAR_Z_q;
  wire [4:4] register_1_q;
  wire [7:0] register_1_q_2;
  wire [15:0] controlled_buffer_2_out, controlled_buffer_5_out, controlled_buffer_7_out, MBR_A_q, MBR_B_q,
       MBR_Z_q, ram_1_dout, ram_2_dout, ram_4_dout, REG_1_q, REG_5_q, REG_6_q, REG_7_q,
       sixteenbitaddsub_1_result;

  assign controlled_buffer_1_out = OPCODE_CB ? {5{1'b0}} : 5'bz;  // Controlled_Buffer controlled_buffer_1
  Register #(.width(5)) register_1 (
    .D(controlled_buffer_1_out), .en(OPCODE_WE), .clk(clock_1_out), .Q({register_1_q[4], register_1_q_2[3:0]}));  // open: clr
  Counter #(.max('h1f), .width(5)) counter_1 (
    .up(undriven), .count(CE), .clk(clock_1_out), .Q(counter_1_q));  // open: clr, load, D, carry
  Register #(.width(16)) REG_1 (
    .D(controlled_buffer_5_out), .en(REG_1_WE), .clk(clock_1_out), .Q(REG_1_q));  // open: clr
  Register #(.width(16)) REG_2 (
    .D(controlled_buffer_5_out), .en(REG_2_WE), .clk(clock_1_out), .Q(REG_1_q));  // open: clr
  Instruction_splitter instruction_splitter_1 (
    .Instruction_Input(controlled_buffer_7_out), .WE(Inst_splitter_OE), .Clock(clock_1_out),
    .Address_B(instruction_splitter_1_address_b), .Address_A(instruction_splitter_1_address_a),
    .OPCODE(controlled_buffer_1_out));  // open: FLAG_BIT
  assign controlled_buffer_2_out = RESULT_CB ? sixteenbitaddsub_1_result : 16'bz;  // Controlled_Buffer controlled_buffer_2
  SixteenBitAddSub sixteenbitaddsub_1 (
    .A(controlled_buffer_5_out), .B(controlled_buffer_2_out), .Result(sixteenbitaddsub_1_result));  // open: CarryIn, Sub, CarryOut
  Register #(.width(16)) REG_3 (
    .D(controlled_buffer_5_out), .en(REG_3_WE), .clk(clock_1_out), .Q(REG_1_q));  // open: clr
  Register #(.width(16)) REG_5 (
    .D(controlled_buffer_2_out), .en(REG_5_WE), .clk(clock_1_out), .Q(REG_5_q));  // open: clr
  Register #(.width(16)) REG_6 (
    .D(controlled_buffer_2_out), .en(REG_6_WE), .clk(clock_1_out), .Q(REG_6_q));  // open: clr
  Register #(.width(5)) MAR_Z (.D(counter_1_q), .en(MAR_Z_WE), .clk(clock_1_out), .Q(MAR_Z_q));  // open: clr
  Register #(.width(5)) MAR_A (
    .D(instruction_splitter_1_address_b), .en(MAR_A_WE), .clk(clock_1_out), .Q(MAR_A_q));  // open: clr
  Register #(.width(16)) REG_4 (
    .D(controlled_buffer_5_out), .en(REG_4_WE), .clk(clock_1_out), .Q(REG_1_q));  // open: clr
  Register #(.width(16)) REG_7 (
    .D(controlled_buffer_2_out), .en(REG_7_WE), .clk(clock_1_out), .Q(REG_7_q));  // open: clr
  Controlled_Buffer #(.width(16)) controlled_buffer_3 (.in(REG_5_q), .out(REG_7_q));  // open: en
  Controlled_Buffer #(.width(16)) controlled_buffer_4 (.in(REG_6_q), .out(REG_7_q));  // open: en
  Register #(.width(16)) REG_8 (
    .D(controlled_buffer_2_out), .en(REG_8_WE), .clk(clock_1_out), .Q(REG_7_q));  // open: clr
  Register #(.width(5)) MAR_B (
    .D(instruction_splitter_1_address_a), .en(MAR_B_WE), .clk(clock_1_out), .Q(MAR_B_q));  // open: clr
  Controlled_Buffer #(.width(16)) controlled_buffer_5 (.in(REG_1_q), .out(controlled_buffer_5_out));  // open: en
  Register #(.width(16)) MBR_Z (.D(ram_1_dout), .en(MBR_Z_WE), .clk(clock_1_out), .Q(MBR_Z_q));  // open: clr
  Controlled_Buffer #(.width(16)) controlled_buffer_6 (.in(REG_7_q), .out(controlled_buffer_2_out));  // open: en
  assign controlled_buffer_7_out = MBR_Z_CB ? MBR_Z_q : 16'bz;  // Controlled_Buffer controlled_buffer_7
  Register #(.width(16)) MBR_A (.D(ram_2_dout), .en(MBR_A_WE), .clk(clock_1_out), .Q(MBR_A_q));  // open: clr
  assign controlled_buffer_5_out = MBR_A_CB ? MBR_A_q : 16'bz;  // Controlled_Buffer controlled_buffer_8
  Register #(.width(16)) MBR_B (.D(ram_4_dout), .en(MBR_B_WE), .clk(clock_1_out), .Q(MBR_B_q));  // open: clr
  Clock clock_1 (.out(clock_1_out));
  assign controlled_buffer_2_out = MBR_B_CB ? MBR_B_q : 16'bz;  // Controlled_Buffer controlled_buffer_9
  RAM #(.addrWidth(5), .dataWidth(16)) ram_1 (
    .addr(MAR_Z_q), .we(INSTRUCT_RAM_OE), .oe(INSTRUCT_RAM_WE), .clk(clock_1_out),
    .din(controlled_buffer_7_out), .dout(ram_1_dout));
  RAM #(.addrWidth(5), .dataWidth(16)) ram_2 (
    .addr(MAR_A_q), .we(RAM_A_WE), .oe(RAM_A_OE), .clk(clock_1_out), .din(controlled_buffer_5_out),
    .dout(ram_2_dout));
  RAM #(.addrWidth(5), .dataWidth(16)) ram_3 (
    .addr(MAR_Z_q), .we(SYSTEM_RAM_WE), .oe(SYSTEM_RAM_OE), .clk(clock_1_out), .din(controlled_buffer_7_out),
    .dout(ram_1_dout));
  RAM #(.addrWidth(5), .dataWidth(16)) ram_4 (
    .addr(MAR_B_q), .we(RAM_B_WE), .oe(RAM_B_OE), .clk(clock_1_out), .din(controlled_buffer_2_out),
    .dout(ram_4_dout));
  ROM #(.dataWidth(32)) rom_1 (.addr(register_1_q_2));  // open: data
  Counter #(.max('hf), .width(4)) counter_2 (
    .clk(clock_1_out), .Q(register_1_q_2[7:4]));  // open: clr, load, up, count, D, carry
endmodule

module comparator_1_bit (
  input  A,
  input  B,
  output A_EQUAL_B,
  output A_GREATER_B,
  output A_LESS_B
);

  wire and_1_out, and_2_out, not_1_out, not_2_out;

  not not_1 (not_1_out, A);
  not not_2 (not_2_out, B);
  and and_1 (and_1_out, not_1_out, not_2_out);
  and and_2 (and_2_out, A, B);
  and and_3 (A_GREATER_B, A, not_2_out);
  and and_4 (A_LESS_B, not_1_out, B);
  or or_1 (A_EQUAL_B, and_1_out, and_2_out);
endmodule

module comparator_2_bit (
  input  [1:0] A,
  input  [1:0] B,
  output A_EQUAL_B,
  output A_GREATER_B,
  output A_LESS_B
);

  wire and_1_out, and_2_out, and_3_out, and_4_out, and_5_out, and_6_out, and_7_out, and_8_out, and_9_out,
       and_10_out, not_1_out, not_2_out, not_3_out, not_4_out;

  not not_1 (not_1_out, A[1]);
  not not_2 (not_2_out, A[0]);
  not not_3 (not_3_out, B[1]);
  not not_4 (not_4_out, B[0]);
  and and_1 (and_1_out, not_1_out, not_2_out, not_3_out, not_4_out);
  and and_2 (and_2_out, not_1_out, A[0], not_3_out, B[0]);
  and and_3 (and_3_out, A[1], not_2_out, B[1], not_4_out);
  and and_4 (and_4_out, A[1], A[0], B[1], B[0]);
  and and_5 (and_5_out, A[0], not_3_out, not_4_out);
  and and_6 (and_6_out, A[1], not_3_out);
  or or_1 (A_GREATER_B, and_5_out, and_6_out, and_7_out);
  and and_7 (and_7_out, A[1], A[0], not_4_out);
  and and_8 (and_8_out, not_1_out, not_2_out, B[0]);
  and and_9 (and_9_out, not_1_out, B[1]);
  or or_2 (A_LESS_B, and_8_out, and_9_out, and_10_out);
  and and_10 (and_10_out, not_2_out, B[1], B[0]);
  or or_3 (A_EQUAL_B, and_1_out, and_2_out, and_3_out, and_4_out);
endmodule

module comparator_4_bit (
  input  [3:0] A,
  input  [3:0] B,
  output A_EQUAL_B,
  output A_GREATER_B,
  output A_LESS_B
);

  wire and_1_out, and_2_out, comparator_2_bit_1_a_equal_b, comparator_2_bit_1_a_greater_b,
       comparator_2_bit_1_a_less_b, comparator_2_bit_2_a_equal_b, comparator_2_bit_2_a_greater_b,
       comparator_2_bit_2_a_less_b;

  comparator_2_bit comparator_2_bit_1 (
    .A(A[1:0]), .B(B[1:0]), .A_EQUAL_B(comparator_2_bit_1_a_equal_b),
    .A_GREATER_B(comparator_2_bit_1_a_greater_b), .A_LESS_B(comparator_2_bit_1_a_less_b));
  comparator_2_bit comparator_2_bit_2 (
    .A(A[3:2]), .B(B[3:2]), .A_EQUAL_B(comparator_2_bit_2_a_equal_b),
    .A_GREATER_B(comparator_2_bit_2_a_greater_b), .A_LESS_B(comparator_2_bit_2_a_less_b));
  and and_1 (and_1_out, comparator_2_bit_1_a_less_b, comparator_2_bit_2_a_equal_b);
  and and_2 (and_2_out, comparator_2_bit_1_a_greater_b, comparator_2_bit_2_a_equal_b);
  and and_3 (A_EQUAL_B, comparator_2_bit_1_a_equal_b, comparator_2_bit_2_a_equal_b);
  or or_1 (A_GREATER_B, comparator_2_bit_2_a_greater_b, and_2_out);
  or or_2 (A_LESS_B, and_1_out, comparator_2_bit_2_a_less_b);
endmodule

module comparator_8_bit (
  input  [7:0] A,
  input  [7:0] B,
  output A_EQUAL_B,
  output A_GREATER_B,
  output A_LESS_B
);

  wire and_1_out, and_2_out, comparator_4_bit_1_a_equal_b, comparator_4_bit_1_a_greater_b,
       comparator_4_bit_1_a_less_b, comparator_4_bit_2_a_equal_b, comparator_4_bit_2_a_greater_b,
       comparator_4_bit_2_a_less_b;

  comparator_4_bit comparator_4_bit_1 (
    .A(A[3:0]), .B(B[3:0]), .A_EQUAL_B(comparator_4_bit_1_a_equal_b),
    .A_GREATER_B(comparator_4_bit_1_a_greater_b), .A_LESS_B(comparator_4_bit_1_a_less_b));
  comparator_4_bit comparator_4_bit_2 (
    .A(A[7:4]), .B(B[7:4]), .A_EQUAL_B(comparator_4_bit_2_a_equal_b),
    .A_GREATER_B(comparator_4_bit_2_a_greater_b), .A_LESS_B(comparator_4_bit_2_a_less_b));
  and and_1 (and_1_out, comparator_4_bit_1_a_less_b, comparator_4_bit_2_a_equal_b);
  and and_2 (and_2_out, comparator_4_bit_1_a_greater_b, comparator_4_bit_2_a_equal_b);
  and and_3 (A_EQUAL_B, comparator_4_bit_1_a_equal_b, comparator_4_bit_2_a_equal_b);
  or or_1 (A_GREATER_B, comparator_4_bit_2_a_greater_b, and_2_out);
  or or_2 (A_LESS_B, and_1_out, comparator_4_bit_2_a_less_b);
endmodule

module comparator_16_bit (
  input  [15:0] A,
  input  [15:0] B,
  output [15:0] Result
);

  wire and_1_out, and_2_out, and_3_out, comparator_8_bit_1_a_equal_b, comparator_8_bit_1_a_greater_b,
       comparator_8_bit_1_a_less_b, comparator_8_bit_2_a_equal_b, comparator_8_bit_2_a_greater_b,
       comparator_8_bit_2_a_less_b, or_1_out, or_2_out;
  wire [2:0] controlled_buffer_1_out;

  comparator_8_bit comparator_8_bit_1 (
    .A(A[7:0]), .B(B[7:0]), .A_EQUAL_B(comparator_8_bit_1_a_equal_b),
    .A_GREATER_B(comparator_8_bit_1_a_greater_b), .A_LESS_B(comparator_8_bit_1_a_less_b));
  comparator_8_bit comparator_8_bit_2 (
    .A(A[15:8]), .B(B[15:8]), .A_EQUAL_B(comparator_8_bit_2_a_equal_b),
    .A_GREATER_B(comparator_8_bit_2_a_greater_b), .A_LESS_B(comparator_8_bit_2_a_less_b));
  and and_1 (and_1_out, comparator_8_bit_1_a_less_b, comparator_8_bit_2_a_equal_b);
  and and_2 (and_2_out, comparator_8_bit_1_a_greater_b, comparator_8_bit_2_a_equal_b);
  and and_3 (and_3_out, comparator_8_bit_1_a_equal_b, comparator_8_bit_2_a_equal_b);
  or or_1 (or_1_out, comparator_8_bit_2_a_greater_b, and_2_out);
  or or_2 (or_2_out, and_1_out, comparator_8_bit_2_a_less_b);
  assign controlled_buffer_1_out = and_3_out ? 3'b010 : 3'bz;  // Controlled_Buffer controlled_buffer_1
  assign controlled_buffer_1_out = or_1_out ? 3'b100 : 3'bz;  // Controlled_Buffer controlled_buffer_2
  assign controlled_buffer_1_out = or_2_out ? 3'b001 : 3'bz;  // Controlled_Buffer controlled_buffer_3
  assign Result = {{13{1'b0}}, controlled_buffer_1_out};  // Bit_Extender bit_extender_1

  // Notes on the sheet:
  //   A = B
  //   A>B
  //   A<B
  //   010 / 2 => A = B
  //   001 / 1 => A < B
  //   100 / 4 => A > B
endmodule

module two_bit_comparator (
  input  [1:0] A,
  input  [1:0] B,
  output A_Equal_B,
  output A_Greater_B,
  output A_Less_B
);

  wire and_1_out, and_2_out, comparator_1_bit_1_a_equal_b, comparator_1_bit_1_a_greater_b,
       comparator_1_bit_1_a_less_b, comparator_1_bit_2_a_equal_b, comparator_1_bit_2_a_greater_b,
       comparator_1_bit_2_a_less_b;

  comparator_1_bit comparator_1_bit_1 (
    .A(A[0]), .B(B[0]), .A_EQUAL_B(comparator_1_bit_1_a_equal_b),
    .A_GREATER_B(comparator_1_bit_1_a_greater_b), .A_LESS_B(comparator_1_bit_1_a_less_b));
  comparator_1_bit comparator_1_bit_2 (
    .A(A[1]), .B(B[1]), .A_EQUAL_B(comparator_1_bit_2_a_equal_b),
    .A_GREATER_B(comparator_1_bit_2_a_greater_b), .A_LESS_B(comparator_1_bit_2_a_less_b));
  and and_1 (and_1_out, comparator_1_bit_1_a_less_b, comparator_1_bit_2_a_equal_b);
  and and_2 (and_2_out, comparator_1_bit_1_a_greater_b, comparator_1_bit_2_a_equal_b);
  and and_3 (A_Equal_B, comparator_1_bit_1_a_equal_b, comparator_1_bit_2_a_equal_b);
  or or_1 (A_Greater_B, comparator_1_bit_2_a_greater_b, and_2_out);
  or or_2 (A_Less_B, and_1_out, comparator_1_bit_2_a_less_b);

  // Notes on the sheet:
  //   Least Significant 
  //   Most Significant
endmodule

module Multiplier_8x8 (
  input  [7:0] A,
  input  [7:0] B,
  output [15:0] Product
);

  wire [3:0] undriven_2, undriven_3, undriven_4, undriven_5;
  wire [7:0] multiplier_4x4_1_product, multiplier_4x4_2_product, multiplier_4x4_3_product,
       multiplier_4x4_4_product, undriven, undriven_6;
  wire [15:0] sixteenbitadder_1_sum, sixteenbitadder_2_sum;

  // Probe on A
  // Probe on B
  Multiplier_4x4 multiplier_4x4_1 (.B(B[3:0]), .A(A[7:4]), .Product(multiplier_4x4_1_product));
  Multiplier_4x4 multiplier_4x4_2 (.B(B[7:4]), .A(A[7:4]), .Product(multiplier_4x4_2_product));
  Multiplier_4x4 multiplier_4x4_3 (.B(B[3:0]), .A(A[3:0]), .Product(multiplier_4x4_3_product));
  Multiplier_4x4 multiplier_4x4_4 (.B(B[7:4]), .A(A[3:0]), .Product(multiplier_4x4_4_product));
  SixteenBitAdder sixteenbitadder_1 (
    .A({undriven, multiplier_4x4_3_product}), .B({undriven_5, multiplier_4x4_4_product, undriven_4}),
    .Sum(sixteenbitadder_1_sum));  // open: CarryIn, CarryOut
  SixteenBitAdder sixteenbitadder_2 (
    .A({undriven_3, multiplier_4x4_1_product, undriven_2}), .B({multiplier_4x4_2_product, undriven_6}),
    .Sum(sixteenbitadder_2_sum));  // open: CarryIn, CarryOut
  // Probe on Product
  SixteenBitAdder sixteenbitadder_3 (
    .A(sixteenbitadder_1_sum), .B(sixteenbitadder_2_sum), .Sum(Product));  // open: CarryIn, CarryOut
endmodule

module Buses_V2 (
  input  in_1,
  input  in_2,
  input  Program_Counter_Increament_By_One,
  input  MAR_Z_WE,
  input  Instruction_Ram_OE,
  input  MBR_Z_WE,
  input  Instruction_Splitter_WE,
  input  MAR_A_WE,
  input  MAR_B_WE,
  input  RAM_A_OE,
  input  Ram_B_OE,
  input  MBR_A_WE,
  input  MBR_B_WE,
  input  Reg_A0_WE,
  input  Reg_B0_WE,
  input  Reg_Out_WE,
  input  Instrction_Ram_WE,
  input  Ram_A_WE,
  input  Ram_B_WE,
  input  OPCODE_WE,
  input  MBR_Z_OE,
  input  MBR_A_OE,
  input  MBR_B_OE,
  input  Reset_Clock,
  input  System_Ram_WE,
  input  System_ram_oe,
  input  reg_out_oe,
  input  Instrction_Ram_CB,
  input  in_29,
  input  in_30,
  input  in_31,
  input  in_32,
  input  in_33,
  input  in_34,
  input  in_35,
  input  in_36,
  input  in_37,
  input  in_38
);

  wire Clock_Main_out, controlled_buffer_6_out, instruction_splitter_1_flag_bit;
  wire [4:0] Current_Opcode_q, instruction_splitter_1_address_a, instruction_splitter_1_address_b,
       instruction_splitter_1_opcode, MAR_A_q, MAR_B_q, MAR_Z_q, ProgramCounter_q;
  wire [15:0] alu_16_bits_1_over_flow, controlled_buffer_1_out, controlled_buffer_3_out,
       controlled_buffer_4_out, controlled_buffer_5_out, MBR_A_q, MBR_B_q, MBR_Z_q, ram_1_dout, Ram_A_dout,
       Ram_B_dout, Reg_A0_q, Reg_B0_q, Reg_Out_q;

  Register #(.width(5)) Current_Opcode (
    .D(instruction_splitter_1_opcode), .en(OPCODE_WE), .clk(Clock_Main_out), .Q(Current_Opcode_q));  // open: clr
  // Probe on Reg_B0_q
  Register #(.width(16)) Reg_B0 (
    .D(controlled_buffer_5_out), .en(Reg_B0_WE), .clk(Clock_Main_out), .Q(Reg_B0_q));  // open: clr
  Register #(.width(16)) Reg_B2 (.D(controlled_buffer_5_out));  // open: en, clk, Q, clr
  Clock Clock_Main (.out(Clock_Main_out));
  // Probe on Reg_A0_q
  Register #(.width(16)) Reg_B1 (.D(controlled_buffer_5_out));  // open: en, clk, Q, clr
  Register #(.width(16)) Reg_B3 (.D(controlled_buffer_5_out));  // open: en, clk, Q, clr
  Counter #(.max('h1f), .width(5)) ProgramCounter (
    .clr(Reset_Clock), .up(1'b1), .count(Program_Counter_Increament_By_One), .clk(Clock_Main_out),
    .Q(ProgramCounter_q));  // open: load, D, carry
  ALU_16_bits alu_16_bits_1 (
    .Opcode(Current_Opcode_q), .Flag(instruction_splitter_1_flag_bit), .Reg_A(Reg_A0_q), .Reg_B(Reg_B0_q),
    .Over_Flow(alu_16_bits_1_over_flow));  // open: Reg_Out
  Register #(.width(16)) Reg_A0 (
    .D(controlled_buffer_4_out), .en(Reg_A0_WE), .clk(Clock_Main_out), .Q(Reg_A0_q));  // open: clr
  Register #(.width(16)) Reg_A2 (.D(controlled_buffer_4_out));  // open: en, clk, Q, clr
  Instruction_splitter instruction_splitter_1 (
    .Instruction_Input(controlled_buffer_3_out), .WE(Instruction_Splitter_WE), .Clock(Clock_Main_out),
    .Address_B(instruction_splitter_1_address_b), .Address_A(instruction_splitter_1_address_a),
    .OPCODE(instruction_splitter_1_opcode), .FLAG_BIT(instruction_splitter_1_flag_bit));
  // Probe on Reg_Out_q
  Register #(.width(16)) Reg_A1 (.D(controlled_buffer_4_out));  // open: en, clk, Q, clr
  Register #(.width(16)) Reg_A3 (.D(controlled_buffer_4_out));  // open: en, clk, Q, clr
  Register #(.width(16)) Reg_Out (
    .D(alu_16_bits_1_over_flow), .en(Reg_Out_WE), .clk(Clock_Main_out), .Q(Reg_Out_q));  // open: clr
  Register #(.width(5)) MAR_Z (.D(ProgramCounter_q), .en(MAR_Z_WE), .clk(Clock_Main_out), .Q(MAR_Z_q));  // open: clr
  Register #(.width(5)) MAR_A (
    .D(instruction_splitter_1_address_b), .en(MAR_A_WE), .clk(Clock_Main_out), .Q(MAR_A_q));  // open: clr
  assign controlled_buffer_1_out = reg_out_oe ? Reg_Out_q : 16'bz;  // Controlled_Buffer controlled_buffer_1
  Register #(.width(16)) MBR_Z (
    .D(controlled_buffer_1_out), .en(MBR_Z_WE), .clk(Clock_Main_out), .Q(MBR_Z_q));  // open: clr
  Register #(.width(5)) MAR_B (
    .D(instruction_splitter_1_address_a), .en(MAR_B_WE), .clk(Clock_Main_out), .Q(MAR_B_q));  // open: clr
  // Probe on controlled_buffer_1_out
  assign controlled_buffer_1_out = Instrction_Ram_CB ? ram_1_dout : 16'bz;  // Controlled_Buffer controlled_buffer_2
  assign controlled_buffer_3_out = MBR_Z_OE ? MBR_Z_q : 16'bz;  // Controlled_Buffer controlled_buffer_3
  Register #(.width(16)) MBR_A (.D(Ram_A_dout), .en(MBR_A_WE), .clk(Clock_Main_out), .Q(MBR_A_q));  // open: clr
  Register #(.width(16)) MBR_B (.D(Ram_B_dout), .en(MBR_B_WE), .clk(Clock_Main_out), .Q(MBR_B_q));  // open: clr
  assign controlled_buffer_4_out = MBR_A_OE ? MBR_A_q : 16'bz;  // Controlled_Buffer controlled_buffer_4
  assign controlled_buffer_5_out = MBR_B_OE ? MBR_B_q : 16'bz;  // Controlled_Buffer controlled_buffer_5
  RAM #(.addrWidth(5), .dataWidth(16)) ram_1 (
    .addr(MAR_Z_q), .we(Instrction_Ram_WE), .oe(Instruction_Ram_OE), .clk(Clock_Main_out),
    .din(controlled_buffer_3_out), .dout(ram_1_dout));
  RAM #(.addrWidth(5), .dataWidth(16)) Ram_A (
    .addr(MAR_A_q), .we(Ram_A_WE), .oe(RAM_A_OE), .clk(Clock_Main_out), .din(controlled_buffer_4_out),
    .dout(Ram_A_dout));
  RAM #(.addrWidth(5), .dataWidth(16)) Ram_B (
    .addr(MAR_B_q), .we(Ram_B_WE), .oe(Ram_B_OE), .clk(Clock_Main_out), .din(controlled_buffer_5_out),
    .dout(Ram_B_dout));
  RAM #(.addrWidth(5), .dataWidth(16)) ram_2 (
    .addr(MAR_A_q), .we(System_Ram_WE), .oe(System_ram_oe), .clk(Clock_Main_out),
    .din(controlled_buffer_3_out));  // open: dout
  assign controlled_buffer_6_out = in_2 ? in_1 : 1'bz;  // Controlled_Buffer controlled_buffer_6
  LED led_1 (.in(controlled_buffer_6_out));
endmodule

module Opcode_Decoder (
  input  [15:0] _0000,
  input  [15:0] Addition_And_Subtraction,
  input  [15:0] _0010,
  input  [15:0] _0100,
  input  [15:0] _1000,
  input  [15:0] Xor_Operation,
  input  [15:0] _0110,
  input  [15:0] Multiplication,
  input  [15:0] Comparation,
  input  [15:0] _1001,
  input  [15:0] Not_Operation,
  input  [15:0] _0101,
  input  [15:0] And_Operation,
  input  [15:0] _0111,
  input  [15:0] _1110,
  input  [15:0] _1111,
  input  A,
  input  B,
  input  C,
  input  D,
  output [15:0] Result
);

  wire and_1_out, and_2_out, and_3_out, and_4_out, and_5_out, and_6_out, and_7_out, and_8_out, and_9_out,
       and_10_out, and_11_out, and_12_out, and_13_out, and_14_out, and_15_out, and_16_out, not_1_out,
       not_2_out, not_3_out, not_4_out;
  wire [15:0] and_17_out, and_18_out, and_19_out, and_20_out, and_21_out, and_22_out, and_23_out, and_24_out,
       and_25_out, and_26_out, and_27_out, and_28_out, and_29_out, and_30_out, and_31_out, and_32_out,
       bit_extender_1_out, bit_extender_2_out, bit_extender_3_out, bit_extender_4_out, bit_extender_5_out,
       bit_extender_6_out, bit_extender_7_out, bit_extender_8_out, bit_extender_9_out, bit_extender_10_out,
       bit_extender_11_out, bit_extender_12_out, bit_extender_13_out, bit_extender_14_out,
       bit_extender_15_out, bit_extender_16_out;

  not not_1 (not_1_out, A);
  not not_2 (not_2_out, B);
  not not_3 (not_3_out, C);
  not not_4 (not_4_out, D);
  and and_1 (and_1_out, not_1_out, not_2_out, not_3_out, not_4_out);
  and and_2 (and_2_out, not_1_out, not_2_out, not_3_out, D);
  and and_3 (and_3_out, not_1_out, not_2_out, C, not_4_out);
  and and_4 (and_4_out, not_1_out, B, not_3_out, not_4_out);
  and and_5 (and_5_out, A, not_2_out, not_3_out, not_4_out);
  and and_6 (and_6_out, A, B, not_3_out, not_4_out);
  and and_7 (and_7_out, not_1_out, B, C, not_4_out);
  and and_8 (and_8_out, not_1_out, not_2_out, C, D);
  and and_9 (and_9_out, A, not_2_out, C, not_4_out);
  and and_10 (and_10_out, A, not_2_out, not_3_out, D);
  and and_11 (and_11_out, A, B, not_3_out, D);
  and and_12 (and_12_out, not_1_out, B, not_3_out, D);
  and and_13 (and_13_out, A, not_2_out, C, D);
  and and_14 (and_14_out, not_1_out, B, C, D);
  and and_15 (and_15_out, A, B, C, not_4_out);
  and and_16 (and_16_out, A, B, C, D);
  assign bit_extender_1_out = {{15{and_1_out}}, and_1_out};  // Bit_Extender bit_extender_1
  assign bit_extender_2_out = {{15{and_2_out}}, and_2_out};  // Bit_Extender bit_extender_2
  assign bit_extender_3_out = {{15{and_3_out}}, and_3_out};  // Bit_Extender bit_extender_3
  assign bit_extender_4_out = {{15{and_4_out}}, and_4_out};  // Bit_Extender bit_extender_4
  assign bit_extender_5_out = {{15{and_5_out}}, and_5_out};  // Bit_Extender bit_extender_5
  assign bit_extender_6_out = {{15{and_6_out}}, and_6_out};  // Bit_Extender bit_extender_6
  assign bit_extender_7_out = {{15{and_7_out}}, and_7_out};  // Bit_Extender bit_extender_7
  assign bit_extender_8_out = {{15{and_8_out}}, and_8_out};  // Bit_Extender bit_extender_8
  assign bit_extender_9_out = {{15{and_9_out}}, and_9_out};  // Bit_Extender bit_extender_9
  assign bit_extender_10_out = {{15{and_10_out}}, and_10_out};  // Bit_Extender bit_extender_10
  assign bit_extender_11_out = {{15{and_11_out}}, and_11_out};  // Bit_Extender bit_extender_11
  assign bit_extender_12_out = {{15{and_12_out}}, and_12_out};  // Bit_Extender bit_extender_12
  assign bit_extender_13_out = {{15{and_13_out}}, and_13_out};  // Bit_Extender bit_extender_13
  assign bit_extender_14_out = {{15{and_14_out}}, and_14_out};  // Bit_Extender bit_extender_14
  assign bit_extender_15_out = {{15{and_15_out}}, and_15_out};  // Bit_Extender bit_extender_15
  assign bit_extender_16_out = {{15{and_16_out}}, and_16_out};  // Bit_Extender bit_extender_16
  assign and_17_out = bit_extender_1_out & _0000;  // AND_Gate and_17, 16 bits wide
  assign and_18_out = Addition_And_Subtraction & bit_extender_2_out;  // AND_Gate and_18, 16 bits wide
  assign and_19_out = _0010 & bit_extender_3_out;  // AND_Gate and_19, 16 bits wide
  assign and_20_out = _0100 & bit_extender_4_out;  // AND_Gate and_20, 16 bits wide
  assign and_21_out = _1000 & bit_extender_5_out;  // AND_Gate and_21, 16 bits wide
  assign and_22_out = Xor_Operation & bit_extender_6_out;  // AND_Gate and_22, 16 bits wide
  assign and_23_out = _0110 & bit_extender_7_out;  // AND_Gate and_23, 16 bits wide
  assign and_24_out = Multiplication & bit_extender_8_out;  // AND_Gate and_24, 16 bits wide
  assign and_25_out = Comparation & bit_extender_9_out;  // AND_Gate and_25, 16 bits wide
  assign and_26_out = _1001 & bit_extender_10_out;  // AND_Gate and_26, 16 bits wide
  assign and_27_out = Not_Operation & bit_extender_11_out;  // AND_Gate and_27, 16 bits wide
  assign and_28_out = _0101 & bit_extender_12_out;  // AND_Gate and_28, 16 bits wide
  assign and_29_out = And_Operation & bit_extender_13_out;  // AND_Gate and_29, 16 bits wide
  assign and_30_out = _0111 & bit_extender_14_out;  // AND_Gate and_30, 16 bits wide
  assign and_31_out = _1110 & bit_extender_15_out;  // AND_Gate and_31, 16 bits wide
  assign and_32_out = _1111 & bit_extender_16_out;  // AND_Gate and_32, 16 bits wide
  assign Result = and_17_out | and_18_out | and_19_out | and_20_out | and_21_out | and_22_out | and_23_out | and_24_out | and_25_out | and_26_out | and_27_out | and_28_out | and_29_out | and_30_out | and_31_out | and_32_out;  // OR_Gate or_1, 16 bits wide

  // Notes on the sheet:
  //   A' B' C' D'
  //   A' B' C' D
  //   A' B' C D'
  //   A' B C' D'
  //   A B' C' D'
  //   A B C' D'
  //   A' B C D'
  //   A' B' C D
  //   A B' C D'
  //   A B' C' D
  //   A B C' D
  //   A' B C' D
  //   A B' C D
  //   A' B C D
  //   A B C D'
  //   A B C D
  //   0000
  //   0001
  //   0010
  //   0100
  //   1000
  //   1100
  //   0110
  //   0011
  //   1010
  //   1001
  //   1101
  //   0101
  //   1011
  //   0111
  //   1110
  //   1111
  //   0001
  //   1100
  //   0011
  //   1010
  //   1101
  //   1011
endmodule

module ALU_16_bits (
  input  [4:0] Opcode,
  input  Flag,
  input  [15:0] Reg_A,
  input  [15:0] Reg_B,
  output [15:0] Over_Flow,
  output [15:0] Reg_Out
);

  wire and_1_out, and_2_out, controlled_buffer_3_out, not_1_out, not_2_out, not_3_out, not_4_out, not_5_out,
       not_6_out, sixteenbitadder_1_carryout;
  wire [7:0] bitselector_1_out, bitselector_2_out;
  wire [15:0] and_operation_1_result, bit_extender_1_out, comparator_16_bit_1_result,
       controlled_buffer_1_out, multiplier_8x8_1_product, not_operation_1_result, sixteenbitadder_1_sum,
       sixteenbitaddsub_1_result, xor_operation_1_result;

  // Probe on Reg_A
  // Probe on Reg_B
  not not_1 (not_1_out, Opcode[1]);
  not not_2 (not_2_out, Opcode[2]);
  not not_3 (not_3_out, Opcode[3]);
  not not_4 (not_4_out, Flag);
  assign bit_extender_1_out = {{15{Flag}}, Flag};  // Bit_Extender bit_extender_1
  and and_1 (and_1_out, Opcode[0], not_1_out, not_2_out, not_3_out);
  and and_2 (and_2_out, and_1_out, not_4_out);
  SixteenBitAddSub sixteenbitaddsub_1 (
    .CarryIn(Flag), .A(Reg_A), .B(Reg_B), .Sub(bit_extender_1_out), .Result(sixteenbitaddsub_1_result));  // open: CarryOut
  BitSelector #(.group(8), .width(16)) bitselector_1 (.in(Reg_A), .out(bitselector_1_out), .sel(1'b0));
  BitSelector #(.group(8), .width(16)) bitselector_2 (.in(Reg_B), .out(bitselector_2_out), .sel(1'b0));
  SixteenBitAdder sixteenbitadder_1 (
    .A(Reg_A), .B(Reg_B), .Sum(sixteenbitadder_1_sum), .CarryOut(sixteenbitadder_1_carryout));  // open: CarryIn
  Multiplier_8x8 multiplier_8x8_1 (.A(bitselector_1_out), .B(bitselector_2_out), .Product(multiplier_8x8_1_product));
  And_Operation and_operation_1 (.A(Reg_A), .B(Reg_B), .Result(and_operation_1_result));
  XOR_Operation xor_operation_1 (.A(Reg_A), .B(Reg_B), .Result(xor_operation_1_result));
  NOT_Operation not_operation_1 (.A(Reg_A), .Result(not_operation_1_result));
  comparator_16_bit comparator_16_bit_1 (.A(Reg_A), .B(Reg_B), .Result(comparator_16_bit_1_result));
  not not_5 (not_5_out, Flag);
  assign controlled_buffer_1_out = Flag ? sixteenbitaddsub_1_result : 16'bz;  // Controlled_Buffer controlled_buffer_1
  assign controlled_buffer_1_out = not_5_out ? sixteenbitadder_1_sum : 16'bz;  // Controlled_Buffer controlled_buffer_2
  Opcode_Decoder opcode_decoder_1 (
    .Addition_And_Subtraction(controlled_buffer_1_out), .Xor_Operation(xor_operation_1_result),
    .Multiplication(multiplier_8x8_1_product), .Comparation(comparator_16_bit_1_result),
    .Not_Operation(not_operation_1_result), .And_Operation(and_operation_1_result), .A(Opcode[3]),
    .B(Opcode[2]), .C(Opcode[1]), .D(Opcode[0]), .Result(Reg_Out));  // open: _0000, _0010, _0100, _1000, _0110, _1001, _0101, _0111, _1110, _1111
  assign controlled_buffer_3_out = and_2_out ? sixteenbitadder_1_carryout : 1'bz;  // Controlled_Buffer controlled_buffer_3
  not not_6 (not_6_out, and_2_out);
  // Probe on Reg_Out
  assign Over_Flow = {{15{1'b0}}, controlled_buffer_3_out};  // Bit_Extender bit_extender_2
  assign Over_Flow = not_6_out ? {16{1'b0}} : 16'bz;  // Controlled_Buffer controlled_buffer_4

  // Notes on the sheet:
  //   0000  --- Load
  //   0001-----Add
  //   0011 ---- mult
  //   1100------ XOR
  //   1101 ----- NOT
  //   1011  --- AND
  //   0001 with flag  --  sub
  //   1010  --- comparation
endmodule

module And_Operation (
  input  [15:0] A,
  input  [15:0] B,
  output [15:0] Result
);

  assign Result = A & B;  // AND_Gate and_1, 16 bits wide
endmodule

module XOR_Operation (
  input  [15:0] A,
  input  [15:0] B,
  output [15:0] Result
);

  // Probe on A
  // Probe on B
  assign Result = A ^ B;  // XOR_Gate xor_1, 16 bits wide
  // Probe on Result
endmodule

module NOT_Operation (
  input  [15:0] A,
  output [15:0] Result
);

  assign Result = ~A;  // NOT_Gate not_1, 16 bits wide
endmodule

module BinaryToHex (
  input  [7:0] in_1,
  input  [7:0] in_2,
  input  [4:0] in_3,
  input  [4:0] in_4,
  input  [15:0] in_5,
  input  [15:0] in_6,
  input  [15:0] Instruction_Input,
  input  WE,
  input  Clock,
  output [7:0] out_10,
  output [7:0] out_11,
  output [4:0] out_12,
  output [4:0] out_13,
  output [15:0] out_14,
  output [15:0] out_15,
  output [4:0] Address_B,
  output [4:0] Address_A,
  output [4:0] OPCODE,
  output FLAG_BIT
);

  // Probe on in_5
  // Probe on in_6
  Register #(.width(16)) register_1 (
    .D(Instruction_Input), .en(WE), .clk(Clock), .Q({FLAG_BIT, OPCODE, Address_A, Address_B}));  // open: clr

  assign out_10 = in_1;
  assign out_11 = in_2;
  assign out_12 = in_3;
  assign out_13 = in_4;
  assign out_14 = in_5;
  assign out_15 = in_6;
endmodule

module PCU (
);

  wire Clock_Main_out, instruction_splitter_1_flag_bit;
  wire [3:0] Step_Counter_q;
  wire [4:0] instruction_splitter_1_address_a, instruction_splitter_1_address_b,
       instruction_splitter_1_opcode, MAR_A_q, MAR_B_q, MAR_Z_q, ProgramCounter_q;
  wire [4:4] Current_Opcode_q;
  wire [7:4] Current_Opcode_q_2;
  wire [15:0] alu_16_bits_1_reg_out, controlled_buffer_1_out, controlled_buffer_3_out,
       controlled_buffer_4_out, controlled_buffer_5_out, Instruction_Ram_dout, MBR_A_q, MBR_B_q, MBR_Z_q,
       Ram_A_dout, Ram_B_dout, Reg_A0_q, Reg_B0_q, Reg_Out_q;
  wire [31:0] rom_1_data;

  Register #(.width(5)) Current_Opcode (
    .D(instruction_splitter_1_opcode), .en(rom_1_data[14]), .clk(Clock_Main_out),
    .Q({Current_Opcode_q[4], Current_Opcode_q_2}));  // open: clr
  // Probe on Reg_B0_q
  Register #(.width(16)) Reg_B0 (
    .D(controlled_buffer_5_out), .en(rom_1_data[19]), .clk(Clock_Main_out), .Q(Reg_B0_q));  // open: clr
  Register #(.width(16)) Reg_B2 (.D(controlled_buffer_5_out), .en(rom_1_data[6]));  // open: clk, Q, clr
  Clock Clock_Main (.out(Clock_Main_out));
  // Probe on Reg_A0_q
  Register #(.width(16)) Reg_B1 (.D(controlled_buffer_5_out), .en(rom_1_data[7]));  // open: clk, Q, clr
  Register #(.width(16)) Reg_B3 (.D(controlled_buffer_5_out), .en(rom_1_data[5]));  // open: clk, Q, clr
  Counter #(.max('h1f), .width(5)) ProgramCounter (
    .up(1'b1), .count(rom_1_data[31]), .clk(Clock_Main_out), .Q(ProgramCounter_q));  // open: clr, load, D, carry
  // Probe on alu_16_bits_1_reg_out
  ALU_16_bits alu_16_bits_1 (
    .Opcode({Current_Opcode_q[4], Current_Opcode_q_2}), .Flag(instruction_splitter_1_flag_bit),
    .Reg_A(Reg_A0_q), .Reg_B(Reg_B0_q), .Reg_Out(alu_16_bits_1_reg_out));  // open: Over_Flow
  Register #(.width(16)) Reg_A0 (
    .D(controlled_buffer_4_out), .en(rom_1_data[20]), .clk(Clock_Main_out), .Q(Reg_A0_q));  // open: clr
  Register #(.width(16)) Reg_A2 (.D(controlled_buffer_4_out), .en(rom_1_data[9]));  // open: clk, Q, clr
  Instruction_splitter instruction_splitter_1 (
    .Instruction_Input(controlled_buffer_3_out), .WE(rom_1_data[27]), .Clock(Clock_Main_out),
    .Address_B(instruction_splitter_1_address_b), .Address_A(instruction_splitter_1_address_a),
    .OPCODE(instruction_splitter_1_opcode), .FLAG_BIT(instruction_splitter_1_flag_bit));
  // Probe on Reg_Out_q
  Register #(.width(16)) Reg_A1 (.D(controlled_buffer_4_out), .en(rom_1_data[10]));  // open: clk, Q, clr
  Register #(.width(16)) Reg_A3 (.D(controlled_buffer_4_out), .en(rom_1_data[8]));  // open: clk, Q, clr
  Register #(.width(16)) Reg_Out (
    .D(alu_16_bits_1_reg_out), .en(rom_1_data[18]), .clk(Clock_Main_out), .Q(Reg_Out_q));  // open: clr
  Register #(.width(5)) MAR_Z (
    .D(ProgramCounter_q), .en(rom_1_data[30]), .clk(Clock_Main_out), .Q(MAR_Z_q));  // open: clr
  assign controlled_buffer_1_out = rom_1_data[2] ? Reg_Out_q : 16'bz;  // Controlled_Buffer controlled_buffer_1
  Register #(.width(5)) MAR_A (
    .D(instruction_splitter_1_address_a), .en(rom_1_data[26]), .clk(Clock_Main_out), .Q(MAR_A_q));  // open: clr
  assign controlled_buffer_1_out = rom_1_data[1] ? Instruction_Ram_dout : 16'bz;  // Controlled_Buffer controlled_buffer_2
  Register #(.width(16)) MBR_Z (
    .D(controlled_buffer_1_out), .en(rom_1_data[28]), .clk(Clock_Main_out), .Q(MBR_Z_q));  // open: clr
  Register #(.width(5)) MAR_B (
    .D(instruction_splitter_1_address_b), .en(rom_1_data[25]), .clk(Clock_Main_out), .Q(MAR_B_q));  // open: clr
  assign controlled_buffer_3_out = rom_1_data[13] ? MBR_Z_q : 16'bz;  // Controlled_Buffer controlled_buffer_3
  Register #(.width(16)) MBR_A (.D(Ram_A_dout), .en(rom_1_data[22]), .clk(Clock_Main_out), .Q(MBR_A_q));  // open: clr
  Register #(.width(16)) MBR_B (.D(Ram_B_dout), .en(rom_1_data[21]), .clk(Clock_Main_out), .Q(MBR_B_q));  // open: clr
  assign controlled_buffer_4_out = rom_1_data[12] ? MBR_A_q : 16'bz;  // Controlled_Buffer controlled_buffer_4
  assign controlled_buffer_5_out = rom_1_data[11] ? MBR_B_q : 16'bz;  // Controlled_Buffer controlled_buffer_5
  RAM #(.addrWidth(5), .dataWidth(16)) Instruction_Ram (
    .addr(MAR_Z_q), .we(rom_1_data[17]), .oe(rom_1_data[29]), .clk(Clock_Main_out),
    .din(controlled_buffer_3_out), .dout(Instruction_Ram_dout));
  RAM #(.addrWidth(5), .dataWidth(16)) Ram_A (
    .addr(MAR_A_q), .we(rom_1_data[16]), .oe(rom_1_data[24]), .clk(Clock_Main_out),
    .din(controlled_buffer_4_out), .dout(Ram_A_dout));
  // Probe on Instruction_Ram_dout
  RAM #(.addrWidth(5), .dataWidth(16)) Ram_B (
    .addr(MAR_B_q), .we(rom_1_data[15]), .oe(rom_1_data[23]), .clk(Clock_Main_out),
    .din(controlled_buffer_5_out), .dout(Ram_B_dout));
  RAM #(.addrWidth(5), .dataWidth(16)) System_Ram (
    .addr(MAR_A_q), .we(rom_1_data[3]), .oe(rom_1_data[4]), .clk(Clock_Main_out),
    .din(controlled_buffer_3_out));  // open: dout
  Counter #(.max('h7), .width(4)) Step_Counter (
    .clr(rom_1_data[0]), .up(1'b1), .count(1'b1), .clk(Clock_Main_out), .Q(Step_Counter_q));  // open: load, D, carry
  ROM #(.dataWidth(32)) rom_1 (.addr({Current_Opcode_q_2, Step_Counter_q}), .data(rom_1_data));
  // Probe on rom_1_data

  // Notes on the sheet:
  //   MAR_Z_WE
  //   Instruction_Ram_OE
  //   MBR_Z_WE
  //   MAR_A_WE
  //   MAR_B_WE
  //   RAM_A_OE
  //   Ram_B_OE
  //   MBR_A_WE
  //   MBR_B_WE
  //   Reg_A0_WE
  //   Reg_B0_WE
  //   Reg_Out_WE
  //   Ram_A_WE
  //   Ram_B_WE
  //   OPCODE_WE
  //   MBR_Z_OE
  //   MBR_A_OE
  //   MBR_B_OE
  //   Reg_A1_WE
  //   Reg_A2_WE
  //   Reg_A3_WE
  //   Reg_B1_WE
  //   Reg_B2_WE
  //   Reg_B3_WE
  //   System_Ram_OE
  //   System_Ram_WE
  //   RegOut_OE
  //   Instrction_Ram_to_MBR_CB
  //   Clock_Reset
  //   Program_Counter_Increament_By_One
  //   Instruction_Splitter_WE
  //   Instrction_Ram_WE
  //   Opcode
  //   Step Counter
  //   contents of rom_1 (hex, n*v repeats v):
  //   e0000000 50002002 8002000 6004000 1800000 600000 181800 40000 8*0 e0000000 50002002 8002000 6004000
  //   1800000 600000 181800 40000 8*0 e0000000 50002002 8002000 6004000 1800000 600000 181800 40000 8*0
  //   e0000000 50002002 8002000 6004000 1800000 600000 181800 40000 8*0 e0000000 50002002 8002000 6004000
  //   10000004 2008 1 9*0 e0000000 50002002 8002000 6004000 1800000 600000 181800 40000 8*0 e0000000
  //   50002002 8002000 6004000 1800000 600000 181800 40000 8*0 e0000000 50002002 8002000 6004000 1800000
  //   600000 181800 40000 8*0 e0000000 50002002 8002000 6004000 1800000 600000 181800 40000 8*0 e0000000
  //   50002002 8002000 6004000 1800000 600000 181800 40000 8*0 e0000000 50002002 8002000 6004000 1800000
  //   600000 181800 40000 8*0 e0000000 50002002 8002000 6004000 1800000 600000 181800 40000 8*0 e0000000
  //   50002002 8002000 6004000 1800000 600000 181800 40000 8*0 e0000000 50002002 8002000 6004000 1800000
  //   600000 181800 40000 8*0 e0000000 50002002 8002000 6004000 1800000 600000 181800 40000 8*0 e0000000
  //   50002002 8002000 6004000 1800000 600000 181800 40000
endmodule

module PCU_v2 (
);

  wire Clock_Main_out, instruction_splitter_1_flag_bit, not_1_out;
  wire [3:0] Step_Counter_q;
  wire [4:0] instruction_splitter_1_address_a, instruction_splitter_1_address_b,
       instruction_splitter_1_opcode, MAR_A_q, MAR_B_q, MAR_Z_q, ProgramCounter_q;
  wire [4:4] Current_Opcode_q;
  wire [7:4] Current_Opcode_q_2;
  wire [15:0] alu_16_bits_1_over_flow, alu_16_bits_1_reg_out, controlled_buffer_1_out,
       controlled_buffer_2_out, controlled_buffer_5_out, controlled_buffer_6_out, controlled_buffer_7_out,
       Instruction_Ram_dout, MBR_A_q, MBR_B_q, MBR_Z_q, OverFlow_Register_q, Ram_A_dout, Ram_B_dout,
       Reg_A0_q, Reg_B0_q, Reg_Out_q;
  wire [31:0] rom_1_data;

  Register #(.width(5)) Current_Opcode (
    .D(instruction_splitter_1_opcode), .en(rom_1_data[14]), .clk(Clock_Main_out),
    .Q({Current_Opcode_q[4], Current_Opcode_q_2}));  // open: clr
  // Probe on Reg_B0_q
  // Probe on alu_16_bits_1_over_flow
  Register #(.width(16)) Reg_B0 (
    .D(controlled_buffer_7_out), .en(rom_1_data[19]), .clk(Clock_Main_out), .Q(Reg_B0_q));  // open: clr
  Register #(.width(16)) Reg_B2 (.D(controlled_buffer_7_out), .en(rom_1_data[6]));  // open: clk, Q, clr
  Clock Clock_Main (.out(Clock_Main_out));
  // Probe on Reg_A0_q
  Register #(.width(16)) OverFlow_Register (
    .D(alu_16_bits_1_over_flow), .en(rom_1_data[18]), .clk(Clock_Main_out), .Q(OverFlow_Register_q));  // open: clr
  Register #(.width(16)) Reg_B1 (.D(controlled_buffer_7_out), .en(rom_1_data[7]));  // open: clk, Q, clr
  Register #(.width(16)) Reg_B3 (.D(controlled_buffer_7_out), .en(rom_1_data[5]));  // open: clk, Q, clr
  Counter #(.max('h1f), .width(5)) ProgramCounter (
    .up(1'b1), .count(rom_1_data[31]), .clk(Clock_Main_out), .Q(ProgramCounter_q));  // open: clr, load, D, carry
  // Probe on alu_16_bits_1_reg_out
  ALU_16_bits alu_16_bits_1 (
    .Opcode({Current_Opcode_q[4], Current_Opcode_q_2}), .Flag(instruction_splitter_1_flag_bit),
    .Reg_A(Reg_A0_q), .Reg_B(Reg_B0_q), .Over_Flow(alu_16_bits_1_over_flow), .Reg_Out(alu_16_bits_1_reg_out));
  Register #(.width(16)) Reg_A0 (
    .D(controlled_buffer_6_out), .en(rom_1_data[20]), .clk(Clock_Main_out), .Q(Reg_A0_q));  // open: clr
  Register #(.width(16)) Reg_A2 (.D(controlled_buffer_6_out), .en(rom_1_data[9]));  // open: clk, Q, clr
  Instruction_splitter instruction_splitter_1 (
    .Instruction_Input(controlled_buffer_5_out), .WE(rom_1_data[27]), .Clock(Clock_Main_out),
    .Address_B(instruction_splitter_1_address_b), .Address_A(instruction_splitter_1_address_a),
    .OPCODE(instruction_splitter_1_opcode), .FLAG_BIT(instruction_splitter_1_flag_bit));
  assign controlled_buffer_1_out = instruction_splitter_1_flag_bit ? OverFlow_Register_q : 16'bz;  // Controlled_Buffer controlled_buffer_1
  // Probe on Reg_Out_q
  Register #(.width(16)) Reg_A1 (.D(controlled_buffer_6_out), .en(rom_1_data[10]));  // open: clk, Q, clr
  Register #(.width(16)) Reg_A3 (.D(controlled_buffer_6_out), .en(rom_1_data[8]));  // open: clk, Q, clr
  Register #(.width(16)) Reg_Out (
    .D(alu_16_bits_1_reg_out), .en(rom_1_data[18]), .clk(Clock_Main_out), .Q(Reg_Out_q));  // open: clr
  Register #(.width(5)) MAR_Z (
    .D(ProgramCounter_q), .en(rom_1_data[30]), .clk(Clock_Main_out), .Q(MAR_Z_q));  // open: clr
  not not_1 (not_1_out, instruction_splitter_1_flag_bit);
  Register #(.width(5)) MAR_A (
    .D(instruction_splitter_1_address_a), .en(rom_1_data[26]), .clk(Clock_Main_out), .Q(MAR_A_q));  // open: clr
  assign controlled_buffer_2_out = rom_1_data[1] ? Instruction_Ram_dout : 16'bz;  // Controlled_Buffer controlled_buffer_2
  assign controlled_buffer_2_out = rom_1_data[2] ? controlled_buffer_1_out : 16'bz;  // Controlled_Buffer controlled_buffer_3
  assign controlled_buffer_1_out = not_1_out ? Reg_Out_q : 16'bz;  // Controlled_Buffer controlled_buffer_4
  Register #(.width(16)) MBR_Z (
    .D(controlled_buffer_2_out), .en(rom_1_data[28]), .clk(Clock_Main_out), .Q(MBR_Z_q));  // open: clr
  Register #(.width(5)) MAR_B (
    .D(instruction_splitter_1_address_b), .en(rom_1_data[25]), .clk(Clock_Main_out), .Q(MAR_B_q));  // open: clr
  assign controlled_buffer_5_out = rom_1_data[13] ? MBR_Z_q : 16'bz;  // Controlled_Buffer controlled_buffer_5
  Register #(.width(16)) MBR_A (.D(Ram_A_dout), .en(rom_1_data[22]), .clk(Clock_Main_out), .Q(MBR_A_q));  // open: clr
  Register #(.width(16)) MBR_B (.D(Ram_B_dout), .en(rom_1_data[21]), .clk(Clock_Main_out), .Q(MBR_B_q));  // open: clr
  assign controlled_buffer_6_out = rom_1_data[12] ? MBR_A_q : 16'bz;  // Controlled_Buffer controlled_buffer_6
  assign controlled_buffer_7_out = rom_1_data[11] ? MBR_B_q : 16'bz;  // Controlled_Buffer controlled_buffer_7
  RAM #(.addrWidth(5), .dataWidth(16), .\type ("nonvolatile")) Instruction_Ram (
    .addr(MAR_Z_q), .we(rom_1_data[17]), .oe(rom_1_data[29]), .clk(Clock_Main_out),
    .din(controlled_buffer_5_out), .dout(Instruction_Ram_dout));
  RAM #(.addrWidth(5), .dataWidth(16), .\type ("nonvolatile")) Ram_A (
    .addr(MAR_A_q), .we(rom_1_data[16]), .oe(rom_1_data[24]), .clk(Clock_Main_out),
    .din(controlled_buffer_6_out), .dout(Ram_A_dout));
  // Probe on Instruction_Ram_dout
  RAM #(.addrWidth(5), .dataWidth(16), .\type ("nonvolatile")) Ram_B (
    .addr(MAR_B_q), .we(rom_1_data[15]), .oe(rom_1_data[23]), .clk(Clock_Main_out),
    .din(controlled_buffer_7_out), .dout(Ram_B_dout));
  RAM #(.addrWidth(5), .dataWidth(16)) System_Ram (
    .addr(MAR_A_q), .we(rom_1_data[3]), .oe(rom_1_data[4]), .clk(Clock_Main_out),
    .din(controlled_buffer_5_out));  // open: dout
  Counter #(.max('h7), .width(4)) Step_Counter (
    .clr(rom_1_data[0]), .up(1'b1), .count(1'b1), .clk(Clock_Main_out), .Q(Step_Counter_q));  // open: load, D, carry
  ROM #(.dataWidth(32)) rom_1 (.addr({Current_Opcode_q_2, Step_Counter_q}), .data(rom_1_data));
  // Probe on rom_1_data

  // Notes on the sheet:
  //   MAR_Z_WE
  //   Instruction_Ram_OE
  //   MBR_Z_WE
  //   MAR_A_WE
  //   MAR_B_WE
  //   RAM_A_OE
  //   Ram_B_OE
  //   MBR_A_WE
  //   MBR_B_WE
  //   Reg_A0_WE
  //   Reg_B0_WE
  //   Reg_Out_WE
  //   Ram_A_WE
  //   Ram_B_WE
  //   OPCODE_WE
  //   MBR_Z_OE
  //   MBR_A_OE
  //   MBR_B_OE
  //   Reg_A1_WE
  //   Reg_A2_WE
  //   Reg_A3_WE
  //   Reg_B1_WE
  //   Reg_B2_WE
  //   Reg_B3_WE
  //   System_Ram_OE
  //   System_Ram_WE
  //   RegOut_OE
  //   Instrction_Ram_to_MBR_CB
  //   Clock_Reset
  //   Program_Counter_Increament_By_One
  //   Instruction_Splitter_WE
  //   Instrction_Ram_WE
  //   Opcode
  //   Step Counter
  //   contents of rom_1 (hex, n*v repeats v):
  //   e0000000 50002002 8002000 6004000 1800000 600000 181800 40000 8*0 e0000000 50002002 8002000 6004000
  //   1800000 600000 181800 40000 8*0 e0000000 50002002 8002000 6004000 1800000 600000 181800 40000 8*0
  //   e0000000 50002002 8002000 6004000 1800000 600000 181800 40000 8*0 e0000000 50002002 8002000 6004000
  //   10000004 2008 1 9*0 e0000000 50002002 8002000 6004000 1800000 600000 181800 40000 8*0 e0000000
  //   50002002 8002000 6004000 1800000 600000 181800 40000 8*0 e0000000 50002002 8002000 6004000 1800000
  //   600000 181800 40000 8*0 e0000000 50002002 8002000 6004000 1800000 600000 181800 40000 8*0 e0000000
  //   50002002 8002000 6004000 1800000 600000 181800 40000 8*0 e0000000 50002002 8002000 6004000 1800000
  //   600000 181800 40000 8*0 e0000000 50002002 8002000 6004000 1800000 600000 181800 40000 8*0 e0000000
  //   50002002 8002000 6004000 1800000 600000 181800 40000 8*0 e0000000 50002002 8002000 6004000 1800000
  //   600000 181800 40000 8*0 e0000000 50002002 8002000 6004000 1800000 600000 181800 40000 8*0 e0000000
  //   50002002 8002000 6004000 1800000 600000 181800 40000
endmodule

module PCU_BlockLoad (
);

  wire Clock_Main_out, instruction_splitter_1_flag_bit, not_1_out, undriven, undriven_2, undriven_3,
       undriven_4;
  wire [3:0] Step_Counter_q;
  wire [4:0] Counter_A_q, Counter_B_q, instruction_splitter_1_address_a, instruction_splitter_1_address_b,
       instruction_splitter_1_opcode, MAR_A_q, MAR_B_q, MAR_Z_q, ProgramCounter_q;
  wire [4:4] Current_Opcode_q;
  wire [7:4] Current_Opcode_q_2;
  wire [15:0] alu_16_bits_1_over_flow, alu_16_bits_1_reg_out, controlled_buffer_1_out,
       controlled_buffer_2_out, controlled_buffer_5_out, controlled_buffer_6_out, controlled_buffer_7_out,
       Instruction_Ram_dout, matmult_2x2_1_regout_0, matmult_2x2_1_regout_1, matmult_2x2_1_regout_2,
       matmult_2x2_1_regout_3, MBR_A_q, MBR_B_q, MBR_Z_q, OverFlow_Register_q, Ram_A_dout, Ram_B_dout,
       Reg_A0_q, Reg_A1_q, Reg_A2_q, Reg_A3_q, Reg_B0_q, Reg_B1_q, Reg_B2_q, Reg_B3_q;
  wire [38:0] rom_1_data;

  Register #(.width(5)) Current_Opcode (
    .D(instruction_splitter_1_opcode), .en(rom_1_data[21]), .clk(Clock_Main_out),
    .Q({Current_Opcode_q[4], Current_Opcode_q_2}));  // open: clr
  Register #(.width(16)) Reg_B0 (
    .D(controlled_buffer_7_out), .en(rom_1_data[26]), .clk(Clock_Main_out), .Q(Reg_B0_q));  // open: clr
  Clock Clock_Main (.out(Clock_Main_out));
  // Probe on Reg_B0_q
  // Probe on alu_16_bits_1_over_flow
  Register #(.width(16)) Reg_B2 (
    .D(controlled_buffer_7_out), .en(rom_1_data[13]), .clk(Clock_Main_out), .Q(Reg_B2_q));  // open: clr
  Counter #(.max('h1f), .width(5)) ProgramCounter (
    .up(1'b1), .count(rom_1_data[38]), .clk(Clock_Main_out), .Q(ProgramCounter_q));  // open: clr, load, D, carry
  // Probe on Reg_A0_q
  Register #(.width(16)) Reg_B1 (
    .D(controlled_buffer_7_out), .en(rom_1_data[14]), .clk(Clock_Main_out), .Q(Reg_B1_q));  // open: clr
  Register #(.width(16)) Reg_B3 (
    .D(controlled_buffer_7_out), .en(rom_1_data[12]), .clk(Clock_Main_out), .Q(Reg_B3_q));  // open: clr
  ALU_16_bits alu_16_bits_1 (
    .Opcode({Current_Opcode_q[4], Current_Opcode_q_2}), .Flag(instruction_splitter_1_flag_bit),
    .Reg_A(Reg_A0_q), .Reg_B(Reg_B0_q), .Over_Flow(alu_16_bits_1_over_flow), .Reg_Out(alu_16_bits_1_reg_out));
  Register #(.width(16)) OverFlow_Register (
    .D(alu_16_bits_1_over_flow), .en(rom_1_data[25]), .clk(Clock_Main_out), .Q(OverFlow_Register_q));  // open: clr
  Matmult_2x2 matmult_2x2_1 (
    .Reg_A0(Reg_A0_q), .Reg_A1(Reg_A1_q), .Reg_A2(Reg_A2_q), .Reg_A3(Reg_A3_q), .Reg_B0(Reg_B0_q),
    .Reg_B1(Reg_B1_q), .Reg_B2(Reg_B2_q), .Reg_B3(Reg_B3_q), .RegOut_0(matmult_2x2_1_regout_0),
    .RegOut_1(matmult_2x2_1_regout_1), .RegOut_2(matmult_2x2_1_regout_2), .RegOut_3(matmult_2x2_1_regout_3));
  // Probe on alu_16_bits_1_reg_out
  Register #(.width(16)) RegOut_3 (.D(matmult_2x2_1_regout_3), .en(undriven));  // open: clk, Q, clr
  Register #(.width(16)) RegOut_2 (.D(matmult_2x2_1_regout_2), .en(undriven_2));  // open: clk, Q, clr
  Register #(.width(16)) Reg_A0 (
    .D(controlled_buffer_6_out), .en(rom_1_data[27]), .clk(Clock_Main_out), .Q(Reg_A0_q));  // open: clr
  Register #(.width(16)) Reg_A2 (
    .D(controlled_buffer_6_out), .en(rom_1_data[16]), .clk(Clock_Main_out), .Q(Reg_A2_q));  // open: clr
  assign controlled_buffer_1_out = instruction_splitter_1_flag_bit ? OverFlow_Register_q : 16'bz;  // Controlled_Buffer controlled_buffer_1
  Register #(.width(16)) RegOut_1 (.D(matmult_2x2_1_regout_1), .en(undriven_3));  // open: clk, Q, clr
  Instruction_splitter instruction_splitter_1 (
    .Instruction_Input(controlled_buffer_5_out), .WE(rom_1_data[34]), .Clock(Clock_Main_out),
    .Address_B(instruction_splitter_1_address_b), .Address_A(instruction_splitter_1_address_a),
    .OPCODE(instruction_splitter_1_opcode), .FLAG_BIT(instruction_splitter_1_flag_bit));
  Register #(.width(16)) Reg_A1 (
    .D(controlled_buffer_6_out), .en(rom_1_data[17]), .clk(Clock_Main_out), .Q(Reg_A1_q));  // open: clr
  Register #(.width(16)) Reg_A3 (
    .D(controlled_buffer_6_out), .en(rom_1_data[15]), .clk(Clock_Main_out), .Q(Reg_A3_q));  // open: clr
  Register #(.width(16)) Reg_Out (
    .D(alu_16_bits_1_reg_out), .en(rom_1_data[25]), .clk(Clock_Main_out), .Q(Reg_A0_q));  // open: clr
  // Probe on Reg_A0_q
  Register #(.width(16)) RegOut_0 (.D(matmult_2x2_1_regout_0), .en(undriven_4));  // open: clk, Q, clr
  Register #(.width(5)) MAR_Z (
    .D(ProgramCounter_q), .en(rom_1_data[37]), .clk(Clock_Main_out), .Q(MAR_Z_q));  // open: clr
  assign controlled_buffer_2_out = rom_1_data[9] ? controlled_buffer_1_out : 16'bz;  // Controlled_Buffer controlled_buffer_2
  assign controlled_buffer_1_out = not_1_out ? Reg_A0_q : 16'bz;  // Controlled_Buffer controlled_buffer_3
  not not_1 (not_1_out, instruction_splitter_1_flag_bit);
  Register #(.width(5)) MAR_A (
    .D(instruction_splitter_1_address_a), .en(rom_1_data[33]), .clk(Clock_Main_out), .Q(MAR_A_q));  // open: clr
  assign controlled_buffer_2_out = rom_1_data[8] ? Instruction_Ram_dout : 16'bz;  // Controlled_Buffer controlled_buffer_4
  Register #(.width(16)) MBR_Z (
    .D(controlled_buffer_2_out), .en(rom_1_data[35]), .clk(Clock_Main_out), .Q(MBR_Z_q));  // open: clr
  Register #(.width(5)) MAR_B (
    .D(instruction_splitter_1_address_b), .en(rom_1_data[32]), .clk(Clock_Main_out), .Q(MAR_B_q));  // open: clr
  assign controlled_buffer_5_out = rom_1_data[20] ? MBR_Z_q : 16'bz;  // Controlled_Buffer controlled_buffer_5
  Register #(.width(16)) MBR_A (.D(Ram_A_dout), .en(rom_1_data[29]), .clk(Clock_Main_out), .Q(MBR_A_q));  // open: clr
  Register #(.width(16)) MBR_B (.D(Ram_B_dout), .en(rom_1_data[28]), .clk(Clock_Main_out), .Q(MBR_B_q));  // open: clr
  assign controlled_buffer_6_out = rom_1_data[19] ? MBR_A_q : 16'bz;  // Controlled_Buffer controlled_buffer_6
  assign controlled_buffer_7_out = rom_1_data[18] ? MBR_B_q : 16'bz;  // Controlled_Buffer controlled_buffer_7
  Counter #(.max('h1f), .width(5)) Counter_A (
    .load(rom_1_data[6]), .D(MAR_A_q), .count(rom_1_data[4]), .Q(Counter_A_q), .clk(Clock_Main_out));  // open: carry, up, clr
  RAM #(.addrWidth(5), .dataWidth(16), .\type ("nonvolatile")) Instruction_Ram (
    .addr(MAR_Z_q), .we(rom_1_data[24]), .oe(rom_1_data[36]), .clk(Clock_Main_out),
    .din(controlled_buffer_5_out), .dout(Instruction_Ram_dout));
  RAM #(.addrWidth(5), .dataWidth(16), .\type ("nonvolatile")) Ram_A (
    .addr(Counter_A_q), .we(rom_1_data[23]), .oe(rom_1_data[31]), .clk(Clock_Main_out), .dout(Ram_A_dout));  // open: din
  // Probe on Instruction_Ram_dout
  Counter #(.max('h1f), .width(5)) Counter_B (
    .load(rom_1_data[5]), .D(MAR_B_q), .count(rom_1_data[3]), .Q(Counter_B_q), .clk(Clock_Main_out));  // open: carry, up, clr
  RAM #(.addrWidth(5), .dataWidth(16), .\type ("nonvolatile")) Ram_B (
    .addr(Counter_B_q), .we(rom_1_data[22]), .oe(rom_1_data[30]), .clk(Clock_Main_out), .dout(Ram_B_dout));  // open: din
  RAM #(.addrWidth(5), .dataWidth(16)) System_Ram (
    .addr(MAR_A_q), .we(rom_1_data[10]), .oe(rom_1_data[11]), .clk(Clock_Main_out),
    .din(controlled_buffer_5_out));  // open: dout
  Counter #(.max('hf), .width(4)) Step_Counter (
    .clr(rom_1_data[7]), .up(1'b1), .count(1'b1), .clk(Clock_Main_out), .Q(Step_Counter_q));  // open: load, D, carry
  ROM #(.dataWidth(39)) rom_1 (.addr({Current_Opcode_q_2, Step_Counter_q}), .data(rom_1_data));
  // Probe on rom_1_data

  // Notes on the sheet:
  //   Bank B 
  //   Bank A
  //   MAR_Z_WE
  //   Instruction_Ram_OE
  //   MBR_Z_WE
  //   Instruction_Splitter_WE
  //   MAR_A_WE
  //   MAR_B_WE
  //   RAM_A_OE
  //   Ram_B_OE
  //   MBR_A_WE
  //   MBR_B_WE
  //   Reg_A0_WE
  //   Reg_B0_WE
  //   Reg_Out_WE
  //   Instrction_Ram_WE
  //   Ram_A_WE
  //   Ram_B_WE
  //   OPCODE_WE
  //   MBR_Z_OE
  //   MBR_A_OE
  //   MBR_B_OE
  //   Reg_A1_WE
  //   Reg_A2_WE
  //   Reg_A3_WE
  //   Reg_B1_WE
  //   Reg_B2_WE
  //   Reg_B3_WE
  //   System_Ram_OE
  //   System_Ram_WE
  //   RegOut_OE
  //   Clock_Reset
  //   Counter _A_WE
  //   Counter_B_WE
  //   Program_Counter_Increament_By_One
  //   Instruction_Ram_to_MBR_CB
  //   Counter_A_Increament_By_One
  //   Counter_B_Increament_By_One
  //   Opcode
  //   Step Counter
  //   contents of rom_1 (hex, n*v repeats v):
  //   7000000000 2800100100 400100000 300200000 60 c0000000 30000000 c0c0000 2000000 80 6*0 7000000000
  //   2800100100 400100000 300200000 60 c0000000 30000000 c0c0000 2000000 80 6*0 7000000000 2800100100
  //   400100000 300200000 60 c0000000 30000000 c0c0000 2000000 80 6*0 7000000000 2800100100 400100000
  //   300200000 60 c0000000 30000000 c0c0000 2000000 80 6*0 7000000000 2800100100 400100000 300200000
  //   800000200 100400 80 9*0 7000000000 2800100100 400100000 300200000 60 c0000000 30000000 c0c0000
  //   2000000 80 6*0 7000000000 2800100100 400100000 300200000 60 c0000000 30000000 c0c0000 2000000 80 6*0
  //   7000000000 2800100100 400100000 300200000 60 c0000018 f0000018 fc0c0018 f00e4000 300d2000 c9000 80
  //   4*0 7000000000 2800100100 400100000 300200000 60 c0000000 30000000 c0c0000 2000000 80 6*0 7000000000
  //   2800100100 400100000 300200000 60 c0000000 30000000 c0c0000 2000000 80 6*0 7000000000 2800100100
  //   400100000 300200000 60 c0000000 30000000 c0c0000 2000000 80 6*0 7000000000 2800100100 400100000
  //   300200000 60 c0000000 30000000 c0c0000 2000000 80 6*0 7000000000 2800100100 400100000 300200000 60
  //   c0000000 30000000 c0c0000 2000000 80 6*0 7000000000 2800100100 400100000 300200000 60 c0000000
  //   30000000 c0c0000 2000000 80 6*0 7000000000 2800100100 400100000 300200000 60 c0000000 30000000
  //   c0c0000 2000000 80 6*0 7000000000 2800100100 400100000 300200000 60 c0000000 30000000 c0c0000
  //   2000000 80
endmodule

module Manual_Blockload (
  input  in_1,
  input  in_2,
  input  in_3,
  input  in_4,
  input  in_5,
  input  in_6,
  input  in_7,
  input  in_8,
  input  in_9,
  input  in_10,
  input  in_11,
  input  in_12,
  input  in_13,
  input  in_14,
  input  in_15,
  input  in_16,
  input  in_17,
  input  in_18,
  input  in_19,
  input  in_20,
  input  in_21,
  input  in_22,
  input  Program_Counter_Increament_By_One,
  input  MAR_Z_WE,
  input  Instruction_Ram_OE,
  input  MBR_Z_WE,
  input  Instruction_Splitter_WE,
  input  MAR_A_WE,
  input  MAR_B_WE,
  input  RAM_A_OE,
  input  Ram_B_OE,
  input  MBR_A_WE,
  input  MBR_B_WE,
  input  Reg_A0_WE,
  input  Reg_B0_WE,
  input  Reg_Out_WE,
  input  Instrction_Ram_WE,
  input  Ram_A_WE,
  input  Ram_B_WE,
  input  OPCODE_WE,
  input  MBR_Z_OE,
  input  MBR_A_OE,
  input  MBR_B_OE,
  input  Reset_Clock,
  input  System_Ram_WE,
  input  System_ram_oe,
  input  reg_out_oe,
  input  Instrction_Ram_CB,
  input  in_49,
  input  in_50,
  input  in_51,
  input  in_52,
  input  in_53,
  input  in_54,
  input  in_55,
  input  in_56,
  input  in_57,
  input  in_58
);

  wire and_1_out, and_2_out, and_3_out, bus_terminus_1_ram_a, bus_terminus_1_ram_b, bus_terminus_2_ram_a,
       bus_terminus_2_ram_b, Clock_Main_out, controlled_buffer_12_out, instruction_splitter_1_flag_bit,
       not_1_out, or_1_out, or_2_out, or_3_out, or_4_out;
  wire [4:0] counter_1_q, counter_2_q, Current_Opcode_q, instruction_splitter_1_address_a,
       instruction_splitter_1_address_b, instruction_splitter_1_opcode, MAR_A_q, MAR_B_q, MAR_Z_q,
       ProgramCounter_q;
  wire [15:0] alu_16_bits_1_over_flow, controlled_buffer_1_out, controlled_buffer_3_out,
       controlled_buffer_4_out, controlled_buffer_5_out, controlled_buffer_6_out, controlled_buffer_7_out,
       MBR_A_q, MBR_B_q, MBR_Z_q, ram_1_dout, Ram_A_dout, Ram_B_dout, Reg_A0_q, Reg_B0_q, Reg_Out_q,
       register_1_q, register_2_q, Terminal_A_q, Terminal_B_q;

  and and_1 (and_1_out, Current_Opcode_q[0], Current_Opcode_q[1], Current_Opcode_q[2], Current_Opcode_q[3]);
  not not_1 (not_1_out, instruction_splitter_1_flag_bit);
  and and_2 (and_2_out, and_1_out, instruction_splitter_1_flag_bit);
  and and_3 (and_3_out, and_1_out, not_1_out);
  Register #(.width(5)) Current_Opcode (
    .D(instruction_splitter_1_opcode), .en(OPCODE_WE), .clk(Clock_Main_out), .Q(Current_Opcode_q));  // open: clr
  // Probe on Reg_B0_q
  Register #(.width(16)) Reg_B0 (
    .D(controlled_buffer_5_out), .en(in_13), .clk(Clock_Main_out), .Q(Reg_B0_q));  // open: clr
  Register #(.width(16)) Reg_B2 (.D(controlled_buffer_5_out), .en(in_15), .clk(Clock_Main_out));  // open: Q, clr
  Clock Clock_Main (.out(Clock_Main_out));
  // Probe on Reg_A0_q
  Register #(.width(16)) Reg_B1 (.D(controlled_buffer_5_out), .en(in_14), .clk(Clock_Main_out));  // open: Q, clr
  Register #(.width(16)) Reg_B3 (.D(controlled_buffer_5_out), .en(in_16), .clk(Clock_Main_out));  // open: Q, clr
  Counter #(.max('h1f), .width(5)) ProgramCounter (
    .clr(Reset_Clock), .up(1'b1), .count(Program_Counter_Increament_By_One), .clk(Clock_Main_out),
    .Q(ProgramCounter_q));  // open: load, D, carry
  ALU_16_bits alu_16_bits_1 (
    .Opcode(Current_Opcode_q), .Flag(instruction_splitter_1_flag_bit), .Reg_A(Reg_A0_q), .Reg_B(Reg_B0_q),
    .Over_Flow(alu_16_bits_1_over_flow));  // open: Reg_Out
  Register #(.width(16)) Reg_A0 (
    .D(controlled_buffer_4_out), .en(in_7), .clk(Clock_Main_out), .Q(Reg_A0_q));  // open: clr
  Register #(.width(16)) Reg_A2 (.D(controlled_buffer_4_out), .en(in_11), .clk(Clock_Main_out));  // open: Q, clr
  Instruction_splitter instruction_splitter_1 (
    .Instruction_Input(controlled_buffer_3_out), .WE(Instruction_Splitter_WE), .Clock(Clock_Main_out),
    .Address_B(instruction_splitter_1_address_b), .Address_A(instruction_splitter_1_address_a),
    .OPCODE(instruction_splitter_1_opcode), .FLAG_BIT(instruction_splitter_1_flag_bit));
  // Probe on Reg_Out_q
  Register #(.width(16)) Reg_A1 (.D(controlled_buffer_4_out), .en(in_6), .clk(Clock_Main_out));  // open: Q, clr
  Register #(.width(16)) Reg_A3 (.D(controlled_buffer_4_out), .en(in_12), .clk(Clock_Main_out));  // open: Q, clr
  Register #(.width(16)) Reg_Out (
    .D(alu_16_bits_1_over_flow), .en(Reg_Out_WE), .clk(Clock_Main_out), .Q(Reg_Out_q));  // open: clr
  Register #(.width(5)) MAR_Z (.D(ProgramCounter_q), .en(MAR_Z_WE), .clk(Clock_Main_out), .Q(MAR_Z_q));  // open: clr
  Register #(.width(5)) MAR_A (
    .D(instruction_splitter_1_address_b), .en(MAR_A_WE), .clk(Clock_Main_out), .Q(MAR_A_q));  // open: clr
  assign controlled_buffer_1_out = reg_out_oe ? Reg_Out_q : 16'bz;  // Controlled_Buffer controlled_buffer_1
  Register #(.width(16)) MBR_Z (
    .D(controlled_buffer_1_out), .en(MBR_Z_WE), .clk(Clock_Main_out), .Q(MBR_Z_q));  // open: clr
  Register #(.width(5)) MAR_B (
    .D(instruction_splitter_1_address_a), .en(MAR_B_WE), .clk(Clock_Main_out), .Q(MAR_B_q));  // open: clr
  // Probe on controlled_buffer_1_out
  assign controlled_buffer_1_out = Instrction_Ram_CB ? ram_1_dout : 16'bz;  // Controlled_Buffer controlled_buffer_2
  assign controlled_buffer_3_out = MBR_Z_OE ? MBR_Z_q : 16'bz;  // Controlled_Buffer controlled_buffer_3
  Register #(.width(16)) MBR_A (
    .D(controlled_buffer_6_out), .en(or_1_out), .clk(Clock_Main_out), .Q(MBR_A_q));  // open: clr
  or or_1 (or_1_out, MBR_A_WE, bus_terminus_2_ram_a);
  Register #(.width(16)) MBR_B (
    .D(controlled_buffer_7_out), .en(or_2_out), .clk(Clock_Main_out), .Q(MBR_B_q));  // open: clr
  or or_2 (or_2_out, MBR_B_WE, bus_terminus_2_ram_b);
  assign controlled_buffer_4_out = MBR_A_OE ? MBR_A_q : 16'bz;  // Controlled_Buffer controlled_buffer_4
  assign controlled_buffer_5_out = MBR_B_OE ? MBR_B_q : 16'bz;  // Controlled_Buffer controlled_buffer_5
  Counter #(.max('h1f), .width(5)) counter_1 (
    .load(in_2), .D(MAR_A_q), .count(in_1), .Q(counter_1_q), .clk(Clock_Main_out));  // open: carry, up, clr
  RAM #(.addrWidth(5), .dataWidth(16), .\type ("nonvolatile")) ram_1 (
    .addr(MAR_Z_q), .we(Instrction_Ram_WE), .oe(Instruction_Ram_OE), .clk(Clock_Main_out),
    .din(controlled_buffer_3_out), .dout(ram_1_dout));
  or or_3 (or_3_out, Ram_A_WE, bus_terminus_2_ram_a);
  RAM #(.addrWidth(5), .dataWidth(16), .\type ("nonvolatile")) Ram_A (
    .addr(counter_1_q), .we(or_3_out), .oe(RAM_A_OE), .clk(Clock_Main_out), .din(controlled_buffer_4_out),
    .dout(Ram_A_dout));
  Register #(.width(16)) Terminal_A (
    .D(controlled_buffer_4_out), .en(in_17), .clk(Clock_Main_out), .Q(Terminal_A_q));  // open: clr
  Register #(.width(16)) Terminal_B (
    .D(controlled_buffer_5_out), .en(in_19), .clk(Clock_Main_out), .Q(Terminal_B_q));  // open: clr
  assign controlled_buffer_6_out = in_10 ? Ram_A_dout : 16'bz;  // Controlled_Buffer controlled_buffer_6
  assign controlled_buffer_7_out = bus_terminus_1_ram_b ? Terminal_A_q : 16'bz;  // Controlled_Buffer controlled_buffer_7
  Bus_Terminus bus_terminus_1 (
    .OE(in_21), .Input_01(in_20), .Input_02(in_22), .Ram_A(bus_terminus_1_ram_a), .Ram_B(bus_terminus_1_ram_b));  // open: System_Ram
  Counter #(.max('h1f), .width(5)) counter_2 (
    .load(in_4), .D(MAR_B_q), .count(in_3), .Q(counter_2_q), .up(Clock_Main_out), .clk(Clock_Main_out));  // open: carry, clr
  assign controlled_buffer_6_out = bus_terminus_1_ram_a ? Terminal_B_q : 16'bz;  // Controlled_Buffer controlled_buffer_8
  or or_4 (or_4_out, Ram_B_WE, bus_terminus_2_ram_b);
  RAM #(.addrWidth(5), .dataWidth(16), .\type ("nonvolatile")) Ram_B (
    .addr(counter_2_q), .we(or_4_out), .oe(Ram_B_OE), .clk(Clock_Main_out), .din(controlled_buffer_5_out),
    .dout(Ram_B_dout));
  RAM #(.addrWidth(5), .dataWidth(16)) ram_2 (
    .addr(MAR_A_q), .we(System_Ram_WE), .oe(System_ram_oe), .clk(Clock_Main_out),
    .din(controlled_buffer_3_out), .dout(controlled_buffer_1_out));
  assign controlled_buffer_7_out = in_9 ? Ram_B_dout : 16'bz;  // Controlled_Buffer controlled_buffer_9
  Register #(.width(16)) register_1 (
    .D(controlled_buffer_3_out), .en(in_18), .clk(Clock_Main_out), .Q(register_1_q));  // open: clr
  Register #(.width(16)) register_2 (
    .D(controlled_buffer_3_out), .en(in_18), .clk(Clock_Main_out), .Q(register_2_q));  // open: clr
  Bus_Terminus bus_terminus_2 (
    .OE(1'b1), .Input_01(and_2_out), .Input_02(and_3_out), .Ram_A(bus_terminus_2_ram_a),
    .Ram_B(bus_terminus_2_ram_b));  // open: System_Ram
  assign controlled_buffer_6_out = bus_terminus_2_ram_a ? register_2_q : 16'bz;  // Controlled_Buffer controlled_buffer_10
  assign controlled_buffer_7_out = bus_terminus_2_ram_b ? register_1_q : 16'bz;  // Controlled_Buffer controlled_buffer_11
  assign controlled_buffer_12_out = in_8 ? in_5 : 1'bz;  // Controlled_Buffer controlled_buffer_12
  LED led_1 (.in(controlled_buffer_12_out));
endmodule

module Matmult_2x2 (
  input  [15:0] Reg_A0,
  input  [15:0] Reg_A1,
  input  [15:0] Reg_A2,
  input  [15:0] Reg_A3,
  input  [15:0] Reg_B0,
  input  [15:0] Reg_B1,
  input  [15:0] Reg_B2,
  input  [15:0] Reg_B3,
  output [15:0] RegOut_0,
  output [15:0] RegOut_1,
  output [15:0] RegOut_2,
  output [15:0] RegOut_3
);

  wire [7:0] bitselector_1_out, bitselector_2_out, bitselector_3_out, bitselector_4_out, bitselector_5_out,
       bitselector_6_out, bitselector_7_out, bitselector_8_out;
  wire [15:0] multiplier_8x8_1_product, multiplier_8x8_2_product, multiplier_8x8_3_product,
       multiplier_8x8_4_product, multiplier_8x8_5_product, multiplier_8x8_6_product,
       multiplier_8x8_7_product, multiplier_8x8_8_product;

  BitSelector #(.group(8), .width(16)) bitselector_1 (.in(Reg_A0), .out(bitselector_1_out), .sel(1'b0));
  BitSelector #(.group(8), .width(16)) bitselector_2 (.in(Reg_A1), .out(bitselector_2_out), .sel(1'b0));
  BitSelector #(.group(8), .width(16)) bitselector_3 (.in(Reg_A2), .out(bitselector_3_out), .sel(1'b0));
  BitSelector #(.group(8), .width(16)) bitselector_4 (.in(Reg_A3), .out(bitselector_4_out), .sel(1'b0));
  BitSelector #(.group(8), .width(16)) bitselector_5 (.in(Reg_B0), .out(bitselector_5_out), .sel(1'b0));
  BitSelector #(.group(8), .width(16)) bitselector_6 (.in(Reg_B1), .out(bitselector_6_out), .sel(1'b0));
  BitSelector #(.group(8), .width(16)) bitselector_7 (.in(Reg_B2), .out(bitselector_7_out), .sel(1'b0));
  BitSelector #(.group(8), .width(16)) bitselector_8 (.in(Reg_B3), .out(bitselector_8_out), .sel(1'b0));
  Multiplier_8x8 multiplier_8x8_1 (.A(bitselector_1_out), .B(bitselector_5_out), .Product(multiplier_8x8_1_product));
  Multiplier_8x8 multiplier_8x8_2 (.A(bitselector_2_out), .B(bitselector_7_out), .Product(multiplier_8x8_2_product));
  Multiplier_8x8 multiplier_8x8_3 (.A(bitselector_1_out), .B(bitselector_6_out), .Product(multiplier_8x8_3_product));
  Multiplier_8x8 multiplier_8x8_4 (.A(bitselector_2_out), .B(bitselector_8_out), .Product(multiplier_8x8_4_product));
  Multiplier_8x8 multiplier_8x8_5 (.A(bitselector_3_out), .B(bitselector_5_out), .Product(multiplier_8x8_5_product));
  Multiplier_8x8 multiplier_8x8_6 (.A(bitselector_4_out), .B(bitselector_7_out), .Product(multiplier_8x8_6_product));
  Multiplier_8x8 multiplier_8x8_7 (.A(bitselector_3_out), .B(bitselector_6_out), .Product(multiplier_8x8_7_product));
  Multiplier_8x8 multiplier_8x8_8 (.A(bitselector_4_out), .B(bitselector_8_out), .Product(multiplier_8x8_8_product));
  SixteenBitAdder sixteenbitadder_1 (
    .A(multiplier_8x8_1_product), .B(multiplier_8x8_2_product), .Sum(RegOut_0));  // open: CarryIn, CarryOut
  SixteenBitAdder sixteenbitadder_2 (
    .A(multiplier_8x8_3_product), .B(multiplier_8x8_4_product), .Sum(RegOut_1));  // open: CarryIn, CarryOut
  SixteenBitAdder sixteenbitadder_3 (
    .A(multiplier_8x8_5_product), .B(multiplier_8x8_6_product), .Sum(RegOut_2));  // open: CarryIn, CarryOut
  SixteenBitAdder sixteenbitadder_4 (
    .A(multiplier_8x8_7_product), .B(multiplier_8x8_8_product), .Sum(RegOut_3));  // open: CarryIn, CarryOut
  // Probe on RegOut_0
  // Probe on RegOut_1
  // Probe on RegOut_2
  // Probe on RegOut_3

  // Notes on the sheet:
  //   A0    A1 
  //   A2
  //   B0
  //   A3
  //   B2
  //   B1
  //   B3
  //   =
  //   A0*B0  + A1*B2
  //   A2*B0 + A3*B2
  //   A0*B1+A1*B3
  //   A2*B1+ A3*B3
  //   1    2
  //   3    4
  //   1   2 
  //   3   4
  //   =
  //   7
  //   15
  //   10
  //   22
  //   10 = a
  //   11 = b
  //   12 = c
  //   13 = d
  //   14 = e
  //   15 = f
endmodule
module PCU_Matmult (
  input  in_1
);

  wire Clock_Main_out, instruction_splitter_1_flag_bit, not_1_out;
  wire [3:0] Step_Counter_q;
  wire [4:0] Counter_A_q, Counter_B_q, instruction_splitter_1_address_a, instruction_splitter_1_address_b,
       instruction_splitter_1_opcode, MAR_A_q, MAR_B_q, MAR_Z_q, ProgramCounter_q;
  wire [4:4] Current_Opcode_q;
  wire [7:4] Current_Opcode_q_2;
  wire [15:0] alu_16_bits_1_over_flow, alu_16_bits_1_reg_out, controlled_buffer_1_out,
       controlled_buffer_2_out, controlled_buffer_5_out, controlled_buffer_6_out, controlled_buffer_7_out,
       Instruction_Ram_dout, matmult_2x2_1_regout_0, matmult_2x2_1_regout_1, matmult_2x2_1_regout_2,
       matmult_2x2_1_regout_3, MBR_A_q, MBR_B_q, MBR_Z_q, OverFlow_Register_q, Ram_A_dout, Ram_B_dout,
       Reg_A0_q, Reg_A1_q, Reg_A2_q, Reg_A3_q, Reg_B0_q, Reg_B1_q, Reg_B2_q, Reg_B3_q, Reg_Out_q;
  wire [38:0] rom_1_data;

  Register #(.width(5)) Current_Opcode (
    .D(instruction_splitter_1_opcode), .en(rom_1_data[21]), .clk(Clock_Main_out),
    .Q({Current_Opcode_q[4], Current_Opcode_q_2}));  // open: clr
  Register #(.width(16)) Reg_B0 (
    .D(controlled_buffer_7_out), .en(rom_1_data[26]), .clk(Clock_Main_out), .Q(Reg_B0_q));  // open: clr
  Clock Clock_Main (.out(Clock_Main_out));
  // Probe on Reg_B0_q
  // Probe on alu_16_bits_1_over_flow
  Register #(.width(16)) Reg_B2 (
    .D(controlled_buffer_7_out), .en(rom_1_data[13]), .clk(Clock_Main_out), .Q(Reg_B2_q));  // open: clr
  Counter #(.max('h1f), .width(5)) ProgramCounter (
    .up(1'b1), .count(rom_1_data[38]), .clk(Clock_Main_out), .Q(ProgramCounter_q));  // open: clr, load, D, carry
  // Probe on Reg_A0_q
  Register #(.width(16)) Reg_B1 (
    .D(controlled_buffer_7_out), .en(rom_1_data[14]), .clk(Clock_Main_out), .Q(Reg_B1_q));  // open: clr
  Register #(.width(16)) Reg_B3 (
    .D(controlled_buffer_7_out), .en(rom_1_data[12]), .clk(Clock_Main_out), .Q(Reg_B3_q));  // open: clr
  ALU_16_bits alu_16_bits_1 (
    .Opcode({Current_Opcode_q[4], Current_Opcode_q_2}), .Flag(instruction_splitter_1_flag_bit),
    .Reg_A(Reg_A0_q), .Reg_B(Reg_B0_q), .Over_Flow(alu_16_bits_1_over_flow), .Reg_Out(alu_16_bits_1_reg_out));
  Register #(.width(16)) OverFlow_Register (
    .D(alu_16_bits_1_over_flow), .en(rom_1_data[25]), .clk(Clock_Main_out), .Q(OverFlow_Register_q));  // open: clr
  Matmult_2x2 matmult_2x2_1 (
    .Reg_A0(Reg_A0_q), .Reg_A1(Reg_A1_q), .Reg_A2(Reg_A2_q), .Reg_A3(Reg_A3_q), .Reg_B0(Reg_B0_q),
    .Reg_B1(Reg_B1_q), .Reg_B2(Reg_B2_q), .Reg_B3(Reg_B3_q), .RegOut_0(matmult_2x2_1_regout_0),
    .RegOut_1(matmult_2x2_1_regout_1), .RegOut_2(matmult_2x2_1_regout_2), .RegOut_3(matmult_2x2_1_regout_3));
  // Probe on alu_16_bits_1_reg_out
  Register #(.width(16)) RegOut_3 (.D(matmult_2x2_1_regout_3), .en(in_1), .clk(Clock_Main_out));  // open: Q, clr
  Register #(.width(16)) RegOut_2 (.D(matmult_2x2_1_regout_2), .en(in_1), .clk(Clock_Main_out));  // open: Q, clr
  Register #(.width(16)) Reg_A0 (
    .D(controlled_buffer_6_out), .en(rom_1_data[27]), .clk(Clock_Main_out), .Q(Reg_A0_q));  // open: clr
  Register #(.width(16)) Reg_A2 (
    .D(controlled_buffer_6_out), .en(rom_1_data[16]), .clk(Clock_Main_out), .Q(Reg_A2_q));  // open: clr
  assign controlled_buffer_1_out = instruction_splitter_1_flag_bit ? OverFlow_Register_q : 16'bz;  // Controlled_Buffer controlled_buffer_1
  Register #(.width(16)) RegOut_1 (.D(matmult_2x2_1_regout_1), .en(in_1), .clk(Clock_Main_out));  // open: Q, clr
  Instruction_splitter instruction_splitter_1 (
    .Instruction_Input(controlled_buffer_5_out), .WE(rom_1_data[34]), .Clock(Clock_Main_out),
    .Address_B(instruction_splitter_1_address_b), .Address_A(instruction_splitter_1_address_a),
    .OPCODE(instruction_splitter_1_opcode), .FLAG_BIT(instruction_splitter_1_flag_bit));
  Register #(.width(16)) Reg_A1 (
    .D(controlled_buffer_6_out), .en(rom_1_data[17]), .clk(Clock_Main_out), .Q(Reg_A1_q));  // open: clr
  Register #(.width(16)) Reg_A3 (
    .D(controlled_buffer_6_out), .en(rom_1_data[15]), .clk(Clock_Main_out), .Q(Reg_A3_q));  // open: clr
  Register #(.width(16)) Reg_Out (
    .D(alu_16_bits_1_reg_out), .en(rom_1_data[25]), .clk(Clock_Main_out), .Q(Reg_Out_q));  // open: clr
  // Probe on Reg_Out_q
  Register #(.width(16)) RegOut_0 (.D(matmult_2x2_1_regout_0), .en(in_1), .clk(Clock_Main_out));  // open: Q, clr
  Register #(.width(5)) MAR_Z (
    .D(ProgramCounter_q), .en(rom_1_data[37]), .clk(Clock_Main_out), .Q(MAR_Z_q));  // open: clr
  assign controlled_buffer_2_out = rom_1_data[9] ? controlled_buffer_1_out : 16'bz;  // Controlled_Buffer controlled_buffer_2
  assign controlled_buffer_1_out = not_1_out ? Reg_Out_q : 16'bz;  // Controlled_Buffer controlled_buffer_3
  not not_1 (not_1_out, instruction_splitter_1_flag_bit);
  Register #(.width(5)) MAR_A (
    .D(instruction_splitter_1_address_a), .en(rom_1_data[33]), .clk(Clock_Main_out), .Q(MAR_A_q));  // open: clr
  assign controlled_buffer_2_out = rom_1_data[8] ? Instruction_Ram_dout : 16'bz;  // Controlled_Buffer controlled_buffer_4
  Register #(.width(16)) MBR_Z (
    .D(controlled_buffer_2_out), .en(rom_1_data[35]), .clk(Clock_Main_out), .Q(MBR_Z_q));  // open: clr
  Register #(.width(5)) MAR_B (
    .D(instruction_splitter_1_address_b), .en(rom_1_data[32]), .clk(Clock_Main_out), .Q(MAR_B_q));  // open: clr
  assign controlled_buffer_5_out = rom_1_data[20] ? MBR_Z_q : 16'bz;  // Controlled_Buffer controlled_buffer_5
  Register #(.width(16)) MBR_A (.D(Ram_A_dout), .en(rom_1_data[29]), .clk(Clock_Main_out), .Q(MBR_A_q));  // open: clr
  Register #(.width(16)) MBR_B (.D(Ram_B_dout), .en(rom_1_data[28]), .clk(Clock_Main_out), .Q(MBR_B_q));  // open: clr
  assign controlled_buffer_6_out = rom_1_data[19] ? MBR_A_q : 16'bz;  // Controlled_Buffer controlled_buffer_6
  assign controlled_buffer_7_out = rom_1_data[18] ? MBR_B_q : 16'bz;  // Controlled_Buffer controlled_buffer_7
  Counter #(.max('h1f), .width(5)) Counter_A (
    .load(rom_1_data[6]), .D(MAR_A_q), .count(rom_1_data[4]), .Q(Counter_A_q), .clk(Clock_Main_out));  // open: carry, up, clr
  RAM #(.addrWidth(5), .dataWidth(16), .\type ("nonvolatile")) Instruction_Ram (
    .addr(MAR_Z_q), .we(rom_1_data[24]), .oe(rom_1_data[36]), .clk(Clock_Main_out),
    .din(controlled_buffer_5_out), .dout(Instruction_Ram_dout));
  RAM #(.addrWidth(5), .dataWidth(16), .\type ("nonvolatile")) Ram_A (
    .addr(Counter_A_q), .we(rom_1_data[23]), .oe(rom_1_data[31]), .clk(Clock_Main_out), .dout(Ram_A_dout));  // open: din
  // Probe on Instruction_Ram_dout
  Counter #(.max('h1f), .width(5)) Counter_B (
    .load(rom_1_data[5]), .D(MAR_B_q), .count(rom_1_data[3]), .Q(Counter_B_q), .clk(Clock_Main_out));  // open: carry, up, clr
  RAM #(.addrWidth(5), .dataWidth(16), .\type ("nonvolatile")) Ram_B (
    .addr(Counter_B_q), .we(rom_1_data[22]), .oe(rom_1_data[30]), .clk(Clock_Main_out), .dout(Ram_B_dout));  // open: din
  RAM #(.addrWidth(5), .dataWidth(16)) System_Ram (
    .addr(MAR_A_q), .we(rom_1_data[10]), .oe(rom_1_data[11]), .clk(Clock_Main_out),
    .din(controlled_buffer_5_out));  // open: dout
  Counter #(.max('hf), .width(4)) Step_Counter (
    .clr(rom_1_data[7]), .up(1'b1), .count(1'b1), .clk(Clock_Main_out), .Q(Step_Counter_q));  // open: load, D, carry
  ROM #(.dataWidth(39)) rom_1 (.addr({Current_Opcode_q_2, Step_Counter_q}), .data(rom_1_data));
  // Probe on rom_1_data

  // Notes on the sheet:
  //   Bank B 
  //   Bank A
  //   MAR_Z_WE
  //   Instruction_Ram_OE
  //   MBR_Z_WE
  //   Instruction_Splitter_WE
  //   MAR_A_WE
  //   MAR_B_WE
  //   RAM_A_OE
  //   Ram_B_OE
  //   MBR_A_WE
  //   MBR_B_WE
  //   Reg_A0_WE
  //   Reg_B0_WE
  //   Reg_Out_WE
  //   Instrction_Ram_WE
  //   Ram_A_WE
  //   Ram_B_WE
  //   OPCODE_WE
  //   MBR_Z_OE
  //   MBR_A_OE
  //   MBR_B_OE
  //   Reg_A1_WE
  //   Reg_A2_WE
  //   Reg_A3_WE
  //   Reg_B1_WE
  //   Reg_B2_WE
  //   Reg_B3_WE
  //   System_Ram_OE
  //   System_Ram_WE
  //   RegOut_OE
  //   Clock_Reset
  //   Counter _A_WE
  //   Counter_B_WE
  //   Program_Counter_Increament_By_One
  //   Instruction_Ram_to_MBR_CB
  //   Counter_A_Increament_By_One
  //   Counter_B_Increament_By_One
  //   Opcode
  //   Step Counter
  //   contents of rom_1 (hex, n*v repeats v):
  //   7000000000 2800100100 400100000 300200000 60 c0000000 30000000 c0c0000 2000000 80 6*0 7000000000
  //   2800100100 400100000 300200000 60 c0000000 30000000 c0c0000 2000000 80 6*0 7000000000 2800100100
  //   400100000 300200000 60 c0000000 30000000 c0c0000 2000000 80 6*0 7000000000 2800100100 400100000
  //   300200000 60 c0000000 30000000 c0c0000 2000000 80 6*0 7000000000 2800100100 400100000 300200000
  //   800000200 100400 80 9*0 7000000000 2800100100 400100000 300200000 60 c0000000 30000000 c0c0000
  //   2000000 80 6*0 7000000000 2800100100 400100000 300200000 60 c0000000 30000000 c0c0000 2000000 80 6*0
  //   7000000000 2800100100 400100000 300200000 60 c0000018 f0000018 fc0c0018 f00e4000 300d2000 c9000 80
  //   4*0 7000000000 2800100100 400100000 300200000 60 c0000000 30000000 c0c0000 2000000 80 6*0 7000000000
  //   2800100100 400100000 300200000 60 c0000000 30000000 c0c0000 2000000 80 6*0 7000000000 2800100100
  //   400100000 300200000 60 c0000000 30000000 c0c0000 2000000 80 6*0 7000000000 2800100100 400100000
  //   300200000 60 c0000000 30000000 c0c0000 2000000 80 6*0 7000000000 2800100100 400100000 300200000 60
  //   c0000000 30000000 c0c0000 2000000 80 6*0 7000000000 2800100100 400100000 300200000 60 c0000000
  //   30000000 c0c0000 2000000 80 6*0 7000000000 2800100100 400100000 300200000 60 c0000000 30000000
  //   c0c0000 2000000 80 6*0 7000000000 2800100100 400100000 300200000 60 c0000000 30000000 c0c0000
  //   2000000 80
endmodule

module PCU_MatMult_v2 (
  input  [7:0] in_1,
  input  [7:0] in_2,
  input  [4:0] in_3,
  input  [4:0] in_4,
  input  [15:0] in_5,
  input  [15:0] in_6,
  input  [15:0] Instruction_Input,
  input  WE,
  input  in_9,
  output [7:0] out_10,
  output [7:0] out_11,
  output [4:0] out_12,
  output [4:0] out_13,
  output [15:0] out_14,
  output [15:0] out_15,
  output [4:0] Address_B,
  output [4:0] Address_A,
  output [4:0] OPCODE,
  output FLAG_BIT
);

  wire and_1_out, and_2_out, Clock_Main_out, controlled_buffer_3_out, instruction_splitter_1_flag_bit,
       not_1_out, not_2_out, not_3_out;
  wire [3:0] Step_Counter_q;
  wire [4:0] controlled_buffer_1_out, Counter_A_q, Counter_B_q, Counter_C_q,
       instruction_splitter_1_address_a, instruction_splitter_1_address_b, instruction_splitter_1_opcode,
       MAR_A_q, MAR_B_q, MAR_Z_q, ProgramCounter_q;
  wire [4:4] Current_Opcode_q;
  wire [7:4] Current_Opcode_q_2;
  wire [15:0] alu_16_bits_1_over_flow, alu_16_bits_1_reg_out, controlled_buffer_2_out,
       controlled_buffer_5_out, controlled_buffer_12_out, controlled_buffer_13_out, controlled_buffer_14_out,
       Instruction_Ram_dout, matmult_2x2_1_regout_0, matmult_2x2_1_regout_1, matmult_2x2_1_regout_2,
       matmult_2x2_1_regout_3, MBR_A_q, MBR_B_q, MBR_Z_q, OverFlow_Register_q, Ram_A_dout, Ram_B_dout,
       Reg_A0_q, Reg_A1_q, Reg_A2_q, Reg_A3_q, Reg_B0_q, Reg_B1_q, Reg_B2_q, Reg_B3_q, Reg_Out_q, RegOut_0_q,
       RegOut_1_q, RegOut_2_q, RegOut_3_q, Terminal_A_q, Terminal_B_q;
  wire [31:0] Rom_A_data, Rom_B_data;

  Register #(.width(5)) Current_Opcode (
    .D(instruction_splitter_1_opcode), .en(Rom_A_data[14]), .clk(controlled_buffer_3_out),
    .Q({Current_Opcode_q[4], Current_Opcode_q_2}));  // open: clr
  Register #(.width(16)) Reg_B0 (
    .D(controlled_buffer_14_out), .en(Rom_A_data[19]), .clk(controlled_buffer_3_out), .Q(Reg_B0_q));  // open: clr
  not not_1 (not_1_out, Current_Opcode_q_2[4]);
  // Probe on Reg_B0_q
  // Probe on alu_16_bits_1_over_flow
  Register #(.width(16)) Reg_B2 (
    .D(controlled_buffer_14_out), .en(Rom_A_data[6]), .clk(controlled_buffer_3_out), .Q(Reg_B2_q));  // open: clr
  // Probe on matmult_2x2_1_regout_0
  // Probe on matmult_2x2_1_regout_2
  and and_1 (and_1_out, not_1_out, Current_Opcode_q_2[5], Current_Opcode_q_2[6], Current_Opcode_q_2[7]);
  Counter #(.max('h1f), .width(5)) ProgramCounter (
    .up(1'b1), .count(Rom_A_data[31]), .clk(controlled_buffer_3_out), .Q(ProgramCounter_q));  // open: clr, load, D, carry
  // Probe on Reg_A0_q
  Register #(.width(16)) Reg_B1 (
    .D(controlled_buffer_14_out), .en(Rom_A_data[7]), .clk(controlled_buffer_3_out), .Q(Reg_B1_q));  // open: clr
  Register #(.width(16)) Reg_B3 (
    .D(controlled_buffer_14_out), .en(Rom_A_data[5]), .clk(controlled_buffer_3_out), .Q(Reg_B3_q));  // open: clr
  ALU_16_bits alu_16_bits_1 (
    .Opcode({Current_Opcode_q[4], Current_Opcode_q_2}), .Flag(instruction_splitter_1_flag_bit),
    .Reg_A(Reg_A0_q), .Reg_B(Reg_B0_q), .Over_Flow(alu_16_bits_1_over_flow), .Reg_Out(alu_16_bits_1_reg_out));
  Register #(.width(16)) OverFlow_Register (
    .D(alu_16_bits_1_over_flow), .en(Rom_A_data[18]), .clk(controlled_buffer_3_out), .Q(OverFlow_Register_q));  // open: clr
  Matmult_2x2 matmult_2x2_1 (
    .Reg_A0(Reg_A0_q), .Reg_A1(Reg_A1_q), .Reg_A2(Reg_A2_q), .Reg_A3(Reg_A3_q), .Reg_B0(Reg_B0_q),
    .Reg_B1(Reg_B1_q), .Reg_B2(Reg_B2_q), .Reg_B3(Reg_B3_q), .RegOut_0(matmult_2x2_1_regout_0),
    .RegOut_1(matmult_2x2_1_regout_1), .RegOut_2(matmult_2x2_1_regout_2), .RegOut_3(matmult_2x2_1_regout_3));
  // Probe on matmult_2x2_1_regout_1
  // Probe on matmult_2x2_1_regout_3
  and and_2 (and_2_out, and_1_out, instruction_splitter_1_flag_bit);
  // Probe on alu_16_bits_1_reg_out
  Register #(.width(16)) RegOut_3 (
    .D(matmult_2x2_1_regout_3), .en(Rom_B_data[27]), .clk(controlled_buffer_3_out), .Q(RegOut_3_q));  // open: clr
  Register #(.width(16)) RegOut_2 (
    .D(matmult_2x2_1_regout_2), .en(Rom_B_data[27]), .clk(controlled_buffer_3_out), .Q(RegOut_2_q));  // open: clr
  not not_2 (not_2_out, and_2_out);
  assign controlled_buffer_1_out = Rom_B_data[26] ? ProgramCounter_q : 5'bz;  // Controlled_Buffer controlled_buffer_1
  Register #(.width(16)) Reg_A0 (
    .D(controlled_buffer_13_out), .en(Rom_A_data[20]), .clk(controlled_buffer_3_out), .Q(Reg_A0_q));  // open: clr
  Register #(.width(16)) Reg_A2 (
    .D(controlled_buffer_13_out), .en(Rom_A_data[9]), .clk(controlled_buffer_3_out), .Q(Reg_A2_q));  // open: clr
  assign controlled_buffer_2_out = instruction_splitter_1_flag_bit ? OverFlow_Register_q : 16'bz;  // Controlled_Buffer controlled_buffer_2
  Register #(.width(16)) RegOut_1 (
    .D(matmult_2x2_1_regout_1), .en(Rom_B_data[27]), .clk(controlled_buffer_3_out), .Q(RegOut_1_q));  // open: clr
  Instruction_splitter instruction_splitter_1 (
    .Instruction_Input(controlled_buffer_12_out), .WE(Rom_A_data[27]), .Clock(controlled_buffer_3_out),
    .Address_B(instruction_splitter_1_address_b), .Address_A(instruction_splitter_1_address_a),
    .OPCODE(instruction_splitter_1_opcode), .FLAG_BIT(instruction_splitter_1_flag_bit));
  Register #(.width(16)) Reg_A1 (
    .D(controlled_buffer_13_out), .en(Rom_A_data[10]), .clk(controlled_buffer_3_out), .Q(Reg_A1_q));  // open: clr
  Register #(.width(16)) Reg_A3 (
    .D(controlled_buffer_13_out), .en(Rom_A_data[8]), .clk(controlled_buffer_3_out), .Q(Reg_A3_q));  // open: clr
  Register #(.width(16)) Reg_Out (
    .D(alu_16_bits_1_reg_out), .en(Rom_A_data[18]), .clk(controlled_buffer_3_out), .Q(Reg_Out_q));  // open: clr
  // Probe on Reg_Out_q
  Register #(.width(16)) RegOut_0 (
    .D(matmult_2x2_1_regout_0), .en(Rom_B_data[27]), .clk(controlled_buffer_3_out), .Q(RegOut_0_q));  // open: clr
  Clock Clock_Main (.out(Clock_Main_out));
  assign controlled_buffer_3_out = not_2_out ? Clock_Main_out : 1'bz;  // Controlled_Buffer controlled_buffer_3
  assign controlled_buffer_1_out = Rom_B_data[25] ? instruction_splitter_1_address_a : 5'bz;  // Controlled_Buffer controlled_buffer_4
  Register #(.width(5)) MAR_Z (
    .D(controlled_buffer_1_out), .en(Rom_A_data[30]), .clk(controlled_buffer_3_out), .Q(MAR_Z_q));  // open: clr
  assign controlled_buffer_5_out = Rom_A_data[2] ? controlled_buffer_2_out : 16'bz;  // Controlled_Buffer controlled_buffer_5
  assign controlled_buffer_2_out = not_3_out ? Reg_Out_q : 16'bz;  // Controlled_Buffer controlled_buffer_6
  not not_3 (not_3_out, instruction_splitter_1_flag_bit);
  Register #(.width(5)) MAR_A (
    .D(instruction_splitter_1_address_a), .en(Rom_A_data[26]), .clk(controlled_buffer_3_out), .Q(MAR_A_q));  // open: clr
  assign controlled_buffer_5_out = Rom_A_data[1] ? Instruction_Ram_dout : 16'bz;  // Controlled_Buffer controlled_buffer_7
  Register #(.width(16)) MBR_Z (
    .D(controlled_buffer_5_out), .en(Rom_A_data[28]), .clk(controlled_buffer_3_out), .Q(MBR_Z_q));  // open: clr
  assign controlled_buffer_5_out = Rom_B_data[22] ? RegOut_0_q : 16'bz;  // Controlled_Buffer controlled_buffer_8
  Register #(.width(5)) MAR_B (
    .D(instruction_splitter_1_address_b), .en(Rom_A_data[25]), .clk(controlled_buffer_3_out), .Q(MAR_B_q));  // open: clr
  assign controlled_buffer_5_out = Rom_B_data[21] ? RegOut_1_q : 16'bz;  // Controlled_Buffer controlled_buffer_9
  assign controlled_buffer_5_out = Rom_B_data[20] ? RegOut_2_q : 16'bz;  // Controlled_Buffer controlled_buffer_10
  assign controlled_buffer_5_out = Rom_B_data[19] ? RegOut_3_q : 16'bz;  // Controlled_Buffer controlled_buffer_11
  assign controlled_buffer_12_out = Rom_A_data[13] ? MBR_Z_q : 16'bz;  // Controlled_Buffer controlled_buffer_12
  Register #(.width(16)) MBR_A (
    .D(Ram_A_dout), .en(Rom_A_data[22]), .clk(controlled_buffer_3_out), .Q(MBR_A_q));  // open: clr
  Register #(.width(16)) MBR_B (
    .D(Ram_B_dout), .en(Rom_A_data[21]), .clk(controlled_buffer_3_out), .Q(MBR_B_q));  // open: clr
  // Probe on MAR_A_q
  assign controlled_buffer_13_out = Rom_A_data[12] ? MBR_A_q : 16'bz;  // Controlled_Buffer controlled_buffer_13
  assign controlled_buffer_14_out = Rom_A_data[11] ? MBR_B_q : 16'bz;  // Controlled_Buffer controlled_buffer_14
  Counter #(.max('h1f), .width(5)) Counter_A (
    .load(Rom_B_data[31]), .D(MAR_A_q), .count(Rom_B_data[29]), .Q(Counter_A_q), .up(1'b1),
    .clk(controlled_buffer_3_out));  // open: carry, clr
  RAM #(.addrWidth(5), .dataWidth(16), .\type ("nonvolatile")) Instruction_Ram (
    .addr(MAR_Z_q), .we(Rom_A_data[17]), .oe(Rom_A_data[29]), .clk(controlled_buffer_3_out),
    .dout(Instruction_Ram_dout));  // open: din
  RAM #(.addrWidth(5), .dataWidth(16), .\type ("nonvolatile")) Ram_A (
    .addr(Counter_A_q), .we(Rom_A_data[16]), .oe(Rom_A_data[24]), .clk(controlled_buffer_3_out),
    .dout(Ram_A_dout));  // open: din
  Register #(.width(16)) Terminal_A (.Q(Terminal_A_q));  // open: D, en, clk, clr
  Register #(.width(16)) Terminal_B (.Q(Terminal_B_q));  // open: D, en, clk, clr
  // Bus_Terminus bus_terminus_1: pin names not known
  // Probe on Instruction_Ram_dout
  Counter #(.max('h1f), .width(5)) Counter_C (
    .load(Rom_B_data[24]), .D(MAR_Z_q), .count(Rom_B_data[23]), .Q(Counter_C_q), .up(1'b1),
    .clk(controlled_buffer_3_out));  // open: carry, clr
  Counter #(.max('h1f), .width(5)) Counter_B (
    .load(Rom_B_data[30]), .D(MAR_B_q), .count(Rom_B_data[28]), .Q(Counter_B_q), .up(1'b1),
    .clk(controlled_buffer_3_out));  // open: carry, clr
  RAM #(.addrWidth(5), .dataWidth(16), .\type ("nonvolatile")) Ram_B (
    .addr(Counter_B_q), .we(Rom_A_data[15]), .oe(Rom_A_data[23]), .clk(controlled_buffer_3_out),
    .dout(Ram_B_dout));  // open: din
  RAM #(.addrWidth(5), .dataWidth(16)) System_Ram (
    .addr(Counter_C_q), .we(Rom_A_data[3]), .oe(Rom_A_data[4]), .clk(controlled_buffer_3_out),
    .din(controlled_buffer_12_out));  // open: dout
  Counter #(.max('hf), .width(4)) Step_Counter (
    .clr(Rom_A_data[0]), .up(1'b1), .count(1'b1), .clk(controlled_buffer_3_out), .Q(Step_Counter_q));  // open: load, D, carry
  // Probe on in_5
  // Probe on in_6
  Register #(.width(16)) register_1 (
    .D(Instruction_Input), .en(WE), .clk(in_9), .Q({FLAG_BIT, OPCODE, Address_A, Address_B}));  // open: clr
  ROM #(.dataWidth(32)) Rom_B (.addr({Current_Opcode_q_2, Step_Counter_q}), .data(Rom_B_data));
  ROM #(.dataWidth(32)) Rom_A (.addr({Current_Opcode_q_2, Step_Counter_q}), .data(Rom_A_data));
  // Probe on Rom_A_data

  assign out_10 = in_1;
  assign out_11 = in_2;
  assign out_12 = in_3;
  assign out_13 = in_4;
  assign out_14 = in_5;
  assign out_15 = in_6;

  // Notes on the sheet:
  //   MatMult Result
  //   Bank B 
  //   Bank A
  //   MAR_Z_WE
  //   Instruction_Ram_OE
  //   MBR_Z_WE
  //   Instruction_Splitter_WE
  //   MAR_A_WE
  //   MAR_B_WE
  //   RAM_A_OE
  //   Ram_B_OE
  //   MBR_A_WE
  //   MBR_B_WE
  //   Reg_A0_WE
  //   Reg_B0_WE
  //   Reg_Out_WE
  //   Instrction_Ram_WE
  //   Ram_A_WE
  //   Ram_B_WE
  //   OPCODE_WE
  //   MBR_Z_OE
  //   MBR_A_OE
  //   MBR_B_OE
  //   Reg_A1_WE
  //   Reg_A2_WE
  //   Reg_A3_WE
  //   Reg_B1_WE
  //   Reg_B2_WE
  //   Reg_B3_WE
  //   System_Ram_OE
  //   System_Ram_WE
  //   RegOut_OE
  //   Clock_Reset
  //   Counter _A_WE
  //   Counter_B_WE
  //   RegOut_0_1_2_3_WE
  //   Program_Counter_CB
  //   Address_A_CB
  //   Counter_C_WE
  //   Counter_C_enable
  //   RegOut_0_CB
  //   Reg_1_CB
  //   Reg_2_CB
  //   Reg_3_CB
  //   Program_Counter_Increament_By_One
  //   Instruction_Ram_to_MBR_CB
  //   Counter_A_Increament_By_One
  //   Counter_B_Increament_By_One
  //   Opcode
  //   Step Counter
  //   contents of Rom_B (hex, n*v repeats v):
  //   4000000 0 0 2000000 c0000000 0 0 0 4000000 7*0 4000000 0 0 2000000 c0000000 0 0 0 4000000 7*0
  //   4000000 0 0 2000000 c0000000 0 0 0 4000000 7*0 4000000 0 0 2000000 c0000000 0 0 0 4000000 7*0
  //   4000000 0 0 2000000 1000000 4000000 10*0 4000000 0 0 2000000 c0000000 0 0 0 4000000 7*0 4000000 0 0
  //   2000000 c0000000 0 0 0 4000000 7*0 4000000 0 0 2000000 c0000000 30000000 30000000 30000000 0 0
  //   4000000 5*0 4000000 0 0 2000000 1400000 a00000 900000 880000 4000000 7*0 4000000 0 0 2000000
  //   c0000000 30000000 30000000 30000000 0 0 0 c000000 4*0 4000000 0 0 2000000 c0000000 0 0 0 4000000 7*0
  //   4000000 0 0 2000000 c0000000 0 0 0 4000000 7*0 4000000 0 0 2000000 c0000000 0 0 0 4000000 7*0
  //   4000000 0 0 2000000 c0000000 0 0 0 4000000 7*0 4000000 0 0 2000000 4000000 0 0 0 4000000 7*0 4000000
  //   0 0 2000000 c0000000 0 0 0 4000000
  //   contents of Rom_A (hex, n*v repeats v):
  //   e0000000 10002002 8002000 46004000 0 1800000 600000 181800 40040000 1 6*0 e0000000 10002002 8002000
  //   46004000 0 1800000 600000 181800 40040000 1 6*0 e0000000 10002002 8002000 46004000 0 1800000 600000
  //   181800 40040000 1 6*0 e0000000 10002002 8002000 46004000 0 1800000 600000 181800 40040000 1 6*0
  //   e0000000 10002002 8002000 46004000 10000004 40002008 1 9*0 e0000000 10002002 8002000 46004000 0
  //   1800000 600000 1800 400000 200000 40018000 1 4*0 e0000000 10002002 8002000 46004000 0 1800000 600000
  //   181800 40040000 1 6*0 e0000000 10002002 8002000 46004000 0 1800000 1e00000 1f81800 1e01c80 601a40
  //   40001920 1 4*0 e0000000 10002002 8002000 46004000 10000000 10002008 10002008 10002008 40002008 1 6*0
  //   e0000000 10002002 8002000 46004000 0 1800000 1e00000 1f81800 1e01c80 601a40 1920 40000000 1 0 0 0
  //   e0000000 10002002 8002000 46004000 0 1800000 600000 181800 40040000 1 6*0 e0000000 10002002 8002000
  //   46004000 0 1800000 600000 181800 40040000 1 6*0 e0000000 10002002 8002000 46004000 0 1800000 600000
  //   181800 40040000 1 6*0 e0000000 10002002 8002000 46004000 0 1800000 600000 181800 40040000 1 6*0
  //   e0000000 10002002 8002000 46004000 40000000 1 10*0 e0000000 10002002 8002000 46004000 0 1800000
  //   600000 181800 40040000 1
endmodule

module Bus_Terminus (
  input  OE,
  input  Input_01,
  input  Input_02,
  output System_Ram,
  output Ram_A,
  output Ram_B
);

  wire and_1_out, and_2_out, and_3_out, not_1_out, not_2_out;

  not not_1 (not_1_out, Input_01);
  not not_2 (not_2_out, Input_02);
  and and_1 (and_1_out, not_1_out, not_2_out);
  and and_2 (and_2_out, not_1_out, Input_02);
  and and_3 (and_3_out, Input_01, not_2_out);
  assign System_Ram = OE ? and_1_out : 1'bz;  // Controlled_Buffer controlled_buffer_1
  assign Ram_A = OE ? and_2_out : 1'bz;  // Controlled_Buffer controlled_buffer_2
  assign Ram_B = OE ? and_3_out : 1'bz;  // Controlled_Buffer controlled_buffer_3

  // Notes on the sheet:
  //   System Ram
  //   Ram A 
  //   Ram B
  //   00
  //   01
  //   10
endmodule

module Reg_Swap (
  input  [4:0] Opcode,
  input  [15:0] Reg_A0,
  input  [15:0] Reg_A1,
  input  [15:0] Reg_A2,
  input  [15:0] Reg_A3,
  input  [15:0] Reg_B0,
  input  [15:0] Reg_B1,
  input  [15:0] Reg_B2,
  input  [15:0] Reg_B3,
  input  [4:0] Address_1,
  input  [4:0] Address_2,
  output [15:0] RegA0,
  output [15:0] RegA1,
  output [15:0] RegA2,
  output [15:0] RegA3,
  output [15:0] RegB0,
  output [15:0] RegB1,
  output [15:0] RegB2,
  output [15:0] RegB3
);

  wire and_1_out, and_2_out, and_3_out, and_4_out, and_5_out, and_6_out, and_7_out, and_8_out, and_9_out,
       not_1_out, not_2_out, not_3_out, not_4_out, not_5_out, not_6_out, not_7_out, not_8_out, not_9_out,
       not_10_out, not_11_out, not_12_out, not_13_out, not_14_out, not_15_out, not_16_out, not_17_out,
       not_18_out, not_19_out, not_20_out;
  wire [15:0] and_10_out, and_11_out, and_12_out, and_13_out, and_14_out, and_15_out, and_16_out, and_17_out,
       bit_extender_1_out, bit_extender_2_out, bit_extender_3_out, bit_extender_4_out, bit_extender_5_out,
       bit_extender_6_out, bit_extender_7_out, bit_extender_8_out, controlled_buffer_1_out,
       controlled_buffer_2_out, controlled_buffer_4_out, controlled_buffer_5_out, controlled_buffer_6_out,
       controlled_buffer_7_out, controlled_buffer_10_out, controlled_buffer_12_out, or_1_out, or_2_out;

  not not_1 (not_1_out, Opcode[0]);
  not not_2 (not_2_out, Opcode[3]);
  and and_1 (and_1_out, not_1_out, Opcode[1], Opcode[2], not_2_out);
  not not_3 (not_3_out, Address_1[0]);
  not not_4 (not_4_out, Address_1[1]);
  not not_5 (not_5_out, Address_1[2]);
  not not_6 (not_6_out, Address_1[3]);
  not not_7 (not_7_out, Address_1[4]);
  not not_8 (not_8_out, Address_2[0]);
  not not_9 (not_9_out, Address_2[1]);
  not not_10 (not_10_out, Address_2[2]);
  not not_11 (not_11_out, Address_2[3]);
  not not_12 (not_12_out, Address_2[4]);
  and and_2 (and_2_out, Address_1[0], not_4_out, not_5_out, not_6_out, not_7_out);
  and and_3 (and_3_out, not_3_out, Address_1[1], not_5_out, not_6_out, not_7_out);
  and and_4 (and_4_out, Address_1[1], Address_1[0], not_5_out, not_6_out, not_7_out);
  and and_5 (and_5_out, not_3_out, not_4_out, Address_1[2], not_6_out, not_7_out);
  and and_6 (and_6_out, Address_2[0], not_9_out, Address_2[2], not_11_out, not_12_out);
  and and_7 (and_7_out, not_8_out, Address_2[1], Address_2[2], not_11_out, not_12_out);
  and and_8 (and_8_out, Address_2[0], Address_2[1], Address_2[2], not_11_out, not_12_out);
  and and_9 (and_9_out, not_8_out, not_9_out, not_10_out, Address_2[3], not_10_out);
  assign bit_extender_1_out = {{15{and_2_out}}, and_2_out};  // Bit_Extender bit_extender_1
  assign bit_extender_2_out = {{15{and_3_out}}, and_3_out};  // Bit_Extender bit_extender_2
  assign bit_extender_3_out = {{15{and_4_out}}, and_4_out};  // Bit_Extender bit_extender_3
  assign bit_extender_4_out = {{15{and_5_out}}, and_5_out};  // Bit_Extender bit_extender_4
  assign bit_extender_5_out = {{15{and_6_out}}, and_6_out};  // Bit_Extender bit_extender_5
  assign bit_extender_6_out = {{15{and_7_out}}, and_7_out};  // Bit_Extender bit_extender_6
  assign bit_extender_7_out = {{15{and_8_out}}, and_8_out};  // Bit_Extender bit_extender_7
  assign bit_extender_8_out = {{15{and_9_out}}, and_9_out};  // Bit_Extender bit_extender_8
  assign and_10_out = bit_extender_1_out & Reg_A0;  // AND_Gate and_10, 16 bits wide
  assign and_11_out = bit_extender_2_out & Reg_A1;  // AND_Gate and_11, 16 bits wide
  assign and_12_out = bit_extender_3_out & Reg_A2;  // AND_Gate and_12, 16 bits wide
  assign and_13_out = bit_extender_4_out & Reg_A3;  // AND_Gate and_13, 16 bits wide
  assign and_14_out = bit_extender_5_out & Reg_B0;  // AND_Gate and_14, 16 bits wide
  assign and_15_out = bit_extender_6_out & Reg_B1;  // AND_Gate and_15, 16 bits wide
  assign and_16_out = bit_extender_7_out & Reg_B2;  // AND_Gate and_16, 16 bits wide
  assign and_17_out = bit_extender_8_out & Reg_B3;  // AND_Gate and_17, 16 bits wide
  assign or_1_out = and_10_out | and_11_out | and_12_out | and_13_out;  // OR_Gate or_1, 16 bits wide
  assign or_2_out = and_14_out | and_15_out | and_16_out | and_17_out;  // OR_Gate or_2, 16 bits wide
  assign controlled_buffer_1_out = and_2_out ? or_2_out : 16'bz;  // Controlled_Buffer controlled_buffer_1
  assign controlled_buffer_2_out = and_6_out ? or_1_out : 16'bz;  // Controlled_Buffer controlled_buffer_2
  not not_13 (not_13_out, and_2_out);
  assign controlled_buffer_1_out = not_13_out ? Reg_A0 : 16'bz;  // Controlled_Buffer controlled_buffer_3
  not not_14 (not_14_out, and_3_out);
  not not_15 (not_15_out, and_4_out);
  not not_16 (not_16_out, and_5_out);
  assign controlled_buffer_4_out = and_3_out ? or_2_out : 16'bz;  // Controlled_Buffer controlled_buffer_4
  assign controlled_buffer_5_out = and_4_out ? or_2_out : 16'bz;  // Controlled_Buffer controlled_buffer_5
  not not_17 (not_17_out, and_6_out);
  not not_18 (not_18_out, and_7_out);
  not not_19 (not_19_out, and_8_out);
  not not_20 (not_20_out, and_9_out);
  assign controlled_buffer_6_out = and_7_out ? or_1_out : 16'bz;  // Controlled_Buffer controlled_buffer_6
  assign controlled_buffer_7_out = and_8_out ? or_1_out : 16'bz;  // Controlled_Buffer controlled_buffer_7
  assign controlled_buffer_4_out = not_14_out ? Reg_A1 : 16'bz;  // Controlled_Buffer controlled_buffer_8
  assign controlled_buffer_5_out = not_15_out ? Reg_A2 : 16'bz;  // Controlled_Buffer controlled_buffer_9
  assign controlled_buffer_10_out = not_16_out ? Reg_A3 : 16'bz;  // Controlled_Buffer controlled_buffer_10
  assign controlled_buffer_10_out = and_5_out ? or_2_out : 16'bz;  // Controlled_Buffer controlled_buffer_11
  assign controlled_buffer_12_out = and_9_out ? or_1_out : 16'bz;  // Controlled_Buffer controlled_buffer_12
  assign controlled_buffer_2_out = not_17_out ? Reg_B0 : 16'bz;  // Controlled_Buffer controlled_buffer_13
  assign controlled_buffer_6_out = not_18_out ? Reg_B1 : 16'bz;  // Controlled_Buffer controlled_buffer_14
  assign controlled_buffer_7_out = not_19_out ? Reg_B2 : 16'bz;  // Controlled_Buffer controlled_buffer_15
  assign controlled_buffer_12_out = not_20_out ? Reg_B3 : 16'bz;  // Controlled_Buffer controlled_buffer_16
  assign RegA0 = and_1_out ? controlled_buffer_1_out : 16'bz;  // Controlled_Buffer controlled_buffer_17
  assign RegA1 = and_1_out ? controlled_buffer_4_out : 16'bz;  // Controlled_Buffer controlled_buffer_18
  assign RegA2 = and_1_out ? controlled_buffer_5_out : 16'bz;  // Controlled_Buffer controlled_buffer_19
  assign RegA3 = and_1_out ? controlled_buffer_10_out : 16'bz;  // Controlled_Buffer controlled_buffer_20
  assign RegB0 = and_1_out ? controlled_buffer_2_out : 16'bz;  // Controlled_Buffer controlled_buffer_21
  assign RegB1 = and_1_out ? controlled_buffer_6_out : 16'bz;  // Controlled_Buffer controlled_buffer_22
  assign RegB2 = and_1_out ? controlled_buffer_7_out : 16'bz;  // Controlled_Buffer controlled_buffer_23
  assign RegB3 = and_1_out ? controlled_buffer_12_out : 16'bz;  // Controlled_Buffer controlled_buffer_24

  // Notes on the sheet:
  //   00001
  //   00010
  //   00011
  //   00100
  //   00101
  //   00110
  //   00111
  //   01000
endmodule

module PCU_Memory_Swap_failed (
  input  [7:0] in_1,
  input  [7:0] in_2,
  input  [4:0] in_3,
  input  [4:0] in_4,
  input  [15:0] in_5,
  input  [15:0] in_6,
  input  [15:0] Instruction_Input,
  input  WE,
  input  in_9,
  input  [4:0] Address_1,
  input  [4:0] Address_2,
  input  in_12,
  input  in_13,
  output [7:0] out_14,
  output [7:0] out_15,
  output [4:0] out_16,
  output [4:0] out_17,
  output [15:0] out_18,
  output [15:0] out_19,
  output [4:0] Address_B,
  output [4:0] Address_A,
  output [4:0] OPCODE,
  output FLAG_BIT
);

  wire and_1_out, and_2_out, bus_terminus_1_ram_a, bus_terminus_1_ram_b, bus_terminus_1_system_ram,
       Clock_Main_out, controlled_buffer_3_out, instruction_splitter_1_flag_bit, not_1_out, not_2_out,
       not_3_out, reg_swap_input_selector_1_p2, reg_swap_input_selector_1_p3, reg_swap_input_selector_1_p5,
       reg_swap_input_selector_1_p7, reg_swap_input_selector_1_p9, reg_swap_input_selector_1_p11,
       reg_swap_input_selector_1_p13, reg_swap_input_selector_1_p15, reg_swap_input_selector_1_p17,
       reg_swap_input_selector_1_p18, reg_swap_input_selector_1_p19, reg_swap_input_selector_1_p20,
       reg_swap_input_selector_1_p21, reg_swap_input_selector_1_p22, reg_swap_input_selector_1_p23,
       reg_swap_input_selector_1_p24, undriven, undriven_2;
  wire [3:0] Step_Counter_q;
  wire [4:0] controlled_buffer_1_out, Counter_A_q, Counter_B_q, Counter_C_q,
       instruction_splitter_1_address_a, instruction_splitter_1_address_b, instruction_splitter_1_opcode,
       MAR_A_q, MAR_B_q, MAR_Z_q, ProgramCounter_q;
  wire [4:4] Current_Opcode_q;
  wire [7:4] Current_Opcode_q_2;
  wire [15:0] alu_16_bits_1_over_flow, alu_16_bits_1_reg_out, controlled_buffer_2_out,
       controlled_buffer_5_out, controlled_buffer_12_out, controlled_buffer_13_out, controlled_buffer_14_out,
       controlled_buffer_16_out, controlled_buffer_17_out, Instruction_Ram_dout, matmult_2x2_1_regout_0,
       matmult_2x2_1_regout_1, matmult_2x2_1_regout_2, matmult_2x2_1_regout_3, MBR_A_q, MBR_B_q, MBR_Z_q,
       OverFlow_Register_q, Ram_A_dout, Reg_A0_q, Reg_A1_q, Reg_A2_q, Reg_A3_q, Reg_B0_q, Reg_B1_q, Reg_B2_q,
       Reg_B3_q, Reg_Out_q, reg_swap_1_p11, reg_swap_1_p19, RegOut_0_q, RegOut_1_q, RegOut_2_q, RegOut_3_q,
       Terminal_A_q;
  wire [31:0] Rom_A_data, Rom_B_data;

  Register #(.width(5)) Current_Opcode (
    .D(instruction_splitter_1_opcode), .en(Rom_A_data[14]), .clk(controlled_buffer_3_out),
    .Q({Current_Opcode_q[4], Current_Opcode_q_2}));  // open: clr
  Register #(.width(16)) Reg_B0 (
    .D(controlled_buffer_14_out), .en(reg_swap_input_selector_1_p21), .clk(controlled_buffer_3_out),
    .Q(Reg_B0_q));  // open: clr
  not not_1 (not_1_out, Current_Opcode_q_2[4]);
  // Probe on Reg_B0_q
  // Probe on alu_16_bits_1_over_flow
  Register #(.width(16)) Reg_B2 (
    .D(controlled_buffer_14_out), .en(reg_swap_input_selector_1_p23), .clk(controlled_buffer_3_out),
    .Q(Reg_B2_q));  // open: clr
  // Probe on matmult_2x2_1_regout_0
  // Probe on matmult_2x2_1_regout_2
  and and_1 (and_1_out, not_1_out, Current_Opcode_q_2[5], Current_Opcode_q_2[6], Current_Opcode_q_2[7]);
  Counter #(.max('h1f), .width(5)) ProgramCounter (
    .up(1'b1), .count(Rom_A_data[31]), .clk(controlled_buffer_3_out), .Q(ProgramCounter_q));  // open: clr, load, D, carry
  // Reg_swap_input_selector reg_swap_input_selector_1: pin names not known; wires that end beside it: Rom_A_data[20], reg_swap_input_selector_1_p2, reg_swap_input_selector_1_p3, Rom_A_data[10], reg_swap_input_selector_1_p5, Rom_A_data[9], reg_swap_input_selector_1_p7, Rom_A_data[8], reg_swap_input_selector_1_p9, Rom_A_data[19], reg_swap_input_selector_1_p11, Rom_A_data[7], reg_swap_input_selector_1_p13, Rom_A_data[6], reg_swap_input_selector_1_p15, Rom_A_data[5], reg_swap_input_selector_1_p17, reg_swap_input_selector_1_p18, reg_swap_input_selector_1_p19, reg_swap_input_selector_1_p20, reg_swap_input_selector_1_p21, reg_swap_input_selector_1_p22, reg_swap_input_selector_1_p23, reg_swap_input_selector_1_p24
  // Probe on Reg_A0_q
  Register #(.width(16)) Reg_B1 (
    .D(controlled_buffer_14_out), .en(reg_swap_input_selector_1_p22), .clk(controlled_buffer_3_out),
    .Q(Reg_B1_q));  // open: clr
  Register #(.width(16)) Reg_B3 (
    .D(controlled_buffer_14_out), .en(reg_swap_input_selector_1_p24), .clk(controlled_buffer_3_out),
    .Q(Reg_B3_q));  // open: clr
  ALU_16_bits alu_16_bits_1 (
    .Opcode({Current_Opcode_q[4], Current_Opcode_q_2}), .Flag(instruction_splitter_1_flag_bit),
    .Reg_A(Reg_A0_q), .Reg_B(Reg_B0_q), .Over_Flow(alu_16_bits_1_over_flow), .Reg_Out(alu_16_bits_1_reg_out));
  Register #(.width(16)) OverFlow_Register (
    .D(alu_16_bits_1_over_flow), .en(Rom_A_data[18]), .clk(controlled_buffer_3_out), .Q(OverFlow_Register_q));  // open: clr
  Matmult_2x2 matmult_2x2_1 (
    .Reg_A0(Reg_A0_q), .Reg_A1(Reg_A1_q), .Reg_A2(Reg_A2_q), .Reg_A3(Reg_A3_q), .Reg_B0(Reg_B0_q),
    .Reg_B1(Reg_B1_q), .Reg_B2(Reg_B2_q), .Reg_B3(Reg_B3_q), .RegOut_0(matmult_2x2_1_regout_0),
    .RegOut_1(matmult_2x2_1_regout_1), .RegOut_2(matmult_2x2_1_regout_2), .RegOut_3(matmult_2x2_1_regout_3));
  // Probe on matmult_2x2_1_regout_1
  // Probe on matmult_2x2_1_regout_3
  and and_2 (and_2_out, and_1_out, instruction_splitter_1_flag_bit);
  // Probe on alu_16_bits_1_reg_out
  Register #(.width(16)) RegOut_3 (
    .D(matmult_2x2_1_regout_3), .en(Rom_B_data[27]), .clk(controlled_buffer_3_out), .Q(RegOut_3_q));  // open: clr
  Register #(.width(16)) RegOut_2 (
    .D(matmult_2x2_1_regout_2), .en(Rom_B_data[27]), .clk(controlled_buffer_3_out), .Q(RegOut_2_q));  // open: clr
  not not_2 (not_2_out, and_2_out);
  assign controlled_buffer_1_out = Rom_B_data[26] ? ProgramCounter_q : 5'bz;  // Controlled_Buffer controlled_buffer_1
  Register #(.width(16)) Reg_A0 (
    .D(controlled_buffer_13_out), .en(reg_swap_input_selector_1_p17), .clk(controlled_buffer_3_out),
    .Q(Reg_A0_q));  // open: clr
  Register #(.width(16)) Reg_A2 (
    .D(controlled_buffer_13_out), .en(reg_swap_input_selector_1_p19), .clk(controlled_buffer_3_out),
    .Q(Reg_A2_q));  // open: clr
  assign controlled_buffer_2_out = instruction_splitter_1_flag_bit ? OverFlow_Register_q : 16'bz;  // Controlled_Buffer controlled_buffer_2
  Register #(.width(16)) RegOut_1 (
    .D(matmult_2x2_1_regout_1), .en(Rom_B_data[27]), .clk(controlled_buffer_3_out), .Q(RegOut_1_q));  // open: clr
  Instruction_splitter instruction_splitter_1 (
    .Instruction_Input(controlled_buffer_12_out), .WE(Rom_A_data[27]), .Clock(controlled_buffer_3_out),
    .Address_B(instruction_splitter_1_address_b), .Address_A(instruction_splitter_1_address_a),
    .OPCODE(instruction_splitter_1_opcode), .FLAG_BIT(instruction_splitter_1_flag_bit));
  Register #(.width(16)) Reg_A1 (
    .D(controlled_buffer_13_out), .en(reg_swap_input_selector_1_p18), .clk(controlled_buffer_3_out),
    .Q(Reg_A1_q));  // open: clr
  Register #(.width(16)) Reg_A3 (
    .D(controlled_buffer_13_out), .en(reg_swap_input_selector_1_p20), .clk(controlled_buffer_3_out),
    .Q(Reg_A3_q));  // open: clr
  Register #(.width(16)) Reg_Out (
    .D(alu_16_bits_1_reg_out), .en(Rom_A_data[18]), .clk(controlled_buffer_3_out), .Q(Reg_Out_q));  // open: clr
  // Probe on Reg_Out_q
  Register #(.width(16)) RegOut_0 (
    .D(matmult_2x2_1_regout_0), .en(Rom_B_data[27]), .clk(controlled_buffer_3_out), .Q(RegOut_0_q));  // open: clr
  Clock Clock_Main (.out(Clock_Main_out));
  assign controlled_buffer_3_out = not_2_out ? Clock_Main_out : 1'bz;  // Controlled_Buffer controlled_buffer_3
  assign controlled_buffer_1_out = Rom_B_data[25] ? instruction_splitter_1_address_a : 5'bz;  // Controlled_Buffer controlled_buffer_4
  Register #(.width(5)) MAR_Z (
    .D(controlled_buffer_1_out), .en(Rom_A_data[30]), .clk(controlled_buffer_3_out), .Q(MAR_Z_q));  // open: clr
  assign controlled_buffer_5_out = Rom_A_data[2] ? controlled_buffer_2_out : 16'bz;  // Controlled_Buffer controlled_buffer_5
  assign controlled_buffer_2_out = not_3_out ? Reg_Out_q : 16'bz;  // Controlled_Buffer controlled_buffer_6
  not not_3 (not_3_out, instruction_splitter_1_flag_bit);
  Register #(.width(5)) MAR_A (
    .D(instruction_splitter_1_address_a), .en(Rom_A_data[26]), .clk(controlled_buffer_3_out), .Q(MAR_A_q));  // open: clr
  assign controlled_buffer_5_out = Rom_A_data[1] ? Instruction_Ram_dout : 16'bz;  // Controlled_Buffer controlled_buffer_7
  Register #(.width(16)) MBR_Z (
    .D(controlled_buffer_5_out), .en(Rom_A_data[28]), .clk(controlled_buffer_3_out), .Q(MBR_Z_q));  // open: clr
  assign controlled_buffer_5_out = Rom_B_data[22] ? RegOut_0_q : 16'bz;  // Controlled_Buffer controlled_buffer_8
  Register #(.width(5)) MAR_B (
    .D(instruction_splitter_1_address_b), .en(Rom_A_data[25]), .clk(controlled_buffer_3_out), .Q(MAR_B_q));  // open: clr
  assign controlled_buffer_5_out = Rom_B_data[21] ? RegOut_1_q : 16'bz;  // Controlled_Buffer controlled_buffer_9
  assign controlled_buffer_5_out = Rom_B_data[20] ? RegOut_2_q : 16'bz;  // Controlled_Buffer controlled_buffer_10
  assign controlled_buffer_5_out = Rom_B_data[19] ? RegOut_3_q : 16'bz;  // Controlled_Buffer controlled_buffer_11
  assign controlled_buffer_12_out = Rom_A_data[13] ? MBR_Z_q : 16'bz;  // Controlled_Buffer controlled_buffer_12
  Register #(.width(16)) MBR_A (
    .D(Ram_A_dout), .en(Rom_A_data[22]), .clk(controlled_buffer_3_out), .Q(MBR_A_q));  // open: clr
  Register #(.width(16)) MBR_B (
    .D(controlled_buffer_16_out), .en(Rom_A_data[21]), .clk(controlled_buffer_3_out), .Q(MBR_B_q));  // open: clr
  // Probe on MAR_A_q
  assign controlled_buffer_13_out = Rom_A_data[12] ? MBR_A_q : 16'bz;  // Controlled_Buffer controlled_buffer_13
  assign controlled_buffer_14_out = Rom_A_data[11] ? MBR_B_q : 16'bz;  // Controlled_Buffer controlled_buffer_14
  Counter #(.max('h1f), .width(5)) Counter_A (
    .load(Rom_B_data[31]), .D(MAR_A_q), .count(Rom_B_data[29]), .Q(Counter_A_q), .up(1'b1),
    .clk(controlled_buffer_3_out));  // open: carry, clr
  RAM #(.addrWidth(5), .dataWidth(16), .\type ("nonvolatile")) Instruction_Ram (
    .addr(MAR_Z_q), .we(Rom_A_data[17]), .oe(Rom_A_data[29]), .clk(controlled_buffer_3_out),
    .dout(Instruction_Ram_dout));  // open: din
  RAM #(.addrWidth(5), .dataWidth(16), .\type ("nonvolatile")) Ram_A (
    .addr(Counter_A_q), .we(Rom_A_data[16]), .oe(Rom_A_data[24]), .clk(controlled_buffer_3_out),
    .dout(Ram_A_dout));  // open: din
  // Reg_Swap reg_swap_1: pin names not known; wires that end beside it: Address_1, Reg_A0_q, Reg_A1_q, Reg_A2_q, Reg_A3_q, Address_2, Reg_B0_q, Reg_B1_q, Reg_B2_q, Reg_B3_q, reg_swap_1_p11, reg_swap_input_selector_1_p2, reg_swap_1_p11, reg_swap_input_selector_1_p3, reg_swap_1_p11, reg_swap_input_selector_1_p5, reg_swap_1_p11, reg_swap_input_selector_1_p7, reg_swap_1_p19, reg_swap_input_selector_1_p9, reg_swap_1_p19, reg_swap_input_selector_1_p11, reg_swap_1_p19, reg_swap_input_selector_1_p13
  Register #(.width(16)) Terminal_A (.D(reg_swap_1_p11), .en(in_12), .Q(Terminal_A_q));  // open: clk, clr
  Register #(.width(16)) Terminal_B (.D(reg_swap_1_p19), .en(in_13), .Q(Terminal_A_q));  // open: clk, clr
  // Probe on Instruction_Ram_dout
  Bus_Terminus bus_terminus_1 (
    .Input_01(undriven), .Input_02(undriven_2), .System_Ram(bus_terminus_1_system_ram),
    .Ram_A(bus_terminus_1_ram_a), .Ram_B(bus_terminus_1_ram_b));  // open: OE
  Counter #(.max('h1f), .width(5)) Counter_C (
    .load(Rom_B_data[24]), .D(MAR_Z_q), .count(Rom_B_data[23]), .Q(Counter_C_q), .up(1'b1),
    .clk(controlled_buffer_3_out));  // open: carry, clr
  Counter #(.max('h1f), .width(5)) Counter_B (
    .load(Rom_B_data[30]), .D(MAR_B_q), .count(Rom_B_data[28]), .Q(Counter_B_q), .up(1'b1),
    .clk(controlled_buffer_3_out));  // open: carry, clr
  assign Ram_A_dout = bus_terminus_1_ram_b ? Terminal_A_q : 16'bz;  // Controlled_Buffer controlled_buffer_15
  assign controlled_buffer_16_out = bus_terminus_1_ram_a ? Terminal_A_q : 16'bz;  // Controlled_Buffer controlled_buffer_16
  assign controlled_buffer_17_out = bus_terminus_1_system_ram ? Terminal_A_q : 16'bz;  // Controlled_Buffer controlled_buffer_17
  RAM #(.addrWidth(5), .dataWidth(16), .\type ("nonvolatile")) Ram_B (
    .addr(Counter_B_q), .we(Rom_A_data[15]), .oe(Rom_A_data[23]), .clk(controlled_buffer_3_out),
    .dout(controlled_buffer_16_out));  // open: din
  RAM #(.addrWidth(5), .dataWidth(16)) System_Ram (
    .addr(Counter_C_q), .we(Rom_A_data[3]), .oe(Rom_A_data[4]), .clk(controlled_buffer_3_out),
    .din(controlled_buffer_12_out));  // open: dout
  Counter #(.max('hf), .width(4)) Step_Counter (
    .clr(Rom_A_data[0]), .up(1'b1), .count(1'b1), .clk(controlled_buffer_3_out), .Q(Step_Counter_q));  // open: load, D, carry
  // Probe on in_5
  // Probe on in_6
  Register #(.width(16)) register_1 (
    .D(Instruction_Input), .en(WE), .clk(in_9), .Q({FLAG_BIT, OPCODE, Address_A, Address_B}));  // open: clr
  ROM #(.dataWidth(32)) Rom_B (.addr({Current_Opcode_q_2, Step_Counter_q}), .data(Rom_B_data));
  ROM #(.dataWidth(32)) Rom_A (.addr({Current_Opcode_q_2, Step_Counter_q}), .data(Rom_A_data));
  // Probe on Rom_A_data

  assign out_14 = in_1;
  assign out_15 = in_2;
  assign out_16 = in_3;
  assign out_17 = in_4;
  assign out_18 = in_5;
  assign out_19 = in_6;

  // Notes on the sheet:
  //   MatMult Result
  //   Bank B 
  //   Bank A
  //   To Ram A
  //   To Ram B
  //   To System Ram
  //   MAR_Z_WE
  //   Instruction_Ram_OE
  //   MBR_Z_WE
  //   Instruction_Splitter_WE
  //   MAR_A_WE
  //   MAR_B_WE
  //   RAM_A_OE
  //   Ram_B_OE
  //   MBR_A_WE
  //   MBR_B_WE
  //   Reg_A0_WE
  //   Reg_B0_WE
  //   Reg_Out_WE
  //   Instrction_Ram_WE
  //   Ram_A_WE
  //   Ram_B_WE
  //   OPCODE_WE
  //   MBR_Z_OE
  //   MBR_A_OE
  //   MBR_B_OE
  //   Reg_A1_WE
  //   Reg_A2_WE
  //   Reg_A3_WE
  //   Reg_B1_WE
  //   Reg_B2_WE
  //   Reg_B3_WE
  //   System_Ram_OE
  //   System_Ram_WE
  //   RegOut_OE
  //   Clock_Reset
  //   Counter _A_WE
  //   Counter_B_WE
  //   RegOut_0_1_2_3_WE
  //   Program_Counter_CB
  //   Address_A_CB
  //   Counter_C_WE
  //   Counter_C_enable
  //   RegOut_0_CB
  //   Reg_1_CB
  //   Reg_2_CB
  //   Reg_3_CB
  //   Program_Counter_Increament_By_One
  //   Instruction_Ram_to_MBR_CB
  //   Counter_A_Increament_By_One
  //   Counter_B_Increament_By_One
  //   Opcode
  //   Step Counter
  //   contents of Rom_B (hex, n*v repeats v):
  //   4000000 0 0 2000000 c0000000 0 0 0 4000000 7*0 4000000 0 0 2000000 c0000000 0 0 0 4000000 7*0
  //   4000000 0 0 2000000 c0000000 0 0 0 4000000 7*0 4000000 0 0 2000000 c0000000 0 0 0 4000000 7*0
  //   4000000 0 0 2000000 1000000 4000000 10*0 4000000 0 0 2000000 c0000000 0 0 0 4000000 7*0 4000000 0 0
  //   2000000 c0000000 0 0 0 4000000 7*0 4000000 0 0 2000000 c0000000 30000000 30000000 30000000 0 0
  //   4000000 5*0 4000000 0 0 2000000 1400000 a00000 900000 880000 4000000 7*0 4000000 0 0 2000000
  //   c0000000 30000000 30000000 30000000 0 0 0 c000000 4*0 4000000 0 0 2000000 c0000000 0 0 0 4000000 7*0
  //   4000000 0 0 2000000 c0000000 0 0 0 4000000 7*0 4000000 0 0 2000000 c0000000 0 0 0 4000000 7*0
  //   4000000 0 0 2000000 c0000000 0 0 0 4000000 7*0 4000000 0 0 2000000 4000000 0 0 0 4000000 7*0 4000000
  //   0 0 2000000 c0000000 0 0 0 4000000
  //   contents of Rom_A (hex, n*v repeats v):
  //   e0000000 10002002 8002000 46004000 0 1800000 600000 181800 40040000 1 6*0 e0000000 10002002 8002000
  //   46004000 0 1800000 600000 181800 40040000 1 6*0 e0000000 10002002 8002000 46004000 0 1800000 600000
  //   181800 40040000 1 6*0 e0000000 10002002 8002000 46004000 0 1800000 600000 181800 40040000 1 6*0
  //   e0000000 10002002 8002000 46004000 10000004 40002008 1 9*0 e0000000 10002002 8002000 46004000 0
  //   1800000 600000 181800 40040000 1 6*0 e0000000 10002002 8002000 46004000 0 1800000 600000 181800
  //   40040000 1 6*0 e0000000 10002002 8002000 46004000 0 1800000 1e00000 1f81800 1e01c80 601a40 40001920
  //   1 4*0 e0000000 10002002 8002000 46004000 10000000 10002008 10002008 10002008 40002008 1 6*0 e0000000
  //   10002002 8002000 46004000 0 1800000 1e00000 1f81800 1e01c80 601a40 1920 40000000 1 0 0 0 e0000000
  //   10002002 8002000 46004000 0 1800000 600000 181800 40040000 1 6*0 e0000000 10002002 8002000 46004000
  //   0 1800000 600000 181800 40040000 1 6*0 e0000000 10002002 8002000 46004000 0 1800000 600000 181800
  //   40040000 1 6*0 e0000000 10002002 8002000 46004000 0 1800000 600000 181800 40040000 1 6*0 e0000000
  //   10002002 8002000 46004000 40000000 1 10*0 e0000000 10002002 8002000 46004000 0 1800000 600000 181800
  //   40040000 1
endmodule

module Reg_swap_input_selector (
  input  We_A0_1,
  input  WE_A0_2,
  input  WE_A1_1,
  input  WE_A1_2,
  input  We_A2_1,
  input  We_A2_2,
  input  We_A3_1,
  input  We_A3_2,
  input  We_B0_1,
  input  We_B0_2,
  input  We_B1_1,
  input  We_B1_2,
  input  We_B2_1,
  input  We_B2_2,
  input  We_B3_1,
  input  We_B3_2,
  output Reg_A0_we,
  output Reg_A1_we,
  output Reg_A2_we,
  output Reg_A3_we,
  output Reg_B0_we,
  output Reg_B1_we,
  output Reg_B2_we,
  output Reg_B3_we
);

  or or_1 (Reg_A0_we, We_A0_1, WE_A0_2);
  or or_2 (Reg_A1_we, WE_A1_1, WE_A1_2);
  or or_3 (Reg_A2_we, We_A2_1, We_A2_2);
  or or_4 (Reg_A3_we, We_A3_1, We_A3_2);
  or or_5 (Reg_B0_we, We_B0_1, We_B0_2);
  or or_6 (Reg_B1_we, We_B1_1, We_B1_2);
  or or_7 (Reg_B2_we, We_B2_1, We_B2_2);
  or or_8 (Reg_B3_we, We_B3_1, We_B3_2);
endmodule

module PCU_Final (
  input  [3:0] in_1,
  input  [7:0] in_2,
  input  [7:0] in_3,
  input  [4:0] in_4,
  input  [4:0] in_5,
  input  [15:0] in_6,
  input  [15:0] in_7,
  input  [15:0] Instruction_Input,
  input  WE,
  input  in_10,
  output [3:0] out_11,
  output [7:0] out_12,
  output [7:0] out_13,
  output [4:0] out_14,
  output [4:0] out_15,
  output [15:0] out_16,
  output [15:0] out_17,
  output [4:0] Address_B,
  output [4:0] Address_A,
  output [4:0] OPCODE,
  output FLAG_BIT
);

  wire and_1_out, and_2_out, and_3_out, bus_terminus_1_ram_a, bus_terminus_1_ram_b, Clock_Main_out,
       controlled_buffer_11_out, controlled_buffer_29_out, controlled_buffer_35_out,
       controlled_buffer_40_out, Debug_Counter_carry, Debug_register_q, instruction_splitter_1_flag_bit,
       mover_decoder_1_a, mover_decoder_1_b, mover_decoder_2_a, mover_decoder_2_b, not_1_out, not_2_out,
       not_3_out, not_4_out, not_5_out, not_6_out, not_7_out, not_8_out;
  wire [3:0] Step_Counter_q;
  wire [4:0] controlled_buffer_9_out, controlled_buffer_27_out, controlled_buffer_34_out,
       controlled_buffer_36_out, Counter_A_q, Counter_B_q, Counter_C_q, Debug_Register_2_q,
       instruction_splitter_1_address_a, instruction_splitter_1_address_b, instruction_splitter_1_opcode,
       MAR_A_q, MAR_B_q, MAR_Z_q, ProgramCounter_q;
  wire [4:4] Current_Opcode_q;
  wire [7:4] Current_Opcode_q_2;
  wire [15:0] alu_16_bits_1_over_flow, alu_16_bits_1_reg_out, controlled_buffer_1_out,
       controlled_buffer_2_out, controlled_buffer_3_out, controlled_buffer_4_out, controlled_buffer_10_out,
       controlled_buffer_14_out, controlled_buffer_22_out, controlled_buffer_23_out,
       controlled_buffer_24_out, controlled_buffer_25_out, controlled_buffer_26_out, Instruction_Ram_dout,
       matmult_2x2_1_regout_0, matmult_2x2_1_regout_1, matmult_2x2_1_regout_2, matmult_2x2_1_regout_3,
       MBR_A_q, MBR_B_q, MBR_Z_q, OverFlow_Register_q, Ram_A_dout, Ram_B_dout, Reg_A0_q, Reg_A1_q, Reg_A2_q,
       Reg_A3_q, Reg_B0_q, Reg_B1_q, Reg_B2_q, Reg_B3_q, Reg_Out_q, reg_swap_1_rega0, reg_swap_1_rega1,
       reg_swap_1_rega2, reg_swap_1_rega3, RegOut_0_q, RegOut_1_q, RegOut_2_q, RegOut_3_q, System_Ram_dout,
       Temp_Reg_q, Terminal_A_q, Terminal_B_q;
  wire [31:0] Rom_A_data;
  wire [38:0] Rom_B_data;

  not not_1 (not_1_out, instruction_splitter_1_opcode[3]);
  not not_2 (not_2_out, instruction_splitter_1_opcode[2]);
  and and_1 (and_1_out, not_1_out, not_2_out, instruction_splitter_1_opcode[1], not_3_out);
  Register #(.width(1)) Debug_register (
    .D(1'b1), .en(and_1_out), .clk(controlled_buffer_11_out), .Q(Debug_register_q));  // open: clr
  Register #(.width(5)) Debug_Register_2 (
    .D(instruction_splitter_1_address_a), .en(and_1_out), .clk(controlled_buffer_11_out),
    .Q(Debug_Register_2_q));  // open: clr
  not not_3 (not_3_out, instruction_splitter_1_opcode[0]);
  Register #(.width(5)) Current_Opcode (
    .D(instruction_splitter_1_opcode), .en(Rom_A_data[14]), .clk(controlled_buffer_11_out),
    .Q({Current_Opcode_q[4], Current_Opcode_q_2}));  // open: clr
  assign controlled_buffer_1_out = Rom_B_data[6] ? controlled_buffer_26_out : 16'bz;  // Controlled_Buffer controlled_buffer_1
  assign controlled_buffer_2_out = Rom_B_data[7] ? controlled_buffer_1_out : 16'bz;  // Controlled_Buffer controlled_buffer_2
  assign controlled_buffer_3_out = Rom_B_data[8] ? controlled_buffer_2_out : 16'bz;  // Controlled_Buffer controlled_buffer_3
  assign controlled_buffer_4_out = Rom_B_data[9] ? controlled_buffer_3_out : 16'bz;  // Controlled_Buffer controlled_buffer_4
  not not_4 (not_4_out, Current_Opcode_q_2[4]);
  Register #(.width(16)) Reg_B0 (
    .D(controlled_buffer_1_out), .en(Rom_A_data[19]), .clk(controlled_buffer_11_out), .Q(Reg_B0_q));  // open: clr
  Register #(.width(16)) Reg_B2 (
    .D(controlled_buffer_3_out), .en(Rom_A_data[6]), .clk(controlled_buffer_11_out), .Q(Reg_B2_q));  // open: clr
  and and_2 (and_2_out, not_4_out, Current_Opcode_q_2[5], Current_Opcode_q_2[6], Current_Opcode_q_2[7]);
  Counter #(.max('h1f), .width(5)) ProgramCounter (
    .up(1'b1), .count(Rom_A_data[31]), .clk(controlled_buffer_11_out), .Q(ProgramCounter_q));  // open: clr, load, D, carry
  // Probe on matmult_2x2_1_regout_0
  // Probe on matmult_2x2_1_regout_2
  Reg_Swap reg_swap_1 (
    .Opcode({Current_Opcode_q[4], Current_Opcode_q_2}), .Reg_A0(Reg_A0_q), .Reg_A1(Reg_A1_q),
    .Reg_A2(Reg_A2_q), .Reg_A3(Reg_A3_q), .Reg_B0(Reg_B0_q), .Reg_B1(Reg_B1_q), .Reg_B2(Reg_B2_q),
    .Reg_B3(Reg_B3_q), .Address_1(instruction_splitter_1_address_a),
    .Address_2(instruction_splitter_1_address_b), .RegA0(reg_swap_1_rega0), .RegA1(reg_swap_1_rega1),
    .RegA2(reg_swap_1_rega2), .RegA3(reg_swap_1_rega3), .RegB0(controlled_buffer_1_out),
    .RegB1(controlled_buffer_2_out), .RegB2(controlled_buffer_3_out), .RegB3(controlled_buffer_4_out));
  ALU_16_bits alu_16_bits_1 (
    .Opcode({Current_Opcode_q[4], Current_Opcode_q_2}), .Flag(instruction_splitter_1_flag_bit),
    .Reg_A(Reg_A0_q), .Reg_B(Reg_B0_q), .Over_Flow(alu_16_bits_1_over_flow), .Reg_Out(alu_16_bits_1_reg_out));
  Register #(.width(16)) OverFlow_Register (
    .D(alu_16_bits_1_over_flow), .en(Rom_A_data[18]), .clk(controlled_buffer_11_out), .Q(OverFlow_Register_q));  // open: clr
  Register #(.width(16)) Reg_B1 (
    .D(controlled_buffer_2_out), .en(Rom_A_data[7]), .clk(controlled_buffer_11_out), .Q(Reg_B1_q));  // open: clr
  Register #(.width(16)) Reg_B3 (
    .D(controlled_buffer_4_out), .en(Rom_A_data[5]), .clk(controlled_buffer_11_out), .Q(Reg_B3_q));  // open: clr
  Matmult_2x2 matmult_2x2_1 (
    .Reg_A0(Reg_A0_q), .Reg_A1(Reg_A1_q), .Reg_A2(Reg_A2_q), .Reg_A3(Reg_A3_q), .Reg_B0(Reg_B0_q),
    .Reg_B1(Reg_B1_q), .Reg_B2(Reg_B2_q), .Reg_B3(Reg_B3_q), .RegOut_0(matmult_2x2_1_regout_0),
    .RegOut_1(matmult_2x2_1_regout_1), .RegOut_2(matmult_2x2_1_regout_2), .RegOut_3(matmult_2x2_1_regout_3));
  and and_3 (and_3_out, and_2_out, instruction_splitter_1_flag_bit);
  Register #(.width(16)) RegOut_3 (
    .D(matmult_2x2_1_regout_3), .en(Rom_B_data[34]), .clk(controlled_buffer_11_out), .Q(RegOut_3_q));  // open: clr
  // Probe on matmult_2x2_1_regout_1
  // Probe on matmult_2x2_1_regout_3
  assign reg_swap_1_rega0 = Rom_B_data[2] ? controlled_buffer_25_out : 16'bz;  // Controlled_Buffer controlled_buffer_5
  assign reg_swap_1_rega1 = Rom_B_data[3] ? reg_swap_1_rega0 : 16'bz;  // Controlled_Buffer controlled_buffer_6
  assign reg_swap_1_rega2 = Rom_B_data[4] ? reg_swap_1_rega1 : 16'bz;  // Controlled_Buffer controlled_buffer_7
  assign reg_swap_1_rega3 = Rom_B_data[5] ? reg_swap_1_rega2 : 16'bz;  // Controlled_Buffer controlled_buffer_8
  Register #(.width(16)) RegOut_2 (
    .D(matmult_2x2_1_regout_2), .en(Rom_B_data[34]), .clk(controlled_buffer_11_out), .Q(RegOut_2_q));  // open: clr
  not not_5 (not_5_out, and_3_out);
  assign controlled_buffer_9_out = Rom_B_data[33] ? ProgramCounter_q : 5'bz;  // Controlled_Buffer controlled_buffer_9
  Register #(.width(16)) Reg_A0 (
    .D(reg_swap_1_rega0), .en(Rom_A_data[20]), .clk(controlled_buffer_11_out), .Q(Reg_A0_q));  // open: clr
  Register #(.width(16)) Reg_A2 (
    .D(reg_swap_1_rega2), .en(Rom_A_data[9]), .clk(controlled_buffer_11_out), .Q(Reg_A2_q));  // open: clr
  assign controlled_buffer_10_out = instruction_splitter_1_flag_bit ? OverFlow_Register_q : 16'bz;  // Controlled_Buffer controlled_buffer_10
  Register #(.width(16)) RegOut_1 (
    .D(matmult_2x2_1_regout_1), .en(Rom_B_data[34]), .clk(controlled_buffer_11_out), .Q(RegOut_1_q));  // open: clr
  Instruction_splitter instruction_splitter_1 (
    .Instruction_Input(controlled_buffer_22_out), .WE(Rom_A_data[27]), .Clock(controlled_buffer_11_out),
    .Address_B(instruction_splitter_1_address_b), .Address_A(instruction_splitter_1_address_a),
    .OPCODE(instruction_splitter_1_opcode), .FLAG_BIT(instruction_splitter_1_flag_bit));
  Register #(.width(16)) Reg_A1 (
    .D(reg_swap_1_rega1), .en(Rom_A_data[10]), .clk(controlled_buffer_11_out), .Q(Reg_A1_q));  // open: clr
  Register #(.width(16)) Reg_A3 (
    .D(reg_swap_1_rega3), .en(Rom_A_data[8]), .clk(controlled_buffer_11_out), .Q(Reg_A3_q));  // open: clr
  Register #(.width(16)) Reg_Out (
    .D(alu_16_bits_1_reg_out), .en(Rom_A_data[18]), .clk(controlled_buffer_11_out), .Q(Reg_Out_q));  // open: clr
  Register #(.width(16)) RegOut_0 (
    .D(matmult_2x2_1_regout_0), .en(Rom_B_data[34]), .clk(controlled_buffer_11_out), .Q(RegOut_0_q));  // open: clr
  Clock Clock_Main (.out(Clock_Main_out));
  assign controlled_buffer_11_out = not_5_out ? Clock_Main_out : 1'bz;  // Controlled_Buffer controlled_buffer_11
  assign controlled_buffer_9_out = Rom_B_data[32] ? instruction_splitter_1_address_a : 5'bz;  // Controlled_Buffer controlled_buffer_12
  assign controlled_buffer_9_out = Rom_B_data[18] ? instruction_splitter_1_address_b : 5'bz;  // Controlled_Buffer controlled_buffer_13
  Register #(.width(5)) MAR_Z (
    .D(controlled_buffer_9_out), .en(Rom_A_data[30]), .clk(controlled_buffer_11_out), .Q(MAR_Z_q));  // open: clr
  assign controlled_buffer_14_out = Rom_A_data[2] ? controlled_buffer_10_out : 16'bz;  // Controlled_Buffer controlled_buffer_14
  assign controlled_buffer_10_out = not_6_out ? Reg_Out_q : 16'bz;  // Controlled_Buffer controlled_buffer_15
  not not_6 (not_6_out, instruction_splitter_1_flag_bit);
  Register #(.width(5)) MAR_A (
    .D(instruction_splitter_1_address_a), .en(Rom_A_data[26]), .clk(controlled_buffer_11_out), .Q(MAR_A_q));  // open: clr
  Register #(.width(16)) MBR_Z (
    .D(controlled_buffer_14_out), .en(Rom_A_data[28]), .clk(controlled_buffer_11_out), .Q(MBR_Z_q));  // open: clr
  assign controlled_buffer_14_out = Rom_A_data[1] ? Instruction_Ram_dout : 16'bz;  // Controlled_Buffer controlled_buffer_16
  assign controlled_buffer_14_out = Rom_B_data[14] ? System_Ram_dout : 16'bz;  // Controlled_Buffer controlled_buffer_17
  assign controlled_buffer_14_out = Rom_B_data[29] ? RegOut_0_q : 16'bz;  // Controlled_Buffer controlled_buffer_18
  Register #(.width(5)) MAR_B (
    .D(instruction_splitter_1_address_b), .en(Rom_A_data[25]), .clk(controlled_buffer_11_out), .Q(MAR_B_q));  // open: clr
  assign controlled_buffer_14_out = Rom_B_data[28] ? RegOut_1_q : 16'bz;  // Controlled_Buffer controlled_buffer_19
  assign controlled_buffer_14_out = Rom_B_data[27] ? RegOut_2_q : 16'bz;  // Controlled_Buffer controlled_buffer_20
  assign controlled_buffer_14_out = Rom_B_data[26] ? RegOut_3_q : 16'bz;  // Controlled_Buffer controlled_buffer_21
  assign controlled_buffer_22_out = Rom_A_data[13] ? MBR_Z_q : 16'bz;  // Controlled_Buffer controlled_buffer_22
  assign controlled_buffer_23_out = Rom_B_data[10] ? controlled_buffer_24_out : 16'bz;  // Controlled_Buffer controlled_buffer_23
  Register #(.width(16)) MBR_A (
    .D(controlled_buffer_24_out), .en(Rom_A_data[22]), .clk(controlled_buffer_11_out), .Q(MBR_A_q));  // open: clr
  Mover_Decoder mover_decoder_1 (
    .OE(Rom_B_data[11]), .Opcode(instruction_splitter_1_opcode), .Flag(instruction_splitter_1_flag_bit),
    .B(mover_decoder_1_b), .A(mover_decoder_1_a));
  Register #(.width(16)) MBR_B (
    .D(controlled_buffer_23_out), .en(Rom_A_data[21]), .clk(controlled_buffer_11_out), .Q(MBR_B_q));  // open: clr
  Register #(.width(16)) Temp_Reg (
    .D(controlled_buffer_22_out), .en(Rom_B_data[13]), .clk(controlled_buffer_11_out), .Q(Temp_Reg_q));  // open: clr
  assign controlled_buffer_24_out = Rom_B_data[12] ? Temp_Reg_q : 16'bz;  // Controlled_Buffer controlled_buffer_24
  assign controlled_buffer_25_out = Rom_A_data[12] ? MBR_A_q : 16'bz;  // Controlled_Buffer controlled_buffer_25
  assign controlled_buffer_26_out = Rom_A_data[11] ? MBR_B_q : 16'bz;  // Controlled_Buffer controlled_buffer_26
  assign controlled_buffer_27_out = Rom_B_data[16] ? Counter_A_q : 5'bz;  // Controlled_Buffer controlled_buffer_27
  Counter #(.max('h1f), .width(5)) Counter_A (
    .load(Rom_B_data[38]), .D(MAR_A_q), .count(Rom_B_data[36]), .Q(Counter_A_q), .up(1'b1),
    .clk(controlled_buffer_11_out));  // open: carry, clr
  assign controlled_buffer_27_out = mover_decoder_2_a ? MAR_A_q : 5'bz;  // Controlled_Buffer controlled_buffer_28
  not not_7 (not_7_out, Rom_B_data[11]);
  RAM #(.addrWidth(5), .dataWidth(16), .\type ("nonvolatile")) Instruction_Ram (
    .addr(MAR_Z_q), .we(Rom_A_data[17]), .oe(Rom_A_data[29]), .clk(controlled_buffer_11_out),
    .dout(Instruction_Ram_dout));  // open: din
  // Probe on controlled_buffer_25_out
  RAM #(.addrWidth(5), .dataWidth(16), .\type ("nonvolatile")) Ram_A (
    .addr(controlled_buffer_27_out), .we(controlled_buffer_29_out), .oe(Rom_A_data[24]),
    .clk(controlled_buffer_11_out), .din(controlled_buffer_25_out), .dout(Ram_A_dout));
  assign controlled_buffer_29_out = mover_decoder_1_a ? Rom_B_data[11] : 1'bz;  // Controlled_Buffer controlled_buffer_29
  assign controlled_buffer_29_out = not_7_out ? Rom_A_data[16] : 1'bz;  // Controlled_Buffer controlled_buffer_30
  Register #(.width(16)) Terminal_A (
    .D(controlled_buffer_25_out), .en(Rom_B_data[21]), .clk(controlled_buffer_11_out), .Q(Terminal_A_q));  // open: clr
  Register #(.width(16)) Terminal_B (
    .D(controlled_buffer_26_out), .en(Rom_B_data[22]), .clk(controlled_buffer_11_out), .Q(Terminal_B_q));  // open: clr
  assign controlled_buffer_23_out = bus_terminus_1_ram_b ? Terminal_A_q : 16'bz;  // Controlled_Buffer controlled_buffer_31
  Bus_Terminus bus_terminus_1 (
    .OE(Rom_B_data[23]), .Input_01(Rom_B_data[24]), .Input_02(Rom_B_data[25]), .Ram_A(bus_terminus_1_ram_a),
    .Ram_B(bus_terminus_1_ram_b));  // open: System_Ram
  // Probe on Instruction_Ram_dout
  assign controlled_buffer_24_out = Rom_B_data[20] ? Ram_A_dout : 16'bz;  // Controlled_Buffer controlled_buffer_32
  assign controlled_buffer_24_out = bus_terminus_1_ram_a ? Terminal_B_q : 16'bz;  // Controlled_Buffer controlled_buffer_33
  Counter #(.max('h1f), .width(5)) Counter_C (
    .load(Rom_B_data[31]), .D(MAR_Z_q), .count(Rom_B_data[30]), .Q(Counter_C_q), .up(1'b1),
    .clk(controlled_buffer_11_out));  // open: carry, clr
  Mover_Decoder mover_decoder_2 (
    .OE(Rom_B_data[17]), .Opcode(instruction_splitter_1_opcode), .Flag(instruction_splitter_1_flag_bit),
    .B(mover_decoder_2_b), .A(mover_decoder_2_a));
  assign controlled_buffer_34_out = Rom_B_data[15] ? Counter_B_q : 5'bz;  // Controlled_Buffer controlled_buffer_34
  Counter #(.max('h1f), .width(5)) Counter_B (
    .load(Rom_B_data[37]), .D(MAR_B_q), .count(Rom_B_data[35]), .Q(Counter_B_q), .up(1'b1),
    .clk(controlled_buffer_11_out));  // open: carry, clr
  // Probe on controlled_buffer_26_out
  assign controlled_buffer_35_out = mover_decoder_1_b ? Rom_B_data[11] : 1'bz;  // Controlled_Buffer controlled_buffer_35
  assign controlled_buffer_36_out = not_8_out ? {5{1'b0}} : 5'bz;  // Controlled_Buffer controlled_buffer_36
  not not_8 (not_8_out, Debug_register_q);
  assign controlled_buffer_34_out = mover_decoder_2_b ? MAR_A_q : 5'bz;  // Controlled_Buffer controlled_buffer_37
  RAM #(.addrWidth(5), .dataWidth(16), .\type ("nonvolatile")) Ram_B (
    .addr(controlled_buffer_34_out), .we(controlled_buffer_35_out), .oe(Rom_A_data[23]),
    .clk(controlled_buffer_11_out), .din(controlled_buffer_26_out), .dout(Ram_B_dout));
  assign controlled_buffer_35_out = not_7_out ? Rom_A_data[15] : 1'bz;  // Controlled_Buffer controlled_buffer_38
  assign controlled_buffer_36_out = Debug_register_q ? Debug_Register_2_q : 5'bz;  // Controlled_Buffer controlled_buffer_39
  RAM #(.addrWidth(5), .dataWidth(16)) System_Ram (
    .addr(Counter_C_q), .we(Rom_A_data[3]), .oe(Rom_A_data[4]), .clk(controlled_buffer_11_out),
    .din(controlled_buffer_22_out), .dout(System_Ram_dout));
  assign controlled_buffer_40_out = Debug_Counter_carry ? 1'b1 : 1'bz;  // Controlled_Buffer controlled_buffer_40
  Counter #(.max('h1f), .width(5)) Debug_Counter (
    .load(controlled_buffer_40_out), .up(1'b0), .count(1'b1), .clk(controlled_buffer_11_out),
    .D(controlled_buffer_36_out), .carry(Debug_Counter_carry));  // open: clr, Q
  assign controlled_buffer_23_out = Rom_B_data[19] ? Ram_B_dout : 16'bz;  // Controlled_Buffer controlled_buffer_41
  Counter #(.max('hf), .width(4)) Step_Counter (
    .clr(Rom_A_data[0]), .up(Debug_Counter_carry), .count(Debug_Counter_carry),
    .clk(controlled_buffer_11_out), .Q(Step_Counter_q));  // open: load, D, carry
  // Probe on in_6
  // Probe on in_7
  Register #(.width(16)) register_1 (
    .D(Instruction_Input), .en(WE), .clk(in_10), .Q({FLAG_BIT, OPCODE, Address_A, Address_B}));  // open: clr
  ROM #(.dataWidth(39)) Rom_B (.addr({Current_Opcode_q_2, Step_Counter_q}), .data(Rom_B_data));
  ROM #(.dataWidth(32)) Rom_A (.addr({Current_Opcode_q_2, Step_Counter_q}), .data(Rom_A_data));
  // Probe on Rom_A_data

  assign out_11 = in_1;
  assign out_12 = in_2;
  assign out_13 = in_3;
  assign out_14 = in_4;
  assign out_15 = in_5;
  assign out_16 = in_6;
  assign out_17 = in_7;

  // Notes on the sheet:
  //   Bank B 
  //   MatMult Result
  //   Bank A
  //   Address 
  //   Decoder
  //   Input_02
  //   Input_01
  //   Ram_B_CB
  //   Reg_B3_CB
  //   Reg_B1_CB
  //   Reg_A2_CB
  //   Reg_A1_CB
  //   Reg_A0_CB
  //   MAR_Z_WE
  //   Instruction_Ram_OE
  //   MBR_Z_WE
  //   Instruction_Splitter_WE
  //   MAR_A_WE
  //   MAR_B_WE
  //   RAM_A_OE
  //   Ram_B_OE
  //   MBR_A_WE
  //   MBR_B_WE
  //   Reg_A0_WE
  //   Reg_B0_WE
  //   Reg_Out_WE
  //   Instrction_Ram_WE
  //   Ram_A_WE
  //   Ram_B_WE
  //   OPCODE_WE
  //   MBR_Z_OE
  //   MBR_A_OE
  //   MBR_B_OE
  //   Reg_A1_WE
  //   Reg_A2_WE
  //   Reg_A3_WE
  //   Reg_B1_WE
  //   Reg_B2_WE
  //   Reg_B3_WE
  //   System_Ram_OE
  //   System_Ram_WE
  //   RegOut_OE
  //   Clock_Reset
  //   Counter _A_WE
  //   Counter_B_WE
  //   RegOut_0_1_2_3_WE
  //   Program_Counter_CB
  //   Address_A_CB
  //   Counter_C_WE
  //   Counter_C_enable
  //   RegOut_0_CB
  //   RegOut_1_CB
  //   RegOut_2_CB
  //   RegOut_3_CB
  //   Bus_Terminus_OE
  //   Terminal_B_WE
  //   Terminal_A_WE
  //   Ram_A_CB
  //   Address B CB
  //   Address Decoder OE
  //   Counter A OE
  //   Counter B OE
  //   System Ram To MBR_CB
  //   Temp_Reg_WE
  //   Temp_REg_OE
  //   Data_Decoder_OE
  //   Connection Buffer MBRs
  //   Reg_B2_CB
  //   Reg_B0_CB
  //   Reg_A3_CB
  //   Program_Counter_Increament_By_One
  //   Instruction_Ram_to_MBR_CB
  //   Counter_A_Increament_By_One
  //   Counter_B_Increament_By_One
  //   Opcode
  //   Step Counter
  //   contents of Rom_B (hex, n*v repeats v):
  //   200000000 0 0 100000000 6000000000 18000 180000 44 200000000 7*0 200000000 0 0 100000000 6000000000
  //   18000 180000 44 200000000 7*0 200000000 0 0 100000000 2000000 11*0 200000000 0 0 100000000
  //   6000000000 18000 180000 44 200000000 7*0 200000000 0 0 100000000 80000000 200000000 10*0 200000000 0
  //   0 100000000 6000000000 18000 180000 600000 2800000 1800000 200018000 5*0 200000000 0 0 100000000
  //   200000000 11*0 200000000 0 0 100000000 6000000000 1800018000 1800198000 1800198044 1980cc 1801dc
  //   2000003fc 5*0 200000000 0 0 100000000 a0000000 50000000 48000000 44000000 200000000 7*0 200000000 0
  //   0 100000000 600000000 11*0 200000000 0 0 100000000 6000000000 18000 180000 44 200000000 7*0
  //   200000000 0 0 100000000 6000000000 18000 180000 44 200000000 7*0 200000000 0 0 100000000 6000000000
  //   18000 180000 44 200000000 7*0 200000000 0 0 100000000 6000000000 18000 180000 44 200000000 7*0
  //   200000000 0 0 100000000 200000000 0 0 440000000 8*0 200000000 0 0 100000000 40000 80000000 0 4000
  //   2000 1400 200020800
  //   contents of Rom_A (hex, n*v repeats v):
  //   e0000000 10002002 8002000 46004000 0 1800000 600000 181800 40040000 1 6*0 e0000000 10002002 8002000
  //   46004000 0 1800000 600000 181800 40040000 1 6*0 e0000000 10002002 8002000 46004000 4000000 1 10*0
  //   e0000000 10002002 8002000 46004000 0 1800000 600000 181800 40040000 1 6*0 e0000000 10002002 8002000
  //   46004000 10000004 40002008 1 9*0 e0000000 10002002 8002000 46004000 0 1800000 600000 1800 400000
  //   200000 40019800 1 4*0 e0000000 10002002 8002000 46004000 401807e0 1 10*0 e0000000 10002002 8002000
  //   46004000 0 1800000 1e00000 1f81800 1e01c80 601a40 40001920 1 4*0 e0000000 10002002 8002000 46004000
  //   10000000 10002008 10002008 10002008 40002008 1 6*0 e0000000 10002002 8002000 46004000 40000000 1
  //   10*0 e0000000 10002002 8002000 46004000 0 1800000 600000 181800 40040000 1 6*0 e0000000 10002002
  //   8002000 46004000 0 1800000 600000 181800 40040000 1 6*0 e0000000 10002002 8002000 46004000 0 1800000
  //   600000 181800 40040000 1 6*0 e0000000 10002002 8002000 46004000 0 1800000 600000 181800 40040000 1
  //   6*0 e0000000 10002002 8002000 46004000 40000000 1 10*0 e0000000 10002002 8002000 46004000 40000000 0
  //   10 10000000 2000 600000 40001800 1
  //   1- 0001 Sub
  //   0000 Reserved
  //   0001 Add
  //   0011 Mult
  //   0010 Debug 
  //   0100 Store
  //   1001 MatMult 
  //   1011 And
  //   1101 Not(A)
  //   1100 Xor
  //   1110 Nop
  //   1- 1110 Halt 
  //   1- 0100 Store Overflow
  //   0101 Mem Swap
  //   0110 Reg Swap
  //   0111 Block Load
  //   1000 Block Store
  //   1010 Compare
  //   1111 Move to ram A 
  //   1- 1111 Move to ram B 
endmodule

module Manual (
  input  [7:0] in_1,
  input  [7:0] in_2,
  input  [4:0] in_3,
  input  [4:0] in_4,
  input  [15:0] in_5,
  input  [15:0] in_6,
  input  in_7,
  input  [15:0] Instruction_Input,
  input  in_9,
  input  WE,
  input  in_11,
  input  in_12,
  input  in_13,
  input  in_14,
  input  in_15,
  input  in_16,
  input  in_17,
  input  Instruction_Decoder_OE,
  input  in_19,
  input  in_20,
  input  in_21,
  input  in_22,
  input  in_23,
  input  in_24,
  input  in_25,
  input  [4:0] in_26,
  input  in_27,
  input  in_28,
  input  in_29,
  input  in_30,
  input  in_31,
  input  in_32,
  input  in_33,
  input  in_34,
  input  in_35,
  input  in_36,
  input  in_37,
  input  in_38,
  input  in_39,
  input  Ram_WE,
  input  in_41,
  input  in_42,
  output [7:0] out_43,
  output [7:0] out_44,
  output [4:0] out_45,
  output [4:0] out_46,
  output [15:0] out_47,
  output [15:0] out_48,
  output [4:0] Address_B,
  output [4:0] Address_A,
  output [4:0] OPCODE,
  output FLAG_BIT
);

  wire and_1_out, and_2_out, bus_terminus_1_ram_a, bus_terminus_1_ram_b, Clock_Main_out,
       controlled_buffer_3_out, controlled_buffer_19_out, controlled_buffer_26_out, controlled_buffer_30_out,
       counter_1_carry, instruction_splitter_1_flag_bit, mover_decoder_1_a, mover_decoder_1_b,
       mover_decoder_2_a, mover_decoder_2_b, not_1_out, not_2_out, not_3_out, not_4_out, not_5_out, not_6_out;
  wire [3:0] Step_Counter_q;
  wire [4:0] controlled_buffer_1_out, controlled_buffer_17_out, controlled_buffer_21_out,
       controlled_buffer_29_out, Counter_A_q, Counter_B_q, Counter_C_q, instruction_splitter_1_address_a,
       instruction_splitter_1_address_b, instruction_splitter_1_opcode, MAR_A_q, MAR_B_q, MAR_Z_q,
       ProgramCounter_q;
  wire [4:4] Current_Opcode_q;
  wire [7:4] Current_Opcode_q_2;
  wire [15:0] alu_16_bits_1_over_flow, alu_16_bits_1_reg_out, controlled_buffer_2_out,
       controlled_buffer_6_out, controlled_buffer_13_out, controlled_buffer_14_out, controlled_buffer_15_out,
       controlled_buffer_16_out, Instruction_Ram_dout, matmult_2x2_1_regout_0, matmult_2x2_1_regout_1,
       matmult_2x2_1_regout_2, matmult_2x2_1_regout_3, MBR_A_q, MBR_B_q, MBR_Z_q, OverFlow_Register_q,
       Ram_A_dout, Ram_B_dout, Reg_A0_q, Reg_A1_q, Reg_A2_q, Reg_A3_q, Reg_B0_q, Reg_B1_q, Reg_B2_q,
       Reg_B3_q, Reg_Out_q, register_1_q, RegOut_0_q, RegOut_1_q, RegOut_2_q, RegOut_3_q, Terminal_A_q,
       Terminal_B_q;
  wire [27:12] undriven;
  wire [31:0] undriven_2;

  Register #(.width(5)) Current_Opcode (
    .D(instruction_splitter_1_address_a), .en(in_24), .clk(controlled_buffer_3_out),
    .Q({Current_Opcode_q[4], Current_Opcode_q_2}));  // open: clr
  Register #(.width(16)) Reg_B0 (
    .D(controlled_buffer_16_out), .en(undriven_2[19]), .clk(controlled_buffer_3_out), .Q(Reg_B0_q));  // open: clr
  not not_1 (not_1_out, Current_Opcode_q_2[4]);
  // Probe on Reg_B0_q
  // Probe on alu_16_bits_1_over_flow
  Register #(.width(16)) Reg_B2 (
    .D(controlled_buffer_16_out), .en(undriven_2[6]), .clk(controlled_buffer_3_out), .Q(Reg_B2_q));  // open: clr
  // Probe on matmult_2x2_1_regout_0
  // Probe on matmult_2x2_1_regout_2
  and and_1 (and_1_out, not_1_out, Current_Opcode_q_2[5], Current_Opcode_q_2[6], Current_Opcode_q_2[7]);
  Counter #(.max('h1f), .width(5)) ProgramCounter (
    .up(1'b1), .count(in_11), .clk(controlled_buffer_3_out), .Q(ProgramCounter_q));  // open: clr, load, D, carry
  // Probe on Reg_A0_q
  Register #(.width(16)) Reg_B1 (
    .D(controlled_buffer_16_out), .en(undriven_2[7]), .clk(controlled_buffer_3_out), .Q(Reg_B1_q));  // open: clr
  Register #(.width(16)) Reg_B3 (
    .D(controlled_buffer_16_out), .en(undriven_2[5]), .clk(controlled_buffer_3_out), .Q(Reg_B3_q));  // open: clr
  ALU_16_bits alu_16_bits_1 (
    .Opcode({Current_Opcode_q[4], Current_Opcode_q_2}), .Flag(instruction_splitter_1_flag_bit),
    .Reg_A(Reg_A0_q), .Reg_B(Reg_B0_q), .Over_Flow(alu_16_bits_1_over_flow), .Reg_Out(alu_16_bits_1_reg_out));
  Register #(.width(16)) OverFlow_Register (
    .D(alu_16_bits_1_over_flow), .en(undriven_2[18]), .clk(controlled_buffer_3_out), .Q(OverFlow_Register_q));  // open: clr
  Matmult_2x2 matmult_2x2_1 (
    .Reg_A0(Reg_A0_q), .Reg_A1(Reg_A1_q), .Reg_A2(Reg_A2_q), .Reg_A3(Reg_A3_q), .Reg_B0(Reg_B0_q),
    .Reg_B1(Reg_B1_q), .Reg_B2(Reg_B2_q), .Reg_B3(Reg_B3_q), .RegOut_0(matmult_2x2_1_regout_0),
    .RegOut_1(matmult_2x2_1_regout_1), .RegOut_2(matmult_2x2_1_regout_2), .RegOut_3(matmult_2x2_1_regout_3));
  // Probe on matmult_2x2_1_regout_1
  // Probe on matmult_2x2_1_regout_3
  and and_2 (and_2_out, and_1_out, instruction_splitter_1_flag_bit);
  // Probe on alu_16_bits_1_reg_out
  Register #(.width(16)) RegOut_3 (
    .D(matmult_2x2_1_regout_3), .en(undriven[27]), .clk(controlled_buffer_3_out), .Q(RegOut_3_q));  // open: clr
  Register #(.width(16)) RegOut_2 (
    .D(matmult_2x2_1_regout_2), .en(undriven[27]), .clk(controlled_buffer_3_out), .Q(RegOut_2_q));  // open: clr
  not not_2 (not_2_out, and_2_out);
  assign controlled_buffer_1_out = in_15 ? ProgramCounter_q : 5'bz;  // Controlled_Buffer controlled_buffer_1
  Register #(.width(16)) Reg_A0 (
    .D(controlled_buffer_15_out), .clk(controlled_buffer_3_out), .Q(Reg_A0_q));  // open: en, clr
  Register #(.width(16)) Reg_A2 (
    .D(controlled_buffer_15_out), .en(undriven_2[9]), .clk(controlled_buffer_3_out), .Q(Reg_A2_q));  // open: clr
  assign controlled_buffer_2_out = instruction_splitter_1_flag_bit ? OverFlow_Register_q : 16'bz;  // Controlled_Buffer controlled_buffer_2
  Register #(.width(16)) RegOut_1 (
    .D(matmult_2x2_1_regout_1), .en(undriven[27]), .clk(controlled_buffer_3_out), .Q(RegOut_1_q));  // open: clr
  Instruction_splitter instruction_splitter_1 (
    .Instruction_Input(controlled_buffer_13_out), .WE(in_27), .Clock(controlled_buffer_3_out),
    .Address_B(instruction_splitter_1_address_b), .Address_A(instruction_splitter_1_address_a),
    .OPCODE(instruction_splitter_1_opcode), .FLAG_BIT(instruction_splitter_1_flag_bit));
  Register #(.width(16)) Reg_A1 (
    .D(controlled_buffer_15_out), .en(undriven_2[10]), .clk(controlled_buffer_3_out), .Q(Reg_A1_q));  // open: clr
  Register #(.width(16)) Reg_A3 (
    .D(controlled_buffer_15_out), .en(undriven_2[8]), .clk(controlled_buffer_3_out), .Q(Reg_A3_q));  // open: clr
  Register #(.width(16)) Reg_Out (
    .D(alu_16_bits_1_reg_out), .en(undriven_2[18]), .clk(controlled_buffer_3_out), .Q(Reg_Out_q));  // open: clr
  // Probe on Reg_Out_q
  Register #(.width(16)) RegOut_0 (
    .D(matmult_2x2_1_regout_0), .en(undriven[27]), .clk(controlled_buffer_3_out), .Q(RegOut_0_q));  // open: clr
  Clock Clock_Main (.out(Clock_Main_out));
  assign controlled_buffer_3_out = not_2_out ? Clock_Main_out : 1'bz;  // Controlled_Buffer controlled_buffer_3
  assign controlled_buffer_1_out = in_17 ? instruction_splitter_1_address_a : 5'bz;  // Controlled_Buffer controlled_buffer_4
  Register #(.width(5)) MAR_Z (
    .D(controlled_buffer_1_out), .en(in_13), .clk(controlled_buffer_3_out), .Q(MAR_Z_q));  // open: clr
  assign controlled_buffer_1_out = in_21 ? instruction_splitter_1_address_b : 5'bz;  // Controlled_Buffer controlled_buffer_5
  assign controlled_buffer_6_out = undriven_2[2] ? controlled_buffer_2_out : 16'bz;  // Controlled_Buffer controlled_buffer_6
  assign controlled_buffer_2_out = not_3_out ? Reg_Out_q : 16'bz;  // Controlled_Buffer controlled_buffer_7
  not not_3 (not_3_out, instruction_splitter_1_flag_bit);
  Register #(.width(5)) MAR_A (
    .D(instruction_splitter_1_address_a), .en(in_20), .clk(controlled_buffer_3_out), .Q(MAR_A_q));  // open: clr
  assign controlled_buffer_6_out = in_32 ? Instruction_Ram_dout : 16'bz;  // Controlled_Buffer controlled_buffer_8
  Register #(.width(16)) MBR_Z (
    .D(controlled_buffer_6_out), .en(in_25), .clk(controlled_buffer_3_out), .Q(MBR_Z_q));  // open: clr
  assign controlled_buffer_6_out = undriven[22] ? RegOut_0_q : 16'bz;  // Controlled_Buffer controlled_buffer_9
  Register #(.width(5)) MAR_B (
    .D(instruction_splitter_1_address_b), .en(in_22), .clk(controlled_buffer_3_out), .Q(MAR_B_q));  // open: clr
  assign controlled_buffer_6_out = undriven[21] ? RegOut_1_q : 16'bz;  // Controlled_Buffer controlled_buffer_10
  assign controlled_buffer_6_out = undriven[20] ? RegOut_2_q : 16'bz;  // Controlled_Buffer controlled_buffer_11
  assign controlled_buffer_6_out = undriven[19] ? RegOut_3_q : 16'bz;  // Controlled_Buffer controlled_buffer_12
  assign controlled_buffer_13_out = in_31 ? MBR_Z_q : 16'bz;  // Controlled_Buffer controlled_buffer_13
  // Probe on MAR_A_q
  Register #(.width(16)) MBR_A (
    .D(controlled_buffer_14_out), .en(in_36), .clk(controlled_buffer_3_out), .Q(MBR_A_q));  // open: clr
  Register #(.width(16)) register_1 (
    .D(controlled_buffer_13_out), .en(in_23), .clk(controlled_buffer_3_out), .Q(register_1_q));  // open: clr
  Register #(.width(16)) MBR_B (
    .D(controlled_buffer_14_out), .en(in_38), .clk(controlled_buffer_3_out), .Q(MBR_B_q));  // open: clr
  Mover_Decoder mover_decoder_1 (
    .OE(Instruction_Decoder_OE), .Opcode(instruction_splitter_1_opcode),
    .Flag(instruction_splitter_1_flag_bit), .B(mover_decoder_1_b), .A(mover_decoder_1_a));
  Controlled_Buffer #(.width(16)) controlled_buffer_14 (.in(register_1_q), .out(controlled_buffer_14_out));  // open: en
  assign controlled_buffer_15_out = in_35 ? MBR_A_q : 16'bz;  // Controlled_Buffer controlled_buffer_15
  assign controlled_buffer_16_out = in_39 ? MBR_B_q : 16'bz;  // Controlled_Buffer controlled_buffer_16
  assign controlled_buffer_17_out = mover_decoder_1_a ? MAR_A_q : 5'bz;  // Controlled_Buffer controlled_buffer_17
  Counter #(.max('h1f), .width(5)) Counter_A (
    .load(in_28), .D(MAR_A_q), .count(in_33), .Q(Counter_A_q), .up(1'b1), .clk(controlled_buffer_3_out));  // open: carry, clr
  Controlled_Buffer #(.width(5)) controlled_buffer_18 (.in(Counter_A_q), .out(controlled_buffer_17_out));  // open: en
  Mover_Decoder mover_decoder_2 (
    .OE(in_37), .Opcode(instruction_splitter_1_opcode), .Flag(instruction_splitter_1_flag_bit),
    .B(mover_decoder_2_b), .A(mover_decoder_2_a));
  RAM #(.addrWidth(5), .dataWidth(16), .\type ("nonvolatile")) Instruction_Ram (
    .addr(MAR_Z_q), .we(in_14), .oe(in_16), .clk(controlled_buffer_3_out), .dout(Instruction_Ram_dout));  // open: din
  RAM #(.addrWidth(5), .dataWidth(16), .\type ("nonvolatile")) Ram_A (
    .addr(controlled_buffer_17_out), .we(controlled_buffer_19_out), .clk(controlled_buffer_3_out),
    .din(controlled_buffer_15_out), .dout(Ram_A_dout));  // open: oe
  assign controlled_buffer_19_out = mover_decoder_2_a ? in_37 : 1'bz;  // Controlled_Buffer controlled_buffer_19
  not not_4 (not_4_out, in_37);
  assign controlled_buffer_19_out = not_4_out ? Ram_WE : 1'bz;  // Controlled_Buffer controlled_buffer_20
  Register #(.width(16)) Terminal_A (
    .D(controlled_buffer_15_out), .en(undriven[14]), .clk(controlled_buffer_3_out), .Q(Terminal_A_q));  // open: clr
  Register #(.width(16)) Terminal_B (
    .D(controlled_buffer_16_out), .en(undriven[15]), .clk(controlled_buffer_3_out), .Q(Terminal_B_q));  // open: clr
  assign controlled_buffer_21_out = mover_decoder_1_b ? MAR_A_q : 5'bz;  // Controlled_Buffer controlled_buffer_21
  assign controlled_buffer_14_out = bus_terminus_1_ram_b ? Terminal_A_q : 16'bz;  // Controlled_Buffer controlled_buffer_22
  Bus_Terminus bus_terminus_1 (
    .OE(undriven[16]), .Input_01(undriven[17]), .Input_02(undriven[18]), .Ram_A(bus_terminus_1_ram_a),
    .Ram_B(bus_terminus_1_ram_b));  // open: System_Ram
  // Probe on Instruction_Ram_dout
  assign controlled_buffer_14_out = undriven[13] ? Ram_A_dout : 16'bz;  // Controlled_Buffer controlled_buffer_23
  assign controlled_buffer_14_out = bus_terminus_1_ram_a ? Terminal_B_q : 16'bz;  // Controlled_Buffer controlled_buffer_24
  Counter #(.max('h1f), .width(5)) Counter_C (
    .load(in_7), .D(MAR_Z_q), .count(in_19), .Q(Counter_C_q), .up(1'b1), .clk(controlled_buffer_3_out));  // open: carry, clr
  assign controlled_buffer_21_out = in_29 ? Counter_B_q : 5'bz;  // Controlled_Buffer controlled_buffer_25
  Counter #(.max('h1f), .width(5)) Counter_B (
    .load(in_30), .D(MAR_B_q), .count(in_34), .Q(Counter_B_q), .up(1'b1), .clk(controlled_buffer_3_out));  // open: carry, clr
  assign controlled_buffer_26_out = mover_decoder_2_b ? in_37 : 1'bz;  // Controlled_Buffer controlled_buffer_26
  assign controlled_buffer_26_out = not_5_out ? in_41 : 1'bz;  // Controlled_Buffer controlled_buffer_27
  not not_5 (not_5_out, in_37);
  RAM #(.addrWidth(5), .dataWidth(16), .\type ("nonvolatile")) Ram_B (
    .addr(controlled_buffer_21_out), .we(controlled_buffer_26_out), .clk(controlled_buffer_3_out),
    .din(controlled_buffer_16_out), .dout(Ram_B_dout));  // open: oe
  RAM #(.addrWidth(5), .dataWidth(16)) System_Ram (
    .addr(Counter_C_q), .we(undriven_2[3]), .oe(in_9), .clk(controlled_buffer_3_out),
    .din(controlled_buffer_13_out), .dout(controlled_buffer_6_out));
  assign controlled_buffer_14_out = undriven[12] ? Ram_B_dout : 16'bz;  // Controlled_Buffer controlled_buffer_28
  Counter #(.max('hf), .width(4)) Step_Counter (
    .clr(undriven_2[0]), .up(counter_1_carry), .count(counter_1_carry), .clk(controlled_buffer_3_out),
    .Q(Step_Counter_q));  // open: load, D, carry
  // Probe on in_5
  // Probe on in_6
  Register #(.width(16)) register_2 (
    .D(Instruction_Input), .en(WE), .clk(in_12), .Q({FLAG_BIT, OPCODE, Address_A, Address_B}));  // open: clr
  ROM #(.dataWidth(32)) Rom_B (.addr({Current_Opcode_q_2, Step_Counter_q}));  // open: data
  ROM #(.dataWidth(32)) Rom_A (.addr({Current_Opcode_q_2, Step_Counter_q}));  // open: data
  // Probe on {undriven_2[31:2], in_32, undriven_2[0]}
  assign controlled_buffer_29_out = not_6_out ? {5{1'b0}} : 5'bz;  // Controlled_Buffer controlled_buffer_29
  assign controlled_buffer_30_out = counter_1_carry ? 1'b1 : 1'bz;  // Controlled_Buffer controlled_buffer_30
  assign controlled_buffer_29_out = in_42 ? in_26 : 5'bz;  // Controlled_Buffer controlled_buffer_31
  Counter #(.max('h1f), .width(5)) counter_1 (
    .load(controlled_buffer_30_out), .up(1'b0), .count(1'b1), .clk(controlled_buffer_3_out),
    .D(controlled_buffer_29_out), .carry(counter_1_carry));  // open: clr, Q
  not not_6 (not_6_out, in_42);
  // AND_Gate and_3 has open pins: in0=Current_Opcode_q_2[4], in1=Current_Opcode_q_2[5], in2=Current_Opcode_q_2[6], in3=Current_Opcode_q_2[7], out=open

  assign out_43 = in_1;
  assign out_44 = in_2;
  assign out_45 = in_3;
  assign out_46 = in_4;
  assign out_47 = in_5;
  assign out_48 = in_6;

  // Notes on the sheet:
  //   MatMult Result
  //   Bank B 
  //   Bank A
  //   Input_02
  //   Input_01
  //   Ram_A_CB
  //   Ram_B_CB
  //   MAR_Z_WE
  //   Instruction_Ram_OE
  //   MBR_Z_WE
  //   Instruction_Splitter_WE
  //   MAR_A_WE
  //   MAR_B_WE
  //   RAM_A_OE
  //   Ram_B_OE
  //   MBR_A_WE
  //   MBR_B_WE
  //   Reg_A0_WE
  //   Reg_B0_WE
  //   Reg_Out_WE
  //   Instrction_Ram_WE
  //   Ram_A_WE
  //   Ram_B_WE
  //   OPCODE_WE
  //   MBR_Z_OE
  //   MBR_A_OE
  //   MBR_B_OE
  //   Reg_A1_WE
  //   Reg_A2_WE
  //   Reg_A3_WE
  //   Reg_B1_WE
  //   Reg_B2_WE
  //   Reg_B3_WE
  //   System_Ram_OE
  //   System_Ram_WE
  //   RegOut_OE
  //   Clock_Reset
  //   Counter _A_WE
  //   Counter_B_WE
  //   RegOut_0_1_2_3_WE
  //   Program_Counter_CB
  //   Address_A_CB
  //   Counter_C_WE
  //   Counter_C_enable
  //   RegOut_0_CB
  //   RegOut_1_CB
  //   RegOut_2_CB
  //   RegOut_3_CB
  //   Bus_Terminus_OE
  //   Terminal_B_WE
  //   Terminal_A_WE
  //   Program_Counter_Increament_By_One
  //   Instruction_Ram_to_MBR_CB
  //   Counter_A_Increament_By_One
  //   Counter_B_Increament_By_One
  //   Opcode
  //   Step Counter
  //   contents of Rom_B (hex, n*v repeats v):
  //   4000000 0 0 2000000 c0000000 0 3000 0 4000000 7*0 4000000 0 0 2000000 c0000000 0 3000 0 4000000 7*0
  //   4000000 0 0 2000000 c0000000 0 0 0 4000000 7*0 4000000 0 0 2000000 c0000000 0 3000 0 4000000 7*0
  //   4000000 0 0 2000000 1000000 4000000 10*0 4000000 0 0 2000000 c0000000 0 3000 c000 50000 30000
  //   4000000 5*0 4000000 0 0 2000000 c0000000 0 0 0 4000000 7*0 4000000 0 0 2000000 c0000000 30000000
  //   30003000 30003000 3000 3000 4000000 5*0 4000000 0 0 2000000 1400000 a00000 900000 880000 4000000 7*0
  //   4000000 0 0 2000000 c0000000 30000000 30003000 30003000 3000 3000 0 c000000 4*0 4000000 0 0 2000000
  //   c0000000 0 3000 0 4000000 7*0 4000000 0 0 2000000 c0000000 0 3000 0 4000000 7*0 4000000 0 0 2000000
  //   c0000000 0 3000 0 4000000 7*0 4000000 0 0 2000000 c0000000 0 3000 0 4000000 7*0 4000000 0 0 2000000
  //   4000000 0 0 0 4000000 7*0 4000000 0 0 2000000 c0000000 0 0 0 4000000
  //   contents of Rom_A (hex, n*v repeats v):
  //   e0000000 10002002 8002000 46004000 0 1800000 600000 181800 40040000 1 6*0 e0000000 10002002 8002000
  //   46004000 0 1800000 600000 181800 40040000 1 6*0 e0000000 10002002 8002000 46004000 0 1800000 600000
  //   181800 40040000 1 6*0 e0000000 10002002 8002000 46004000 0 1800000 600000 181800 40040000 1 6*0
  //   e0000000 10002002 8002000 46004000 10000004 40002008 1 9*0 e0000000 10002002 8002000 46004000 0
  //   1800000 600000 1800 400000 200000 40019800 1 4*0 e0000000 10002002 8002000 46004000 0 1800000 600000
  //   181800 40040000 1 6*0 e0000000 10002002 8002000 46004000 0 1800000 1e00000 1f81800 1e01c80 601a40
  //   40001920 1 4*0 e0000000 10002002 8002000 46004000 10000000 10002008 10002008 10002008 40002008 1 6*0
  //   e0000000 10002002 8002000 46004000 0 1800000 1e00000 1f81800 1e01c80 601a40 1920 40000000 1 0 0 0
  //   e0000000 10002002 8002000 46004000 0 1800000 600000 181800 40040000 1 6*0 e0000000 10002002 8002000
  //   46004000 0 1800000 600000 181800 40040000 1 6*0 e0000000 10002002 8002000 46004000 0 1800000 600000
  //   181800 40040000 1 6*0 e0000000 10002002 8002000 46004000 0 1800000 600000 181800 40040000 1 6*0
  //   e0000000 10002002 8002000 46004000 40000000 1 10*0 e0000000 10002002 8002000 46004000 0 1800000
  //   600000 181800 40040000 1
endmodule

module Mover_Decoder (
  input  OE,
  input  [4:0] Opcode,
  input  Flag,
  output B,
  output A
);

  wire and_1_out, and_2_out, and_3_out, not_1_out;

  and and_1 (and_1_out, Opcode[0], Opcode[1], Opcode[2], Opcode[3]);
  not not_1 (not_1_out, Flag);
  and and_2 (and_2_out, and_1_out, Flag);
  and and_3 (and_3_out, and_1_out, not_1_out);
  assign B = OE ? and_2_out : 1'bz;  // Controlled_Buffer controlled_buffer_1
  assign A = OE ? and_3_out : 1'bz;  // Controlled_Buffer controlled_buffer_2

  // Notes on the sheet:
  //   Flag On
  //   Flag Off
endmodule
